// Logisim project 2C0x_PPU.circ as structural Verilog
module _2C02_NTSC (
  input  nDBE,
  input  RS2,
  input  RS1,
  input  RS0,
  input  R_W,
  input  D7,
  input  D6,
  input  D5,
  input  D4,
  input  D3,
  input  D2,
  input  D1,
  input  D0,
  input  nRES,
  input  EXT3,
  input  EXT2,
  input  EXT1,
  input  EXT0,
  input  PD7,
  input  PD6,
  input  PD5,
  input  PD4,
  input  PD3,
  input  PD2,
  input  PD1,
  input  PD0,
  output D7_2,
  output D6_2,
  output D5_2,
  output D4_2,
  output D3_2,
  output D2_2,
  output D1_2,
  output D0_2,
  output [10:0] VOUT,
  output nINT,
  output out_37,
  output out_38,
  output out_39,
  output out_40,
  output nRD,
  output nWR,
  output PA13,
  output PA12,
  output PA11,
  output PA10,
  output PA9,
  output PA8,
  output PA7,
  output PA6,
  output PA5,
  output PA4,
  output PA3,
  output PA2,
  output PA1,
  output PA0,
  output ALE,
  output PD7_W,
  output PD6_W,
  output PD5_W,
  output PD4_W,
  output PD3_W,
  output PD2_W,
  output PD1_W,
  output PD0_W
);

  wire CLK_out, controlled_buffer_1_out, not_1_out, not_3_out, not_19_out, PCLK, undriven, undriven_2,
       undriven_4;
  wire [7:0] ram_1_data, ram_2_data, undriven_5;
  wire [8:0] undriven_3;
  wire [13:0] PPU_ADR;

  Clock CLK (.out(CLK_out));
  not not_1 (not_1_out, CLK_out);
  not not_2 (nINT, undriven);
  Pull_Resistor #(.pull(1)) pull_resistor_1 (.node(nDBE));
  RAM #(.addrWidth(13)) ram_1 (.addr(PPU_ADR[12:0]), .data(ram_1_data), .sel(PPU_ADR[13]), .ld(nRD));  // open: clk, clr
  ROM #(.addrWidth(13)) rom_1 (.addr(PPU_ADR[12:0]), .data(ram_1_data), .sel(not_3_out));
  assign controlled_buffer_1_out = nRES ? PCLK : 1'bz;  // Controlled_Buffer controlled_buffer_1
  not not_3 (not_3_out, PPU_ADR[13]);
  not not_4 (PA13, PPU_ADR[13]);
  not not_5 (PA12, PPU_ADR[12]);
  not not_6 (PA11, PPU_ADR[11]);
  not not_7 (PA10, PPU_ADR[10]);
  not not_8 (PA9, PPU_ADR[9]);
  not not_9 (PA7, PPU_ADR[7]);
  not not_10 (PA8, PPU_ADR[8]);
  not not_11 (PA6, PPU_ADR[6]);
  not not_12 (PA5, PPU_ADR[5]);
  not not_13 (PA4, PPU_ADR[4]);
  not not_14 (PA3, PPU_ADR[3]);
  not not_15 (PA2, PPU_ADR[2]);
  not not_16 (PA1, PPU_ADR[1]);
  not not_17 (PA0, PPU_ADR[0]);
  not not_18 (ALE, undriven_2);
  not not_19 (not_19_out, undriven_4);
  RAM #(.addrWidth(9), .bus("separate")) ram_2 (
    .addr(undriven_3), .din(undriven_5), .data(ram_2_data), .str(not_19_out), .sel(1'b1), .clk(PCLK),
    .ld(undriven_4));  // open: clr

  // Other names for the same wires on the sheet: PPU_DATA[7:0] = {PD7, PD6, PD5, PD4, PD3, PD2, PD1, PD0};
  //   PPU_DATA_W[7:0] = {PD7_W, PD6_W, PD5_W, PD4_W, PD3_W, PD2_W, PD1_W, PD0_W}

  // Notes on the sheet:
  //   !!!
  //   2C02 PPU
  //   VRAM
  //   CHR ROM
  //   contents of rom_1 (hex, n*v repeats v):
  //   17*0 7f 7f 60 60 60 63 63 0 40 60 7f 7f 7f 7d 7c 8*63 8*7c 78 cc c0 7c 6 c6 7c 9*0 3c 66 c0 c0 c0 66
  //   3c 9*0 7c 5*c6 7c 9*0 fc c6 c6 ce f8 dc ce 9*0 fe c0 c0 fc c0 c0 fe 8*0 1e 6 6 6 c6 c6 7c 8*0 c6 c6
  //   d6 fe fe ee c6 9*0 6*60 7e 9*0 66 66 66 3c 18 18 18 9*0 c6 c6 c6 ee 7c 38 10 10*0 3f 20 23 2e 38 10
  //   d 3f 0 0 1c 11 6 c 30 e0 a0 0 e0 e0 e0 a0 90 6*0 40 60 1b 17 30 27 1c 1 10 27 20 0 f 18 0 0 f 18 88
  //   cc c4 46 d6 b6 a2 26 30 10 18 8 8 8 1c 18 38 3 19 19 0 f 19 9 0 0 6 6 1f 0 6 6 a2 a6 84 84 4c 4 48
  //   58 1c 18 38 38 b0 38 30 20 4 2 2 6 6 6 4 4 2 0 0 1 1 1 3 3 f8 f8 e8 68 68 78 78 78 0 0 10 90 90 80
  //   80 84 c c c 8 4*18 3 3 3 5*7 38 3c 3c 4*1c 3c c4 c0 c0 4*e0 c0 18 18 10 10 4*18 7 7 f f 4*7 3c 7c 78
  //   78 f8 f8 f0 f0 c0 80 80 80 4*0 1c 1c c e a 8 8 18 3 3 3 1 5 7 7 7 78 78 78 3c 3c 3c 3d 3d 80 80 80
  //   c0 c0 c2 c2 c2 18 89 b 6f 30 c1 81 3 81 0 c0 0 0 e 3e 7c 31 23 a0 fe 3 81 80 c1 0 0 2 0 0 78 7e 3e
  //   5*18 1c 1c 1c 5*7 3 3 3 1d 1c 1e 3e 3e 3c 3c 3c e2 e3 e1 c1 c1 c3 c2 c2 0 0 20 20 30 10 48 48 80
  //   4*40 60 20 a0 2f 32 e 2 0 2 5 7 5*0 4 2 0 4 13 ae fc d8 f0 bc 7e 78 e0 41 3 7 f 3 1 60 18 27 19 6 7
  //   7f ff 1f 87 c0 e0 f8 f8 80 0 c9 b3 d7 ea f6 f6 bc 9c 0 40 20 10 8 8 0 20 5*0 17 4*0 7f 7f 40 57 40
  //   7f 0 0 0 1 0 b1 0 1 bf 95 ff ff 5 b5 5 fd c c c 4*e 6 3 3 3 5*1 3c 3c 38 30 21 23 6 8 c0 c0 c1 c3 c6
  //   cc d9 94 88 84 54 d0 a0 a4 20 64 60 48 80 4 c 8 4 b 3 2 15 35 72 77 73 75 4 10 28 48 4 0 4 2 62 62
  //   4c 40 c0 40 40 1 1d 1d 33 4*3f 3e e1 f3 ff e1 e1 f1 f3 f7 1e c 0 1e 1e e c 8 8c a4 9c bc a4 8e 9a b8
  //   30 18 0 0 8 20 4 6 0 2b 2a 22 29 2 2b 8 40 7f 7f 77 7d 57 7f 5d 0 a9 a0 a9 80 21 20 89 5 fd f5 fd d5
  //   75 75 dd 7 7 3 82 a0 20 60 60 5*0 1 1 3 11 3 7 c 6c 1c b1 7d a2 2c 58 30 90 e0 44 80 e 8 4 8 10 93
  //   13 33 1 4 19 91 21 28 28 40 33 a7 a7 57 66 23 cd 7c 4 10 10 80 0 80 0 80 80 a1 c0 60 60 da 99 b8 3f
  //   1e 1f f 7 1 4 6 e7 87 c6 4c 5b 77 cf 3f 18 38 38 30 a0 80 11*0 2 0 0 6 e 17 ff 22 2a 20 22 8 2a 2 2b
  //   77 7f 75 77 5d 7f 57 7f a8 a1 28 89 88 a1 a8 29 fd f5 7d dd dd f5 fd 7d 61 51 47 fe bf df cc e0 1e
  //   2c 38 0 0 0 2 0 7a cb f7 e7 66 c4 1d 3 0 30 0 0 81 3 2 b0 71 f1 f7 67 e7 e1 e9 e1 4 6 0 80 0 6 6 e
  //   ee cc fb 49 e8 c8 cb a4 0 0 4*4 10 12 b8 3c cc 72 70 40 28 a 7 3 3 81 81 30 50 20 cf f 7 7 7 f f 1f
  //   30 f0 f8 f8 f8 f0 70 20 c4 ce c6 c7 c7 e7 e4 e1 8 0 5*8 2 7*0 7f ff 6*80 ff 7*0 b6 ff 6*1 b7 cf fe
  //   fc 1 d 1b 17 1b 30 7*0 97 77 f 98 9c 3f 3e 6e 8 0 30 66 61 c0 c0 80 c3 c3 42 c7 c5 81 8c 8b 24 c 8d
  //   8 a 1e 12 34 62 a1 41 40 30 31 b0 33 15 14 b4 b5 85 8c f 88 60 30 0 d0 0 2 88 8 15 4 d2 26 82 b0 6
  //   b7 0 2 83 de 4b 3e c 30 80 fd 2c 0 0 40 51 3 21 81 89 0 7a 72 26 6f a a 12 b9 0 85 c9 80 d0 f0 b2 c7
  //   e5 6f a b 20 e 4c 18 12 90 f5 44 4*0 80 c0 c0 e0 9*0 1f 0 77 0 73 0 27 80 9f 80 f7 80 f3 80 a7 0 ce
  //   0 de 0 8a 0 6e 1 cf 1 df 1 8b 1 6f 8 9*0 8 8 0 e d 1f 1c 8 0 1 3 6 6 6 1 3 1 2 4*0 7e fd fd db e1 c3
  //   d3 a 80 4*0 4 c 30 98 86 84 8c e 4 14 15 27 31 33 33 71 73 43 62 30 21 3c c ba 41 1 0 8d 9c 80 10 4
  //   88 ee ef 24 38 d0 e6 44 23 b6 cc 92 c4 29 11 13 9c 0 10 61 41 86 44 d 1b 36 28 2 8e 19 3a 30 60 40
  //   c6 65 43 24 c8 6c 33 f e 80 4 a 2 0 c 10 51 8 4 40 9a b8 39 52 b5 37 98 81 41 47 c6 ac 42 0 0 20 68
  //   dc bc fa d2 f0 0 0 80 0 0 0 c 0 10 7 13 2 14 3 15 18 18 1f 1b 1a 1c 1b 1d 70 cc 24 fc fa c0 49 18 82
  //   20 c8 0 0 18 0 0 5 19 11 21 29 19 31 19 f8 60 68 d8 d4 e4 ce e6 e6 e3 f3 fa ef d6 f4 74 1 10 0 1 10
  //   28 b b e0 e0 e7 43 93 7 4 14 11 3 0 ac 4c 98 38 2b f9 d0 b0 91 90 a0 bc b2 4 7 f 6e 63 57 43 4d 66
  //   2a 87 ac 19 5a 39 3c 81 c5 40 43 46 5 86 3 1c 88 1c 84 16 b 10 e6 62 57 e3 73 e9 94 ed 19 fb fd 67
  //   77 7f 3f 3f 3b 4 0 90 0 80 c0 c0 c0 0 0 80 80 c0 e0 e0 f0 8*0 7 12 7 12 5 13 6 11 1f 1a 1f 1a 1d 1b
  //   1e 19 3c 38 fc 78 c4 f0 6a 2e 1 1 1 3 3 3 5 51 30 1c 1c 34 1c 21 a1 83 ce e2 e2 cb e3 de 5e 7c b0 f0
  //   f8 61 60 80 87 4 e c 1 12 7 e 18 19 1c 3e 2e f e7 d0 a8 91 61 c1 d1 80 0 e 53 4e fe ae c4 9c 7c 38
  //   18 ba 1 10 2a 42 80 c4 e0 41 2c 50 40 50 21 2 39 b1 13 2f 3f 2f de fd 86 4e 62 2 4e a 24 20 60 0 9d
  //   fd b1 e5 cb cf 8b 6f 3d 2c 29 44 40 8 8a 89 c2 d1 c2 ab a9 e3 41 4 f0 f8 dc 72 e0 a0 21 f0 0 0 20 84
  //   6 56 c6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
  //   CPU INTERFACE
  //   Logisim doesn't support bidirectional pads and wires
  //   So we have to add workaround by separate I/O wires
  //   MASTER/SLAVE
  //   VRAM INTERFACE
  //   Logisim doesn't support bidirectional pads and wires
  //   So we have to add workaround by separate I/O wires
  //   OB
endmodule

module _2C04_0003_RGB (
  input  nDBE,
  input  RS2,
  input  RS1,
  input  RS0,
  input  R_W,
  input  D7,
  input  D6,
  input  D5,
  input  D4,
  input  D3,
  input  D2,
  input  D1,
  input  D0,
  input  nRES,
  input  EXT3,
  input  EXT2,
  input  EXT1,
  input  EXT0,
  input  PD7,
  input  PD6,
  input  PD5,
  input  PD4,
  input  PD3,
  input  PD2,
  input  PD1,
  input  PD0,
  output D7_2,
  output D6_2,
  output D5_2,
  output D4_2,
  output D3_2,
  output D2_2,
  output D1_2,
  output D0_2,
  output SYNC,
  output [7:0] RED,
  output [7:0] GREEN,
  output [7:0] BLUE,
  output nINT,
  output out_40,
  output out_41,
  output out_42,
  output out_43,
  output PD7_W,
  output PD6_W,
  output PD5_W,
  output PD4_W,
  output PD3_W,
  output PD2_W,
  output PD1_W,
  output PD0_W,
  output nWR,
  output nRD,
  output PA13,
  output PA12,
  output PA11,
  output PA10,
  output PA9,
  output PA8,
  output PA7,
  output PA6,
  output PA5,
  output PA4,
  output PA3,
  output PA2,
  output PA1,
  output PA0,
  output ALE
);

  wire CLK_out, controlled_buffer_1_out, not_1_out, not_3_out, not_19_out, PCLK, undriven, undriven_2,
       undriven_4;
  wire [7:0] PPU_DATA;
  wire [8:0] undriven_3;
  wire [13:0] PPU_ADR;

  Clock CLK (.out(CLK_out));
  not not_1 (not_1_out, CLK_out);
  not not_2 (nINT, undriven);
  RAM #(.addrWidth(13)) ram_1 (.addr(PPU_ADR[12:0]), .data(PPU_DATA), .sel(PPU_ADR[13]), .ld(nRD));  // open: clk, clr
  ROM #(.addrWidth(13)) rom_1 (.addr(PPU_ADR[12:0]), .data(PPU_DATA), .sel(not_3_out));
  not not_3 (not_3_out, PPU_ADR[13]);
  not not_4 (PA13, PPU_ADR[13]);
  not not_5 (PA12, PPU_ADR[12]);
  assign controlled_buffer_1_out = nRES ? PCLK : 1'bz;  // Controlled_Buffer controlled_buffer_1
  not not_6 (PA11, PPU_ADR[11]);
  not not_7 (PA10, PPU_ADR[10]);
  not not_8 (PA9, PPU_ADR[9]);
  not not_9 (PA8, PPU_ADR[8]);
  not not_10 (PA7, PPU_ADR[7]);
  not not_11 (PA6, PPU_ADR[6]);
  not not_12 (PA5, PPU_ADR[5]);
  not not_13 (PA4, PPU_ADR[4]);
  not not_14 (PA3, PPU_ADR[3]);
  not not_15 (PA2, PPU_ADR[2]);
  not not_16 (PA0, PPU_ADR[0]);
  not not_17 (PA1, PPU_ADR[1]);
  not not_18 (ALE, undriven_2);
  not not_19 (not_19_out, undriven_4);
  RAM #(.addrWidth(9), .bus("separate")) ram_2 (
    .addr(undriven_3), .str(not_19_out), .sel(1'b1), .clk(PCLK), .ld(undriven_4));  // open: din, data, clr

  // Other names for the same wires on the sheet: PPU_DATA_W[7:0] = {PD7_W, PD6_W, PD5_W, PD4_W, PD3_W, PD2_W, PD1_W, PD0_W}

  // Notes on the sheet:
  //   2C04 - 0003  RGB  PPU
  //   not used
  //   VRAM
  //   CHR ROM
  //   contents of rom_1 (hex, n*v repeats v):
  //   17*0 7f 7f 60 60 60 63 63 0 40 60 7f 7f 7f 7d 7c 8*63 8*7c 78 cc c0 7c 6 c6 7c 9*0 3c 66 c0 c0 c0 66
  //   3c 9*0 7c 5*c6 7c 9*0 fc c6 c6 ce f8 dc ce 9*0 fe c0 c0 fc c0 c0 fe 8*0 1e 6 6 6 c6 c6 7c 8*0 c6 c6
  //   d6 fe fe ee c6 9*0 6*60 7e 9*0 66 66 66 3c 18 18 18 9*0 c6 c6 c6 ee 7c 38 10 10*0 3f 20 23 2e 38 10
  //   d 3f 0 0 1c 11 6 c 30 e0 a0 0 e0 e0 e0 a0 90 6*0 40 60 1b 17 30 27 1c 1 10 27 20 0 f 18 0 0 f 18 88
  //   cc c4 46 d6 b6 a2 26 30 10 18 8 8 8 1c 18 38 3 19 19 0 f 19 9 0 0 6 6 1f 0 6 6 a2 a6 84 84 4c 4 48
  //   58 1c 18 38 38 b0 38 30 20 4 2 2 6 6 6 4 4 2 0 0 1 1 1 3 3 f8 f8 e8 68 68 78 78 78 0 0 10 90 90 80
  //   80 84 c c c 8 4*18 3 3 3 5*7 38 3c 3c 4*1c 3c c4 c0 c0 4*e0 c0 18 18 10 10 4*18 7 7 f f 4*7 3c 7c 78
  //   78 f8 f8 f0 f0 c0 80 80 80 4*0 1c 1c c e a 8 8 18 3 3 3 1 5 7 7 7 78 78 78 3c 3c 3c 3d 3d 80 80 80
  //   c0 c0 c2 c2 c2 18 89 b 6f 30 c1 81 3 81 0 c0 0 0 e 3e 7c 31 23 a0 fe 3 81 80 c1 0 0 2 0 0 78 7e 3e
  //   5*18 1c 1c 1c 5*7 3 3 3 1d 1c 1e 3e 3e 3c 3c 3c e2 e3 e1 c1 c1 c3 c2 c2 0 0 20 20 30 10 48 48 80
  //   4*40 60 20 a0 2f 32 e 2 0 2 5 7 5*0 4 2 0 4 13 ae fc d8 f0 bc 7e 78 e0 41 3 7 f 3 1 60 18 27 19 6 7
  //   7f ff 1f 87 c0 e0 f8 f8 80 0 c9 b3 d7 ea f6 f6 bc 9c 0 40 20 10 8 8 0 20 5*0 17 4*0 7f 7f 40 57 40
  //   7f 0 0 0 1 0 b1 0 1 bf 95 ff ff 5 b5 5 fd c c c 4*e 6 3 3 3 5*1 3c 3c 38 30 21 23 6 8 c0 c0 c1 c3 c6
  //   cc d9 94 88 84 54 d0 a0 a4 20 64 60 48 80 4 c 8 4 b 3 2 15 35 72 77 73 75 4 10 28 48 4 0 4 2 62 62
  //   4c 40 c0 40 40 1 1d 1d 33 4*3f 3e e1 f3 ff e1 e1 f1 f3 f7 1e c 0 1e 1e e c 8 8c a4 9c bc a4 8e 9a b8
  //   30 18 0 0 8 20 4 6 0 2b 2a 22 29 2 2b 8 40 7f 7f 77 7d 57 7f 5d 0 a9 a0 a9 80 21 20 89 5 fd f5 fd d5
  //   75 75 dd 7 7 3 82 a0 20 60 60 5*0 1 1 3 11 3 7 c 6c 1c b1 7d a2 2c 58 30 90 e0 44 80 e 8 4 8 10 93
  //   13 33 1 4 19 91 21 28 28 40 33 a7 a7 57 66 23 cd 7c 4 10 10 80 0 80 0 80 80 a1 c0 60 60 da 99 b8 3f
  //   1e 1f f 7 1 4 6 e7 87 c6 4c 5b 77 cf 3f 18 38 38 30 a0 80 11*0 2 0 0 6 e 17 ff 22 2a 20 22 8 2a 2 2b
  //   77 7f 75 77 5d 7f 57 7f a8 a1 28 89 88 a1 a8 29 fd f5 7d dd dd f5 fd 7d 61 51 47 fe bf df cc e0 1e
  //   2c 38 0 0 0 2 0 7a cb f7 e7 66 c4 1d 3 0 30 0 0 81 3 2 b0 71 f1 f7 67 e7 e1 e9 e1 4 6 0 80 0 6 6 e
  //   ee cc fb 49 e8 c8 cb a4 0 0 4*4 10 12 b8 3c cc 72 70 40 28 a 7 3 3 81 81 30 50 20 cf f 7 7 7 f f 1f
  //   30 f0 f8 f8 f8 f0 70 20 c4 ce c6 c7 c7 e7 e4 e1 8 0 5*8 2 7*0 7f ff 6*80 ff 7*0 b6 ff 6*1 b7 cf fe
  //   fc 1 d 1b 17 1b 30 7*0 97 77 f 98 9c 3f 3e 6e 8 0 30 66 61 c0 c0 80 c3 c3 42 c7 c5 81 8c 8b 24 c 8d
  //   8 a 1e 12 34 62 a1 41 40 30 31 b0 33 15 14 b4 b5 85 8c f 88 60 30 0 d0 0 2 88 8 15 4 d2 26 82 b0 6
  //   b7 0 2 83 de 4b 3e c 30 80 fd 2c 0 0 40 51 3 21 81 89 0 7a 72 26 6f a a 12 b9 0 85 c9 80 d0 f0 b2 c7
  //   e5 6f a b 20 e 4c 18 12 90 f5 44 4*0 80 c0 c0 e0 9*0 1f 0 77 0 73 0 27 80 9f 80 f7 80 f3 80 a7 0 ce
  //   0 de 0 8a 0 6e 1 cf 1 df 1 8b 1 6f 8 9*0 8 8 0 e d 1f 1c 8 0 1 3 6 6 6 1 3 1 2 4*0 7e fd fd db e1 c3
  //   d3 a 80 4*0 4 c 30 98 86 84 8c e 4 14 15 27 31 33 33 71 73 43 62 30 21 3c c ba 41 1 0 8d 9c 80 10 4
  //   88 ee ef 24 38 d0 e6 44 23 b6 cc 92 c4 29 11 13 9c 0 10 61 41 86 44 d 1b 36 28 2 8e 19 3a 30 60 40
  //   c6 65 43 24 c8 6c 33 f e 80 4 a 2 0 c 10 51 8 4 40 9a b8 39 52 b5 37 98 81 41 47 c6 ac 42 0 0 20 68
  //   dc bc fa d2 f0 0 0 80 0 0 0 c 0 10 7 13 2 14 3 15 18 18 1f 1b 1a 1c 1b 1d 70 cc 24 fc fa c0 49 18 82
  //   20 c8 0 0 18 0 0 5 19 11 21 29 19 31 19 f8 60 68 d8 d4 e4 ce e6 e6 e3 f3 fa ef d6 f4 74 1 10 0 1 10
  //   28 b b e0 e0 e7 43 93 7 4 14 11 3 0 ac 4c 98 38 2b f9 d0 b0 91 90 a0 bc b2 4 7 f 6e 63 57 43 4d 66
  //   2a 87 ac 19 5a 39 3c 81 c5 40 43 46 5 86 3 1c 88 1c 84 16 b 10 e6 62 57 e3 73 e9 94 ed 19 fb fd 67
  //   77 7f 3f 3f 3b 4 0 90 0 80 c0 c0 c0 0 0 80 80 c0 e0 e0 f0 8*0 7 12 7 12 5 13 6 11 1f 1a 1f 1a 1d 1b
  //   1e 19 3c 38 fc 78 c4 f0 6a 2e 1 1 1 3 3 3 5 51 30 1c 1c 34 1c 21 a1 83 ce e2 e2 cb e3 de 5e 7c b0 f0
  //   f8 61 60 80 87 4 e c 1 12 7 e 18 19 1c 3e 2e f e7 d0 a8 91 61 c1 d1 80 0 e 53 4e fe ae c4 9c 7c 38
  //   18 ba 1 10 2a 42 80 c4 e0 41 2c 50 40 50 21 2 39 b1 13 2f 3f 2f de fd 86 4e 62 2 4e a 24 20 60 0 9d
  //   fd b1 e5 cb cf 8b 6f 3d 2c 29 44 40 8 8a 89 c2 d1 c2 ab a9 e3 41 4 f0 f8 dc 72 e0 a0 21 f0 0 0 20 84
  //   6 56 c6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
  //   CPU INTERFACE
  //   /R4 NOT USED
  //   Logisim doesn't support bidirectional pads and wires
  //   So we have to add workaround by separate I/O wires
  //   MASTER/SLAVE
  //   VRAM INTERFACE
  //   Logisim doesn't support bidirectional pads and wires
  //   So we have to add workaround by separate I/O wires
endmodule

module _2C07_PAL (
  input  nDBE,
  input  RS2,
  input  RS1,
  input  RS0,
  input  R_W,
  input  D7,
  input  D6,
  input  D5,
  input  D4,
  input  D3,
  input  D2,
  input  D1,
  input  D0,
  input  nRES,
  input  EXT3,
  input  EXT2,
  input  EXT1,
  input  EXT0,
  input  PD7,
  input  PD6,
  input  PD5,
  input  PD4,
  input  PD3,
  input  PD2,
  input  PD1,
  input  PD0,
  output D7_2,
  output D6_2,
  output D5_2,
  output D4_2,
  output D3_2,
  output D2_2,
  output D1_2,
  output D0_2,
  output [10:0] VOUT,
  output nINT,
  output out_37,
  output out_38,
  output out_39,
  output out_40,
  output nRD,
  output nWR,
  output PA13,
  output PA12,
  output PA11,
  output PA10,
  output PA9,
  output PA8,
  output PA7,
  output PA6,
  output PA5,
  output PA4,
  output PA3,
  output PA2,
  output PA1,
  output PA0,
  output ALE,
  output PD7_W,
  output PD6_W,
  output PD5_W,
  output PD4_W,
  output PD3_W,
  output PD2_W,
  output PD1_W,
  output PD0_W
);

  wire CLK_out, controlled_buffer_1_out, not_1_out, not_3_out, PCLK, undriven, undriven_2, undriven_3;
  wire [7:0] PPU_DATA, ram_2_data;
  wire [8:0] undriven_4;
  wire [13:0] PPU_ADR;

  Clock CLK (.out(CLK_out));
  not not_1 (not_1_out, CLK_out);
  not not_2 (nINT, undriven);
  RAM #(.addrWidth(13)) ram_1 (.addr(PPU_ADR[12:0]), .data(PPU_DATA), .sel(PPU_ADR[13]), .ld(nRD));  // open: clk, clr
  ROM #(.addrWidth(13)) rom_1 (.addr(PPU_ADR[12:0]), .data(PPU_DATA), .sel(not_3_out));
  not not_3 (not_3_out, PPU_ADR[13]);
  assign controlled_buffer_1_out = nRES ? PCLK : 1'bz;  // Controlled_Buffer controlled_buffer_1
  not not_4 (PA12, PPU_ADR[12]);
  not not_5 (PA13, PPU_ADR[13]);
  not not_6 (PA10, PPU_ADR[10]);
  not not_7 (PA11, PPU_ADR[11]);
  not not_8 (PA9, PPU_ADR[9]);
  not not_9 (PA7, PPU_ADR[7]);
  not not_10 (PA8, PPU_ADR[8]);
  not not_11 (PA6, PPU_ADR[6]);
  not not_12 (PA4, PPU_ADR[4]);
  not not_13 (PA5, PPU_ADR[5]);
  not not_14 (PA2, PPU_ADR[2]);
  not not_15 (PA3, PPU_ADR[3]);
  not not_16 (PA1, PPU_ADR[1]);
  not not_17 (PA0, PPU_ADR[0]);
  not not_18 (ALE, undriven_2);
  RAM #(.addrWidth(9)) ram_2 (
    .addr(undriven_4), .data(ram_2_data), .sel(1'b1), .clk(PCLK), .ld(undriven_3));  // open: clr

  // Other names for the same wires on the sheet: PPU_DATA_W[7:0] = {PD7_W, PD6_W, PD5_W, PD4_W, PD3_W, PD2_W, PD1_W, PD0_W}

  // Notes on the sheet:
  //   2C07 PPU
  //   VRAM
  //   CHR ROM
  //   contents of rom_1 (hex, n*v repeats v):
  //   17*0 7f 7f 60 60 60 63 63 0 40 60 7f 7f 7f 7d 7c 8*63 8*7c 78 cc c0 7c 6 c6 7c 9*0 3c 66 c0 c0 c0 66
  //   3c 9*0 7c 5*c6 7c 9*0 fc c6 c6 ce f8 dc ce 9*0 fe c0 c0 fc c0 c0 fe 8*0 1e 6 6 6 c6 c6 7c 8*0 c6 c6
  //   d6 fe fe ee c6 9*0 6*60 7e 9*0 66 66 66 3c 18 18 18 9*0 c6 c6 c6 ee 7c 38 10 10*0 3f 20 23 2e 38 10
  //   d 3f 0 0 1c 11 6 c 30 e0 a0 0 e0 e0 e0 a0 90 6*0 40 60 1b 17 30 27 1c 1 10 27 20 0 f 18 0 0 f 18 88
  //   cc c4 46 d6 b6 a2 26 30 10 18 8 8 8 1c 18 38 3 19 19 0 f 19 9 0 0 6 6 1f 0 6 6 a2 a6 84 84 4c 4 48
  //   58 1c 18 38 38 b0 38 30 20 4 2 2 6 6 6 4 4 2 0 0 1 1 1 3 3 f8 f8 e8 68 68 78 78 78 0 0 10 90 90 80
  //   80 84 c c c 8 4*18 3 3 3 5*7 38 3c 3c 4*1c 3c c4 c0 c0 4*e0 c0 18 18 10 10 4*18 7 7 f f 4*7 3c 7c 78
  //   78 f8 f8 f0 f0 c0 80 80 80 4*0 1c 1c c e a 8 8 18 3 3 3 1 5 7 7 7 78 78 78 3c 3c 3c 3d 3d 80 80 80
  //   c0 c0 c2 c2 c2 18 89 b 6f 30 c1 81 3 81 0 c0 0 0 e 3e 7c 31 23 a0 fe 3 81 80 c1 0 0 2 0 0 78 7e 3e
  //   5*18 1c 1c 1c 5*7 3 3 3 1d 1c 1e 3e 3e 3c 3c 3c e2 e3 e1 c1 c1 c3 c2 c2 0 0 20 20 30 10 48 48 80
  //   4*40 60 20 a0 2f 32 e 2 0 2 5 7 5*0 4 2 0 4 13 ae fc d8 f0 bc 7e 78 e0 41 3 7 f 3 1 60 18 27 19 6 7
  //   7f ff 1f 87 c0 e0 f8 f8 80 0 c9 b3 d7 ea f6 f6 bc 9c 0 40 20 10 8 8 0 20 5*0 17 4*0 7f 7f 40 57 40
  //   7f 0 0 0 1 0 b1 0 1 bf 95 ff ff 5 b5 5 fd c c c 4*e 6 3 3 3 5*1 3c 3c 38 30 21 23 6 8 c0 c0 c1 c3 c6
  //   cc d9 94 88 84 54 d0 a0 a4 20 64 60 48 80 4 c 8 4 b 3 2 15 35 72 77 73 75 4 10 28 48 4 0 4 2 62 62
  //   4c 40 c0 40 40 1 1d 1d 33 4*3f 3e e1 f3 ff e1 e1 f1 f3 f7 1e c 0 1e 1e e c 8 8c a4 9c bc a4 8e 9a b8
  //   30 18 0 0 8 20 4 6 0 2b 2a 22 29 2 2b 8 40 7f 7f 77 7d 57 7f 5d 0 a9 a0 a9 80 21 20 89 5 fd f5 fd d5
  //   75 75 dd 7 7 3 82 a0 20 60 60 5*0 1 1 3 11 3 7 c 6c 1c b1 7d a2 2c 58 30 90 e0 44 80 e 8 4 8 10 93
  //   13 33 1 4 19 91 21 28 28 40 33 a7 a7 57 66 23 cd 7c 4 10 10 80 0 80 0 80 80 a1 c0 60 60 da 99 b8 3f
  //   1e 1f f 7 1 4 6 e7 87 c6 4c 5b 77 cf 3f 18 38 38 30 a0 80 11*0 2 0 0 6 e 17 ff 22 2a 20 22 8 2a 2 2b
  //   77 7f 75 77 5d 7f 57 7f a8 a1 28 89 88 a1 a8 29 fd f5 7d dd dd f5 fd 7d 61 51 47 fe bf df cc e0 1e
  //   2c 38 0 0 0 2 0 7a cb f7 e7 66 c4 1d 3 0 30 0 0 81 3 2 b0 71 f1 f7 67 e7 e1 e9 e1 4 6 0 80 0 6 6 e
  //   ee cc fb 49 e8 c8 cb a4 0 0 4*4 10 12 b8 3c cc 72 70 40 28 a 7 3 3 81 81 30 50 20 cf f 7 7 7 f f 1f
  //   30 f0 f8 f8 f8 f0 70 20 c4 ce c6 c7 c7 e7 e4 e1 8 0 5*8 2 7*0 7f ff 6*80 ff 7*0 b6 ff 6*1 b7 cf fe
  //   fc 1 d 1b 17 1b 30 7*0 97 77 f 98 9c 3f 3e 6e 8 0 30 66 61 c0 c0 80 c3 c3 42 c7 c5 81 8c 8b 24 c 8d
  //   8 a 1e 12 34 62 a1 41 40 30 31 b0 33 15 14 b4 b5 85 8c f 88 60 30 0 d0 0 2 88 8 15 4 d2 26 82 b0 6
  //   b7 0 2 83 de 4b 3e c 30 80 fd 2c 0 0 40 51 3 21 81 89 0 7a 72 26 6f a a 12 b9 0 85 c9 80 d0 f0 b2 c7
  //   e5 6f a b 20 e 4c 18 12 90 f5 44 4*0 80 c0 c0 e0 9*0 1f 0 77 0 73 0 27 80 9f 80 f7 80 f3 80 a7 0 ce
  //   0 de 0 8a 0 6e 1 cf 1 df 1 8b 1 6f 8 9*0 8 8 0 e d 1f 1c 8 0 1 3 6 6 6 1 3 1 2 4*0 7e fd fd db e1 c3
  //   d3 a 80 4*0 4 c 30 98 86 84 8c e 4 14 15 27 31 33 33 71 73 43 62 30 21 3c c ba 41 1 0 8d 9c 80 10 4
  //   88 ee ef 24 38 d0 e6 44 23 b6 cc 92 c4 29 11 13 9c 0 10 61 41 86 44 d 1b 36 28 2 8e 19 3a 30 60 40
  //   c6 65 43 24 c8 6c 33 f e 80 4 a 2 0 c 10 51 8 4 40 9a b8 39 52 b5 37 98 81 41 47 c6 ac 42 0 0 20 68
  //   dc bc fa d2 f0 0 0 80 0 0 0 c 0 10 7 13 2 14 3 15 18 18 1f 1b 1a 1c 1b 1d 70 cc 24 fc fa c0 49 18 82
  //   20 c8 0 0 18 0 0 5 19 11 21 29 19 31 19 f8 60 68 d8 d4 e4 ce e6 e6 e3 f3 fa ef d6 f4 74 1 10 0 1 10
  //   28 b b e0 e0 e7 43 93 7 4 14 11 3 0 ac 4c 98 38 2b f9 d0 b0 91 90 a0 bc b2 4 7 f 6e 63 57 43 4d 66
  //   2a 87 ac 19 5a 39 3c 81 c5 40 43 46 5 86 3 1c 88 1c 84 16 b 10 e6 62 57 e3 73 e9 94 ed 19 fb fd 67
  //   77 7f 3f 3f 3b 4 0 90 0 80 c0 c0 c0 0 0 80 80 c0 e0 e0 f0 8*0 7 12 7 12 5 13 6 11 1f 1a 1f 1a 1d 1b
  //   1e 19 3c 38 fc 78 c4 f0 6a 2e 1 1 1 3 3 3 5 51 30 1c 1c 34 1c 21 a1 83 ce e2 e2 cb e3 de 5e 7c b0 f0
  //   f8 61 60 80 87 4 e c 1 12 7 e 18 19 1c 3e 2e f e7 d0 a8 91 61 c1 d1 80 0 e 53 4e fe ae c4 9c 7c 38
  //   18 ba 1 10 2a 42 80 c4 e0 41 2c 50 40 50 21 2 39 b1 13 2f 3f 2f de fd 86 4e 62 2 4e a 24 20 60 0 9d
  //   fd b1 e5 cb cf 8b 6f 3d 2c 29 44 40 8 8a 89 c2 d1 c2 ab a9 e3 41 4 f0 f8 dc 72 e0 a0 21 f0 0 0 20 84
  //   6 56 c6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
  //   CPU INTERFACE
  //   Logisim doesn't support bidirectional pads and wires
  //   So we have to add workaround by separate I/O wires
  //   MASTER/SLAVE
  //   VRAM INTERFACE
  //   Logisim doesn't support bidirectional pads and wires
  //   So we have to add workaround by separate I/O wires
endmodule

module D_latch (
  input  EN,
  input  D,
  output Q,
  output NOT_Q
);

  D_Flip_Flop #(.trigger("high")) d_ff_1 (.clk(EN), .D(D), .Q(Q), .Qn(NOT_Q));  // open: preset, en, reset
endmodule

module PIXEL_CLOCK_NTSC (
  input  nCLK,
  input  RES,
  output PCLK,
  output nPCLK
);

  wire _2_out, _3_out, d_latch_1_not_q, d_latch_2_not_q, d_latch_3_not_q, nor_1_out, not_1_out, not_2_out,
       transistor_1_out, transistor_3_out, transistor_5_out;

  not not_1 (not_1_out, nCLK);
  nor nor_1 (nor_1_out, RES, PCLK);
  not not_2 (not_2_out, PCLK);
  D_latch d_latch_1 (.EN(nCLK), .D(nor_1_out), .NOT_Q(d_latch_1_not_q));  // open: Q
  nor _3 (_3_out, PCLK, _2_out);
  nor _2 (_2_out, _3_out, not_2_out);
  D_latch d_latch_2 (.EN(not_1_out), .D(d_latch_1_not_q), .NOT_Q(d_latch_2_not_q));  // open: Q
  D_latch d_latch_3 (.EN(nCLK), .D(d_latch_2_not_q), .NOT_Q(d_latch_3_not_q));  // open: Q
  D_latch d_latch_4 (.EN(not_1_out), .D(d_latch_3_not_q), .NOT_Q(PCLK));  // open: Q
  Transistor #(.\type ("n")) transistor_1 (.in(1'b1), .out(transistor_1_out), .gate(_3_out));
  Transistor #(.\type ("n")) transistor_2 (.in(1'b0), .out(transistor_1_out), .gate(_2_out));
  Transistor #(.\type ("n")) transistor_3 (.in(1'b1), .out(transistor_3_out), .gate(_2_out));
  Transistor #(.\type ("n")) transistor_4 (.in(1'b0), .out(transistor_3_out), .gate(_3_out));
  Transistor #(.\type ("n")) transistor_5 (.in(1'b1), .out(transistor_5_out), .gate(transistor_3_out));
  Transistor #(.\type ("n")) transistor_6 (.in(1'b1), .out(transistor_5_out), .gate(transistor_3_out));
  Transistor #(.\type ("n")) transistor_7 (.in(1'b0), .out(transistor_5_out), .gate(transistor_1_out));
  Transistor #(.\type ("n")) transistor_8 (.in(1'b0), .out(transistor_5_out), .gate(transistor_1_out));
  Transistor #(.\type ("n")) transistor_9 (.in(1'b1), .out(nPCLK), .gate(transistor_1_out));
  Transistor #(.\type ("n")) transistor_10 (.in(1'b1), .out(nPCLK), .gate(transistor_1_out));
  Transistor #(.\type ("n")) transistor_11 (.in(1'b0), .out(nPCLK), .gate(transistor_3_out));
  Transistor #(.\type ("n")) transistor_12 (.in(1'b0), .out(nPCLK), .gate(transistor_3_out));
  Transistor #(.\type ("n")) transistor_13 (.in(1'b1), .out(transistor_5_out), .gate(transistor_3_out));
  Transistor #(.\type ("n")) transistor_14 (.in(1'b1), .out(transistor_5_out), .gate(transistor_3_out));
  Transistor #(.\type ("n")) transistor_15 (.in(1'b0), .out(transistor_5_out), .gate(transistor_1_out));
  Transistor #(.\type ("n")) transistor_16 (.in(1'b0), .out(transistor_5_out), .gate(transistor_1_out));
  Transistor #(.\type ("n")) transistor_17 (.in(1'b1), .out(nPCLK), .gate(transistor_1_out));
  Transistor #(.\type ("n")) transistor_18 (.in(1'b1), .out(nPCLK), .gate(transistor_1_out));
  Transistor #(.\type ("n")) transistor_19 (.in(1'b0), .out(nPCLK), .gate(transistor_3_out));
  Transistor #(.\type ("n")) transistor_20 (.in(1'b0), .out(nPCLK), .gate(transistor_3_out));

  // Notes on the sheet:
  //   1
  //   Pixel clock is disabled during RESET (PPU stall)
  //   PCLK DISTRIBUTION
  //   I
  //   II
  //   PCLK = CLK / 4
endmodule

module PIXEL_CLOCK_PAL (
  input  nCLK,
  input  RES,
  output PCLK,
  output nPCLK
);

  wire _2_2_out, _2_out, _3_2_out, _3_out, d_latch_1_q, d_latch_2_not_q, d_latch_3_not_q, d_latch_4_not_q,
       d_latch_5_not_q, d_latch_6_not_q, nor_1_out, not_1_out, not_2_out, not_3_out, transistor_1_out,
       transistor_3_out, transistor_5_out;

  not not_1 (not_1_out, nCLK);
  not not_2 (not_2_out, _3_2_out);
  D_latch d_latch_1 (.EN(nCLK), .D(_3_2_out), .Q(d_latch_1_q));  // open: NOT_Q
  D_latch d_latch_2 (.EN(not_1_out), .D(nor_1_out), .NOT_Q(d_latch_2_not_q));  // open: Q
  nor nor_1 (nor_1_out, d_latch_1_q, RES);
  nor _3 (_3_out, _3_2_out, _2_out);
  nor _2 (_2_out, _3_out, not_2_out);
  D_latch d_latch_3 (.EN(nCLK), .D(d_latch_2_not_q), .NOT_Q(d_latch_3_not_q));  // open: Q
  D_latch d_latch_4 (.EN(not_1_out), .D(d_latch_3_not_q), .NOT_Q(d_latch_4_not_q));  // open: Q
  Transistor #(.\type ("n")) transistor_1 (.in(1'b1), .out(transistor_1_out), .gate(_3_out));
  Transistor #(.\type ("n")) transistor_2 (.in(1'b0), .out(transistor_1_out), .gate(_2_out));
  Transistor #(.\type ("n")) transistor_3 (.in(1'b1), .out(transistor_3_out), .gate(_2_out));
  Transistor #(.\type ("n")) transistor_4 (.in(1'b0), .out(transistor_3_out), .gate(_3_out));
  D_latch d_latch_5 (.EN(nCLK), .D(d_latch_4_not_q), .NOT_Q(d_latch_5_not_q));  // open: Q
  Transistor #(.\type ("n")) transistor_5 (.in(1'b1), .out(transistor_5_out), .gate(transistor_3_out));
  Transistor #(.\type ("n")) transistor_6 (.in(1'b0), .out(transistor_5_out), .gate(transistor_1_out));
  Transistor #(.\type ("n")) transistor_7 (.in(1'b1), .out(nPCLK), .gate(transistor_1_out));
  Transistor #(.\type ("n")) transistor_8 (.in(1'b0), .out(nPCLK), .gate(transistor_3_out));
  D_latch d_latch_6 (.EN(not_1_out), .D(d_latch_5_not_q), .NOT_Q(d_latch_6_not_q));  // open: Q
  not not_3 (not_3_out, d_latch_5_not_q);
  Transistor #(.\type ("n")) transistor_9 (.in(1'b1), .out(transistor_5_out), .gate(transistor_3_out));
  Transistor #(.\type ("n")) transistor_10 (.in(1'b1), .out(transistor_5_out), .gate(transistor_3_out));
  Transistor #(.\type ("n")) transistor_11 (.in(1'b0), .out(transistor_5_out), .gate(transistor_1_out));
  Transistor #(.\type ("n")) transistor_12 (.in(1'b0), .out(transistor_5_out), .gate(transistor_1_out));
  Transistor #(.\type ("n")) transistor_13 (.in(1'b1), .out(nPCLK), .gate(transistor_1_out));
  Transistor #(.\type ("n")) transistor_14 (.in(1'b1), .out(nPCLK), .gate(transistor_1_out));
  Transistor #(.\type ("n")) transistor_15 (.in(1'b0), .out(nPCLK), .gate(transistor_3_out));
  Transistor #(.\type ("n")) transistor_16 (.in(1'b0), .out(nPCLK), .gate(transistor_3_out));
  nor _2_2 (_2_2_out, d_latch_6_not_q, not_3_out);
  nor _3_2 (_3_2_out, d_latch_6_not_q, d_latch_4_not_q);
  Transistor #(.\type ("n")) transistor_17 (.in(1'b1), .out(transistor_5_out), .gate(transistor_3_out));
  Transistor #(.\type ("n")) transistor_18 (.in(1'b0), .out(transistor_5_out), .gate(transistor_1_out));
  Transistor #(.\type ("n")) transistor_19 (.in(1'b1), .out(nPCLK), .gate(transistor_1_out));
  Transistor #(.\type ("n")) transistor_20 (.in(1'b0), .out(nPCLK), .gate(transistor_3_out));
  not not_4 (PCLK, _2_2_out);

  // Notes on the sheet:
  //   9
  //   1
  //   8
  //   Pixel clock is disabled during RESET (PPU stall)
  //   7
  //   PCLK DISTRIBUTION
  //   6
  //   I
  //   II
  //   5
  //   4
  //   1
  //   PCLK = CLK / 5
  //   !
endmodule

module RESET_FF (
  input  nRES,
  input  RESCL,
  output RES,
  output RC
);

  wire nor_1_out;

  not not_1 (RES, nRES);
  nor nor_1 (nor_1_out, RES, RC);
  nor nor_2 (RC, nor_1_out, RESCL);

  // Notes on the sheet:
  //   Reset flip/flop remains set after RESET, until not cleared by RESCL
  //   Reset flip/flop
  //   (REG CLEAR)
endmodule

module HV_COUNTER_BIT (
  input  CLK,
  input  in,
  input  RES,
  input  clear,
  output OUT,
  output PROP_DELAY_OUT,
  output carry_out
);

  wire d_latch_1_q, multiplexer_1_out, multiplexer_2_out, nor_3_out, not_2_out, not_3_out;

  not not_1 (PROP_DELAY_OUT, multiplexer_1_out);
  nor nor_1 (OUT, PROP_DELAY_OUT, RES);
  nor nor_2 (carry_out, PROP_DELAY_OUT, not_2_out);
  not not_2 (not_2_out, in);
  Multiplexer #(.enable("false")) multiplexer_1 (.in0(OUT), .in1(nor_3_out), .out(multiplexer_1_out), .sel(CLK));
  not not_3 (not_3_out, CLK);
  Multiplexer #(.enable("false")) multiplexer_2 (.in0(PROP_DELAY_OUT), .in1(OUT), .out(multiplexer_2_out), .sel(in));
  nor nor_3 (nor_3_out, d_latch_1_q, clear);
  D_latch d_latch_1 (.EN(not_3_out), .D(multiplexer_2_out), .Q(d_latch_1_q));  // open: NOT_Q

  // Notes on the sheet:
  //   carry_in
  //   global RESET
  //   clear manually
endmodule

module H_COUNTER (
  input  RES,
  input  HC,
  input  CLK,
  output H0,
  output H1,
  output H2,
  output H3,
  output H4,
  output H5,
  output H6,
  output H7,
  output H8
);

  wire nor_1_out, undriven, undriven_2, undriven_3, undriven_4, undriven_5;

  nor nor_1 (nor_1_out, undriven_5, undriven_4, undriven_3, undriven_2, undriven);

  // Notes on the sheet:
  //   reduce propagation delay
endmodule

module V_COUNTER (
  input  VIN,
  input  CLK,
  input  RES,
  input  VC,
  output V0,
  output V1,
  output V2,
  output V3,
  output V4,
  output V5,
  output V6,
  output V7,
  output V8
);

  wire nor_1_out, not_1_out, undriven, undriven_2, undriven_3, undriven_4, undriven_5;

  not not_1 (not_1_out, VIN);
  nor nor_1 (nor_1_out, undriven_5, undriven_4, undriven_3, undriven_2, undriven, not_1_out);

  // Notes on the sheet:
  //   reduce propagation delay
endmodule

module HV_SELECT_NTSC (
  input  H8,
  input  H7,
  input  H6,
  input  H5,
  input  H4,
  input  H3,
  input  H2,
  input  H1,
  input  H0,
  input  VB,
  input  BLNK,
  input  V8,
  input  V7,
  input  V6,
  input  V5,
  input  V4,
  input  V3,
  input  V2,
  input  V1,
  input  V0,
  output [5:0] Hnn,
  output _279,
  output _256,
  output _65,
  output _0_7__256_263,
  output _0_255,
  output _339,
  output _63,
  output _255,
  output _0_63,
  output _256_319,
  output _0_255_2,
  output _0_1,
  output _6_7,
  output _4_5,
  output _320_355,
  output _0_255_3,
  output _2_3,
  output _270,
  output _328,
  output _279_2,
  output _304,
  output _323,
  output _308,
  output _340,
  output [7:0] VPOS,
  output _247,
  output _244,
  output _261,
  output _241,
  output _241_2,
  output _0,
  output _240,
  output _261_2,
  output _261_3
);

  wire not_1_out, not_2_out, not_3_out, not_4_out, not_5_out, not_6_out, not_7_out, not_8_out, not_9_out,
       not_10_out, not_11_out, not_12_out, not_13_out, not_14_out, not_15_out, not_16_out, not_17_out;

  not not_1 (not_1_out, H8);
  not not_2 (not_2_out, H7);
  not not_3 (not_3_out, H6);
  not not_4 (not_4_out, H5);
  not not_5 (not_5_out, H4);
  not not_6 (not_6_out, H3);
  not not_7 (not_7_out, H2);
  not not_8 (not_8_out, H1);
  not not_9 (not_9_out, H0);
  not not_10 (not_10_out, V8);
  not not_11 (not_11_out, V7);
  not not_12 (not_12_out, V6);
  not not_13 (not_13_out, V5);
  not not_14 (not_14_out, V4);
  not not_15 (not_15_out, V2);
  not not_16 (not_16_out, V1);
  not not_17 (not_17_out, V0);
  Pull_Resistor #(.pull(1)) pull_resistor_1 (.node(_279));
  Transistor #(.\type ("n")) transistor_1 (.in(1'b0), .out(_279), .gate(not_1_out));
  Transistor #(.\type ("n")) transistor_2 (.in(1'b0), .out(_279), .gate(H7));
  Transistor #(.\type ("n")) transistor_3 (.in(1'b0), .out(_279), .gate(H6));
  Transistor #(.\type ("n")) transistor_4 (.in(1'b0), .out(_279), .gate(H5));
  Transistor #(.\type ("n")) transistor_5 (.in(1'b0), .out(_279), .gate(not_5_out));
  Transistor #(.\type ("n")) transistor_6 (.in(1'b0), .out(_279), .gate(H3));
  Transistor #(.\type ("n")) transistor_7 (.in(1'b0), .out(_279), .gate(not_7_out));
  Transistor #(.\type ("n")) transistor_8 (.in(1'b0), .out(_279), .gate(not_8_out));
  Transistor #(.\type ("n")) transistor_9 (.in(1'b0), .out(_279), .gate(not_9_out));
  Pull_Resistor #(.pull(1)) pull_resistor_2 (.node(_247));
  Transistor #(.\type ("n")) transistor_10 (.in(1'b0), .out(_247), .gate(not_11_out));
  Transistor #(.\type ("n")) transistor_11 (.in(1'b0), .out(_247), .gate(not_12_out));
  Transistor #(.\type ("n")) transistor_12 (.in(1'b0), .out(_247), .gate(not_13_out));
  Transistor #(.\type ("n")) transistor_13 (.in(1'b0), .out(_247), .gate(not_14_out));
  Transistor #(.\type ("n")) transistor_14 (.in(1'b0), .out(_247), .gate(V3));
  Transistor #(.\type ("n")) transistor_15 (.in(1'b0), .out(_247), .gate(not_15_out));
  Transistor #(.\type ("n")) transistor_16 (.in(1'b0), .out(_247), .gate(not_16_out));
  Transistor #(.\type ("n")) transistor_17 (.in(1'b0), .out(_247), .gate(not_17_out));
  Pull_Resistor #(.pull(1)) pull_resistor_3 (.node(_256));
  Transistor #(.\type ("n")) transistor_18 (.in(1'b0), .out(_256), .gate(not_1_out));
  Transistor #(.\type ("n")) transistor_19 (.in(1'b0), .out(_256), .gate(H7));
  Transistor #(.\type ("n")) transistor_20 (.in(1'b0), .out(_256), .gate(H6));
  Transistor #(.\type ("n")) transistor_21 (.in(1'b0), .out(_256), .gate(H5));
  Transistor #(.\type ("n")) transistor_22 (.in(1'b0), .out(_256), .gate(H4));
  Transistor #(.\type ("n")) transistor_23 (.in(1'b0), .out(_256), .gate(H3));
  Transistor #(.\type ("n")) transistor_24 (.in(1'b0), .out(_256), .gate(H2));
  Transistor #(.\type ("n")) transistor_25 (.in(1'b0), .out(_256), .gate(H1));
  Transistor #(.\type ("n")) transistor_26 (.in(1'b0), .out(_256), .gate(H0));
  Pull_Resistor #(.pull(1)) pull_resistor_4 (.node(_244));
  Transistor #(.\type ("n")) transistor_27 (.in(1'b0), .out(_244), .gate(not_11_out));
  Transistor #(.\type ("n")) transistor_28 (.in(1'b0), .out(_244), .gate(not_12_out));
  Transistor #(.\type ("n")) transistor_29 (.in(1'b0), .out(_244), .gate(not_13_out));
  Transistor #(.\type ("n")) transistor_30 (.in(1'b0), .out(_244), .gate(not_14_out));
  Transistor #(.\type ("n")) transistor_31 (.in(1'b0), .out(_244), .gate(V3));
  Transistor #(.\type ("n")) transistor_32 (.in(1'b0), .out(_244), .gate(not_15_out));
  Transistor #(.\type ("n")) transistor_33 (.in(1'b0), .out(_244), .gate(V1));
  Transistor #(.\type ("n")) transistor_34 (.in(1'b0), .out(_244), .gate(V0));
  Pull_Resistor #(.pull(1)) pull_resistor_5 (.node(_65));
  Transistor #(.\type ("n")) transistor_35 (.in(1'b0), .out(_65), .gate(H8));
  Transistor #(.\type ("n")) transistor_36 (.in(1'b0), .out(_65), .gate(H7));
  Transistor #(.\type ("n")) transistor_37 (.in(1'b0), .out(_65), .gate(not_3_out));
  Transistor #(.\type ("n")) transistor_38 (.in(1'b0), .out(_65), .gate(H5));
  Transistor #(.\type ("n")) transistor_39 (.in(1'b0), .out(_65), .gate(H4));
  Transistor #(.\type ("n")) transistor_40 (.in(1'b0), .out(_65), .gate(H3));
  Transistor #(.\type ("n")) transistor_41 (.in(1'b0), .out(_65), .gate(H2));
  Transistor #(.\type ("n")) transistor_42 (.in(1'b0), .out(_65), .gate(H1));
  Transistor #(.\type ("n")) transistor_43 (.in(1'b0), .out(_65), .gate(not_9_out));
  Transistor #(.\type ("n")) transistor_44 (.in(1'b0), .out(_65), .gate(BLNK));
  Pull_Resistor #(.pull(1)) pull_resistor_6 (.node(_261));
  Transistor #(.\type ("n")) transistor_45 (.in(1'b0), .out(_261), .gate(not_10_out));
  Transistor #(.\type ("n")) transistor_46 (.in(1'b0), .out(_261), .gate(V7));
  Transistor #(.\type ("n")) transistor_47 (.in(1'b0), .out(_261), .gate(V6));
  Transistor #(.\type ("n")) transistor_48 (.in(1'b0), .out(_261), .gate(V5));
  Transistor #(.\type ("n")) transistor_49 (.in(1'b0), .out(_261), .gate(V4));
  Transistor #(.\type ("n")) transistor_50 (.in(1'b0), .out(_261), .gate(V3));
  Transistor #(.\type ("n")) transistor_51 (.in(1'b0), .out(_261), .gate(not_15_out));
  Transistor #(.\type ("n")) transistor_52 (.in(1'b0), .out(_261), .gate(V1));
  Transistor #(.\type ("n")) transistor_53 (.in(1'b0), .out(_261), .gate(not_17_out));
  Pull_Resistor #(.pull(1)) pull_resistor_7 (.node(_0_7__256_263));
  Transistor #(.\type ("n")) transistor_54 (.in(1'b0), .out(_0_7__256_263), .gate(H7));
  Transistor #(.\type ("n")) transistor_55 (.in(1'b0), .out(_0_7__256_263), .gate(H6));
  Transistor #(.\type ("n")) transistor_56 (.in(1'b0), .out(_0_7__256_263), .gate(H5));
  Transistor #(.\type ("n")) transistor_57 (.in(1'b0), .out(_0_7__256_263), .gate(H4));
  Transistor #(.\type ("n")) transistor_58 (.in(1'b0), .out(_0_7__256_263), .gate(H3));
  Pull_Resistor #(.pull(1)) pull_resistor_8 (.node(_241));
  Transistor #(.\type ("n")) transistor_59 (.in(1'b0), .out(_241), .gate(not_11_out));
  Transistor #(.\type ("n")) transistor_60 (.in(1'b0), .out(_241), .gate(not_12_out));
  Transistor #(.\type ("n")) transistor_61 (.in(1'b0), .out(_241), .gate(not_13_out));
  Transistor #(.\type ("n")) transistor_62 (.in(1'b0), .out(_241), .gate(not_14_out));
  Transistor #(.\type ("n")) transistor_63 (.in(1'b0), .out(_241), .gate(V3));
  Transistor #(.\type ("n")) transistor_64 (.in(1'b0), .out(_241), .gate(V2));
  Transistor #(.\type ("n")) transistor_65 (.in(1'b0), .out(_241), .gate(V1));
  Transistor #(.\type ("n")) transistor_66 (.in(1'b0), .out(_241), .gate(not_17_out));
  Pull_Resistor #(.pull(1)) pull_resistor_9 (.node(_339));
  Pull_Resistor #(.pull(1)) pull_resistor_10 (.node(_0_255));
  Transistor #(.\type ("n")) transistor_67 (.in(1'b0), .out(_0_255), .gate(H8));
  Transistor #(.\type ("n")) transistor_68 (.in(1'b0), .out(_339), .gate(not_1_out));
  Transistor #(.\type ("n")) transistor_69 (.in(1'b0), .out(_339), .gate(H7));
  Transistor #(.\type ("n")) transistor_70 (.in(1'b0), .out(_339), .gate(not_3_out));
  Transistor #(.\type ("n")) transistor_71 (.in(1'b0), .out(_339), .gate(H5));
  Transistor #(.\type ("n")) transistor_72 (.in(1'b0), .out(_339), .gate(not_5_out));
  Transistor #(.\type ("n")) transistor_73 (.in(1'b0), .out(_339), .gate(H3));
  Transistor #(.\type ("n")) transistor_74 (.in(1'b0), .out(_339), .gate(H2));
  Transistor #(.\type ("n")) transistor_75 (.in(1'b0), .out(_339), .gate(not_8_out));
  Transistor #(.\type ("n")) transistor_76 (.in(1'b0), .out(_339), .gate(not_9_out));
  Transistor #(.\type ("n")) transistor_77 (.in(1'b0), .out(_0_255), .gate(VB));
  Transistor #(.\type ("n")) transistor_78 (.in(1'b0), .out(_339), .gate(BLNK));
  Pull_Resistor #(.pull(1)) pull_resistor_11 (.node(_0));
  Pull_Resistor #(.pull(1)) pull_resistor_12 (.node(_241_2));
  Transistor #(.\type ("n")) transistor_79 (.in(1'b0), .out(_0), .gate(V8));
  Transistor #(.\type ("n")) transistor_80 (.in(1'b0), .out(_0), .gate(V7));
  Transistor #(.\type ("n")) transistor_81 (.in(1'b0), .out(_241_2), .gate(not_11_out));
  Transistor #(.\type ("n")) transistor_82 (.in(1'b0), .out(_0), .gate(V6));
  Transistor #(.\type ("n")) transistor_83 (.in(1'b0), .out(_241_2), .gate(not_12_out));
  Transistor #(.\type ("n")) transistor_84 (.in(1'b0), .out(_0), .gate(V5));
  Transistor #(.\type ("n")) transistor_85 (.in(1'b0), .out(_241_2), .gate(not_13_out));
  Transistor #(.\type ("n")) transistor_86 (.in(1'b0), .out(_0), .gate(V4));
  Transistor #(.\type ("n")) transistor_87 (.in(1'b0), .out(_241_2), .gate(not_14_out));
  Transistor #(.\type ("n")) transistor_88 (.in(1'b0), .out(_241_2), .gate(V3));
  Transistor #(.\type ("n")) transistor_89 (.in(1'b0), .out(_0), .gate(V3));
  Transistor #(.\type ("n")) transistor_90 (.in(1'b0), .out(_241_2), .gate(V2));
  Transistor #(.\type ("n")) transistor_91 (.in(1'b0), .out(_0), .gate(V2));
  Transistor #(.\type ("n")) transistor_92 (.in(1'b0), .out(_241_2), .gate(V1));
  Transistor #(.\type ("n")) transistor_93 (.in(1'b0), .out(_0), .gate(V1));
  Transistor #(.\type ("n")) transistor_94 (.in(1'b0), .out(_0), .gate(V0));
  Transistor #(.\type ("n")) transistor_95 (.in(1'b0), .out(_241_2), .gate(not_17_out));
  Pull_Resistor #(.pull(1)) pull_resistor_13 (.node(_63));
  Transistor #(.\type ("n")) transistor_96 (.in(1'b0), .out(_63), .gate(H8));
  Transistor #(.\type ("n")) transistor_97 (.in(1'b0), .out(_63), .gate(H7));
  Transistor #(.\type ("n")) transistor_98 (.in(1'b0), .out(_63), .gate(H6));
  Transistor #(.\type ("n")) transistor_99 (.in(1'b0), .out(_63), .gate(not_4_out));
  Transistor #(.\type ("n")) transistor_100 (.in(1'b0), .out(_63), .gate(not_5_out));
  Transistor #(.\type ("n")) transistor_101 (.in(1'b0), .out(_63), .gate(not_6_out));
  Transistor #(.\type ("n")) transistor_102 (.in(1'b0), .out(_63), .gate(not_7_out));
  Transistor #(.\type ("n")) transistor_103 (.in(1'b0), .out(_63), .gate(not_8_out));
  Transistor #(.\type ("n")) transistor_104 (.in(1'b0), .out(_63), .gate(not_9_out));
  Transistor #(.\type ("n")) transistor_105 (.in(1'b0), .out(_63), .gate(BLNK));
  Pull_Resistor #(.pull(1)) pull_resistor_14 (.node(_240));
  Transistor #(.\type ("n")) transistor_106 (.in(1'b0), .out(_240), .gate(not_11_out));
  Transistor #(.\type ("n")) transistor_107 (.in(1'b0), .out(_240), .gate(not_12_out));
  Transistor #(.\type ("n")) transistor_108 (.in(1'b0), .out(_240), .gate(not_13_out));
  Transistor #(.\type ("n")) transistor_109 (.in(1'b0), .out(_240), .gate(not_14_out));
  Transistor #(.\type ("n")) transistor_110 (.in(1'b0), .out(_240), .gate(V3));
  Transistor #(.\type ("n")) transistor_111 (.in(1'b0), .out(_240), .gate(V2));
  Transistor #(.\type ("n")) transistor_112 (.in(1'b0), .out(_240), .gate(V1));
  Transistor #(.\type ("n")) transistor_113 (.in(1'b0), .out(_240), .gate(V0));
  Pull_Resistor #(.pull(1)) pull_resistor_15 (.node(_255));
  Transistor #(.\type ("n")) transistor_114 (.in(1'b0), .out(_255), .gate(not_2_out));
  Transistor #(.\type ("n")) transistor_115 (.in(1'b0), .out(_255), .gate(not_3_out));
  Transistor #(.\type ("n")) transistor_116 (.in(1'b0), .out(_255), .gate(not_4_out));
  Transistor #(.\type ("n")) transistor_117 (.in(1'b0), .out(_255), .gate(not_5_out));
  Transistor #(.\type ("n")) transistor_118 (.in(1'b0), .out(_255), .gate(not_6_out));
  Transistor #(.\type ("n")) transistor_119 (.in(1'b0), .out(_255), .gate(not_7_out));
  Transistor #(.\type ("n")) transistor_120 (.in(1'b0), .out(_255), .gate(not_8_out));
  Transistor #(.\type ("n")) transistor_121 (.in(1'b0), .out(_255), .gate(not_9_out));
  Transistor #(.\type ("n")) transistor_122 (.in(1'b0), .out(_255), .gate(BLNK));
  Pull_Resistor #(.pull(1)) pull_resistor_16 (.node(_261_2));
  Transistor #(.\type ("n")) transistor_123 (.in(1'b0), .out(_261_2), .gate(not_10_out));
  Transistor #(.\type ("n")) transistor_124 (.in(1'b0), .out(_261_2), .gate(V7));
  Transistor #(.\type ("n")) transistor_125 (.in(1'b0), .out(_261_2), .gate(V6));
  Transistor #(.\type ("n")) transistor_126 (.in(1'b0), .out(_261_2), .gate(V5));
  Transistor #(.\type ("n")) transistor_127 (.in(1'b0), .out(_261_2), .gate(V4));
  Transistor #(.\type ("n")) transistor_128 (.in(1'b0), .out(_261_2), .gate(V3));
  Transistor #(.\type ("n")) transistor_129 (.in(1'b0), .out(_261_2), .gate(not_15_out));
  Transistor #(.\type ("n")) transistor_130 (.in(1'b0), .out(_261_2), .gate(V1));
  Transistor #(.\type ("n")) transistor_131 (.in(1'b0), .out(_261_2), .gate(not_17_out));
  Pull_Resistor #(.pull(1)) pull_resistor_17 (.node(_0_63));
  Transistor #(.\type ("n")) transistor_132 (.in(1'b0), .out(_0_63), .gate(H8));
  Transistor #(.\type ("n")) transistor_133 (.in(1'b0), .out(_0_63), .gate(H7));
  Transistor #(.\type ("n")) transistor_134 (.in(1'b0), .out(_0_63), .gate(H6));
  Transistor #(.\type ("n")) transistor_135 (.in(1'b0), .out(_0_63), .gate(BLNK));
  Pull_Resistor #(.pull(1)) pull_resistor_18 (.node(_261_3));
  Transistor #(.\type ("n")) transistor_136 (.in(1'b0), .out(_261_3), .gate(not_10_out));
  Transistor #(.\type ("n")) transistor_137 (.in(1'b0), .out(_261_3), .gate(V7));
  Transistor #(.\type ("n")) transistor_138 (.in(1'b0), .out(_261_3), .gate(V6));
  Transistor #(.\type ("n")) transistor_139 (.in(1'b0), .out(_261_3), .gate(V5));
  Transistor #(.\type ("n")) transistor_140 (.in(1'b0), .out(_261_3), .gate(V4));
  Transistor #(.\type ("n")) transistor_141 (.in(1'b0), .out(_261_3), .gate(V3));
  Transistor #(.\type ("n")) transistor_142 (.in(1'b0), .out(_261_3), .gate(not_15_out));
  Transistor #(.\type ("n")) transistor_143 (.in(1'b0), .out(_261_3), .gate(V1));
  Transistor #(.\type ("n")) transistor_144 (.in(1'b0), .out(_261_3), .gate(not_17_out));
  Pull_Resistor #(.pull(1)) pull_resistor_19 (.node(_256_319));
  Transistor #(.\type ("n")) transistor_145 (.in(1'b0), .out(_256_319), .gate(not_1_out));
  Transistor #(.\type ("n")) transistor_146 (.in(1'b0), .out(_256_319), .gate(H7));
  Transistor #(.\type ("n")) transistor_147 (.in(1'b0), .out(_256_319), .gate(H6));
  Transistor #(.\type ("n")) transistor_148 (.in(1'b0), .out(_256_319), .gate(BLNK));
  Pull_Resistor #(.pull(1)) pull_resistor_20 (.node(_0_255_2));
  Transistor #(.\type ("n")) transistor_149 (.in(1'b0), .out(_0_255_2), .gate(H8));
  Transistor #(.\type ("n")) transistor_150 (.in(1'b0), .out(_0_255_2), .gate(VB));
  Transistor #(.\type ("n")) transistor_151 (.in(1'b0), .out(_0_255_2), .gate(BLNK));
  Pull_Resistor #(.pull(1)) pull_resistor_21 (.node(_0_1));
  Transistor #(.\type ("n")) transistor_152 (.in(1'b0), .out(_0_1), .gate(H2));
  Transistor #(.\type ("n")) transistor_153 (.in(1'b0), .out(_0_1), .gate(H1));
  Transistor #(.\type ("n")) transistor_154 (.in(1'b0), .out(_0_1), .gate(BLNK));
  Pull_Resistor #(.pull(1)) pull_resistor_22 (.node(_6_7));
  Pull_Resistor #(.pull(1)) pull_resistor_23 (.node(_4_5));
  Transistor #(.\type ("n")) transistor_155 (.in(1'b0), .out(_4_5), .gate(not_7_out));
  Transistor #(.\type ("n")) transistor_156 (.in(1'b0), .out(_6_7), .gate(not_7_out));
  Transistor #(.\type ("n")) transistor_157 (.in(1'b0), .out(_4_5), .gate(H1));
  Transistor #(.\type ("n")) transistor_158 (.in(1'b0), .out(_6_7), .gate(not_8_out));
  Pull_Resistor #(.pull(1)) pull_resistor_24 (.node(_320_355));
  Transistor #(.\type ("n")) transistor_159 (.in(1'b0), .out(_320_355), .gate(not_1_out));
  Transistor #(.\type ("n")) transistor_160 (.in(1'b0), .out(_320_355), .gate(not_3_out));
  Transistor #(.\type ("n")) transistor_161 (.in(1'b0), .out(_320_355), .gate(H5));
  Transistor #(.\type ("n")) transistor_162 (.in(1'b0), .out(_320_355), .gate(H4));
  Transistor #(.\type ("n")) transistor_163 (.in(1'b0), .out(_320_355), .gate(BLNK));
  Pull_Resistor #(.pull(1)) pull_resistor_25 (.node(_0_255_3));
  Transistor #(.\type ("n")) transistor_164 (.in(1'b0), .out(_0_255_3), .gate(H8));
  Transistor #(.\type ("n")) transistor_165 (.in(1'b0), .out(_0_255_3), .gate(BLNK));
  Pull_Resistor #(.pull(1)) pull_resistor_26 (.node(_2_3));
  Transistor #(.\type ("n")) transistor_166 (.in(1'b0), .out(_2_3), .gate(H2));
  Transistor #(.\type ("n")) transistor_167 (.in(1'b0), .out(_2_3), .gate(not_8_out));
  Pull_Resistor #(.pull(1)) pull_resistor_27 (.node(_270));
  Transistor #(.\type ("n")) transistor_168 (.in(1'b0), .out(_270), .gate(not_1_out));
  Transistor #(.\type ("n")) transistor_169 (.in(1'b0), .out(_270), .gate(H7));
  Transistor #(.\type ("n")) transistor_170 (.in(1'b0), .out(_270), .gate(H6));
  Transistor #(.\type ("n")) transistor_171 (.in(1'b0), .out(_270), .gate(H5));
  Transistor #(.\type ("n")) transistor_172 (.in(1'b0), .out(_270), .gate(H4));
  Transistor #(.\type ("n")) transistor_173 (.in(1'b0), .out(_270), .gate(not_6_out));
  Transistor #(.\type ("n")) transistor_174 (.in(1'b0), .out(_270), .gate(not_7_out));
  Transistor #(.\type ("n")) transistor_175 (.in(1'b0), .out(_270), .gate(not_8_out));
  Transistor #(.\type ("n")) transistor_176 (.in(1'b0), .out(_270), .gate(H0));
  Pull_Resistor #(.pull(1)) pull_resistor_28 (.node(_328));
  Transistor #(.\type ("n")) transistor_177 (.in(1'b0), .out(_328), .gate(not_1_out));
  Transistor #(.\type ("n")) transistor_178 (.in(1'b0), .out(_328), .gate(H7));
  Transistor #(.\type ("n")) transistor_179 (.in(1'b0), .out(_328), .gate(not_3_out));
  Transistor #(.\type ("n")) transistor_180 (.in(1'b0), .out(_328), .gate(H5));
  Transistor #(.\type ("n")) transistor_181 (.in(1'b0), .out(_328), .gate(H4));
  Transistor #(.\type ("n")) transistor_182 (.in(1'b0), .out(_328), .gate(not_6_out));
  Transistor #(.\type ("n")) transistor_183 (.in(1'b0), .out(_328), .gate(H2));
  Transistor #(.\type ("n")) transistor_184 (.in(1'b0), .out(_328), .gate(H1));
  Transistor #(.\type ("n")) transistor_185 (.in(1'b0), .out(_328), .gate(H0));
  Pull_Resistor #(.pull(1)) pull_resistor_29 (.node(_279_2));
  Transistor #(.\type ("n")) transistor_186 (.in(1'b0), .out(_279_2), .gate(not_1_out));
  Transistor #(.\type ("n")) transistor_187 (.in(1'b0), .out(_279_2), .gate(H7));
  Transistor #(.\type ("n")) transistor_188 (.in(1'b0), .out(_279_2), .gate(H6));
  Transistor #(.\type ("n")) transistor_189 (.in(1'b0), .out(_279_2), .gate(H5));
  Transistor #(.\type ("n")) transistor_190 (.in(1'b0), .out(_279_2), .gate(not_5_out));
  Transistor #(.\type ("n")) transistor_191 (.in(1'b0), .out(_279_2), .gate(H3));
  Transistor #(.\type ("n")) transistor_192 (.in(1'b0), .out(_279_2), .gate(not_7_out));
  Transistor #(.\type ("n")) transistor_193 (.in(1'b0), .out(_279_2), .gate(not_8_out));
  Transistor #(.\type ("n")) transistor_194 (.in(1'b0), .out(_279_2), .gate(not_9_out));
  Pull_Resistor #(.pull(1)) pull_resistor_30 (.node(_304));
  Pull_Resistor #(.pull(1)) pull_resistor_31 (.node(_323));
  Transistor #(.\type ("n")) transistor_195 (.in(1'b0), .out(_323), .gate(not_1_out));
  Transistor #(.\type ("n")) transistor_196 (.in(1'b0), .out(_304), .gate(not_1_out));
  Transistor #(.\type ("n")) transistor_197 (.in(1'b0), .out(_304), .gate(H7));
  Transistor #(.\type ("n")) transistor_198 (.in(1'b0), .out(_323), .gate(H7));
  Transistor #(.\type ("n")) transistor_199 (.in(1'b0), .out(_304), .gate(H6));
  Transistor #(.\type ("n")) transistor_200 (.in(1'b0), .out(_323), .gate(not_3_out));
  Transistor #(.\type ("n")) transistor_201 (.in(1'b0), .out(_323), .gate(H5));
  Transistor #(.\type ("n")) transistor_202 (.in(1'b0), .out(_304), .gate(not_4_out));
  Transistor #(.\type ("n")) transistor_203 (.in(1'b0), .out(_323), .gate(H4));
  Transistor #(.\type ("n")) transistor_204 (.in(1'b0), .out(_304), .gate(not_5_out));
  Transistor #(.\type ("n")) transistor_205 (.in(1'b0), .out(_304), .gate(H3));
  Transistor #(.\type ("n")) transistor_206 (.in(1'b0), .out(_323), .gate(H3));
  Transistor #(.\type ("n")) transistor_207 (.in(1'b0), .out(_304), .gate(H2));
  Transistor #(.\type ("n")) transistor_208 (.in(1'b0), .out(_323), .gate(H2));
  Transistor #(.\type ("n")) transistor_209 (.in(1'b0), .out(_304), .gate(H1));
  Transistor #(.\type ("n")) transistor_210 (.in(1'b0), .out(_323), .gate(not_8_out));
  Transistor #(.\type ("n")) transistor_211 (.in(1'b0), .out(_304), .gate(H0));
  Transistor #(.\type ("n")) transistor_212 (.in(1'b0), .out(_323), .gate(not_9_out));
  Pull_Resistor #(.pull(1)) pull_resistor_32 (.node(_308));
  Transistor #(.\type ("n")) transistor_213 (.in(1'b0), .out(_308), .gate(not_1_out));
  Transistor #(.\type ("n")) transistor_214 (.in(1'b0), .out(_308), .gate(H7));
  Transistor #(.\type ("n")) transistor_215 (.in(1'b0), .out(_308), .gate(H6));
  Transistor #(.\type ("n")) transistor_216 (.in(1'b0), .out(_308), .gate(not_4_out));
  Transistor #(.\type ("n")) transistor_217 (.in(1'b0), .out(_308), .gate(not_5_out));
  Transistor #(.\type ("n")) transistor_218 (.in(1'b0), .out(_308), .gate(H3));
  Transistor #(.\type ("n")) transistor_219 (.in(1'b0), .out(_308), .gate(not_7_out));
  Transistor #(.\type ("n")) transistor_220 (.in(1'b0), .out(_308), .gate(H1));
  Transistor #(.\type ("n")) transistor_221 (.in(1'b0), .out(_308), .gate(H0));
  Pull_Resistor #(.pull(1)) pull_resistor_33 (.node(_340));
  Transistor #(.\type ("n")) transistor_222 (.in(1'b0), .out(_340), .gate(not_1_out));
  Transistor #(.\type ("n")) transistor_223 (.in(1'b0), .out(_340), .gate(H7));
  Transistor #(.\type ("n")) transistor_224 (.in(1'b0), .out(_340), .gate(not_3_out));
  Transistor #(.\type ("n")) transistor_225 (.in(1'b0), .out(_340), .gate(H5));
  Transistor #(.\type ("n")) transistor_226 (.in(1'b0), .out(_340), .gate(not_5_out));
  Transistor #(.\type ("n")) transistor_227 (.in(1'b0), .out(_340), .gate(H3));
  Transistor #(.\type ("n")) transistor_228 (.in(1'b0), .out(_340), .gate(not_7_out));
  Transistor #(.\type ("n")) transistor_229 (.in(1'b0), .out(_340), .gate(H1));
  Transistor #(.\type ("n")) transistor_230 (.in(1'b0), .out(_340), .gate(H0));

  assign Hnn = {H5, H4, H3, H2, H1, H0};
  assign VPOS = {V7, V6, V5, V4, V3, V2, V1, V0};
endmodule

module HV_SELECT_PAL (
  input  H8,
  input  H7,
  input  H6,
  input  H5,
  input  H4,
  input  H3,
  input  H2,
  input  H1,
  input  H0,
  input  VB,
  input  BLNK,
  input  V8,
  input  V7,
  input  V6,
  input  V5,
  input  V4,
  input  V3,
  input  V2,
  input  V1,
  input  V0,
  output [5:0] Hnn,
  output _277,
  output _256,
  output _65,
  output _0_7__256_263,
  output _0_255,
  output _339,
  output _63,
  output _255,
  output _0_63,
  output _256_319,
  output _0_255_2,
  output _0_1,
  output _6_7,
  output _4_5,
  output _320_355,
  output _0___255,
  output _2_3,
  output _256_2,
  output _4,
  output _277_2,
  output _302,
  output _321,
  output _306,
  output _340,
  output [7:0] VPOS,
  output _272,
  output _269,
  output _1,
  output _240,
  output _241,
  output _0,
  output _240_2,
  output _311,
  output _311_2,
  output _265
);

  wire not_1_out, not_2_out, not_3_out, not_4_out, not_5_out, not_6_out, not_7_out, not_8_out, not_9_out,
       not_10_out, not_11_out, not_12_out, not_13_out, not_14_out, not_15_out, not_16_out, not_17_out,
       not_18_out;

  not not_1 (not_1_out, H8);
  not not_2 (not_2_out, H7);
  not not_3 (not_3_out, H6);
  not not_4 (not_4_out, H5);
  not not_5 (not_5_out, H4);
  not not_6 (not_6_out, H3);
  not not_7 (not_7_out, H2);
  not not_8 (not_8_out, H1);
  not not_9 (not_9_out, H0);
  not not_10 (not_10_out, V8);
  not not_11 (not_11_out, V7);
  not not_12 (not_12_out, V6);
  not not_13 (not_13_out, V5);
  not not_14 (not_14_out, V4);
  not not_15 (not_15_out, V3);
  not not_16 (not_16_out, V2);
  not not_17 (not_17_out, V1);
  not not_18 (not_18_out, V0);
  Pull_Resistor #(.pull(1)) pull_resistor_1 (.node(_277));
  Transistor #(.\type ("n")) transistor_1 (.in(1'b0), .out(_277), .gate(not_1_out));
  Transistor #(.\type ("n")) transistor_2 (.in(1'b0), .out(_277), .gate(H7));
  Transistor #(.\type ("n")) transistor_3 (.in(1'b0), .out(_277), .gate(H6));
  Transistor #(.\type ("n")) transistor_4 (.in(1'b0), .out(_277), .gate(H5));
  Transistor #(.\type ("n")) transistor_5 (.in(1'b0), .out(_277), .gate(not_5_out));
  Transistor #(.\type ("n")) transistor_6 (.in(1'b0), .out(_277), .gate(H3));
  Transistor #(.\type ("n")) transistor_7 (.in(1'b0), .out(_277), .gate(not_7_out));
  Transistor #(.\type ("n")) transistor_8 (.in(1'b0), .out(_277), .gate(H1));
  Transistor #(.\type ("n")) transistor_9 (.in(1'b0), .out(_277), .gate(not_9_out));
  Pull_Resistor #(.pull(1)) pull_resistor_2 (.node(_272));
  Transistor #(.\type ("n")) transistor_10 (.in(1'b0), .out(_272), .gate(not_10_out));
  Transistor #(.\type ("n")) transistor_11 (.in(1'b0), .out(_272), .gate(V7));
  Transistor #(.\type ("n")) transistor_12 (.in(1'b0), .out(_272), .gate(V6));
  Transistor #(.\type ("n")) transistor_13 (.in(1'b0), .out(_272), .gate(V5));
  Transistor #(.\type ("n")) transistor_14 (.in(1'b0), .out(_272), .gate(not_14_out));
  Transistor #(.\type ("n")) transistor_15 (.in(1'b0), .out(_272), .gate(V3));
  Transistor #(.\type ("n")) transistor_16 (.in(1'b0), .out(_272), .gate(V2));
  Transistor #(.\type ("n")) transistor_17 (.in(1'b0), .out(_272), .gate(V1));
  Transistor #(.\type ("n")) transistor_18 (.in(1'b0), .out(_272), .gate(V0));
  Pull_Resistor #(.pull(1)) pull_resistor_3 (.node(_256));
  Transistor #(.\type ("n")) transistor_19 (.in(1'b0), .out(_256), .gate(not_1_out));
  Transistor #(.\type ("n")) transistor_20 (.in(1'b0), .out(_256), .gate(H7));
  Transistor #(.\type ("n")) transistor_21 (.in(1'b0), .out(_256), .gate(H6));
  Transistor #(.\type ("n")) transistor_22 (.in(1'b0), .out(_256), .gate(H5));
  Transistor #(.\type ("n")) transistor_23 (.in(1'b0), .out(_256), .gate(H4));
  Transistor #(.\type ("n")) transistor_24 (.in(1'b0), .out(_256), .gate(H3));
  Transistor #(.\type ("n")) transistor_25 (.in(1'b0), .out(_256), .gate(H2));
  Transistor #(.\type ("n")) transistor_26 (.in(1'b0), .out(_256), .gate(H1));
  Transistor #(.\type ("n")) transistor_27 (.in(1'b0), .out(_256), .gate(H0));
  Pull_Resistor #(.pull(1)) pull_resistor_4 (.node(_269));
  Transistor #(.\type ("n")) transistor_28 (.in(1'b0), .out(_269), .gate(not_10_out));
  Transistor #(.\type ("n")) transistor_29 (.in(1'b0), .out(_269), .gate(V7));
  Transistor #(.\type ("n")) transistor_30 (.in(1'b0), .out(_269), .gate(V6));
  Transistor #(.\type ("n")) transistor_31 (.in(1'b0), .out(_269), .gate(V5));
  Transistor #(.\type ("n")) transistor_32 (.in(1'b0), .out(_269), .gate(V4));
  Transistor #(.\type ("n")) transistor_33 (.in(1'b0), .out(_269), .gate(not_15_out));
  Transistor #(.\type ("n")) transistor_34 (.in(1'b0), .out(_269), .gate(not_16_out));
  Transistor #(.\type ("n")) transistor_35 (.in(1'b0), .out(_269), .gate(V1));
  Transistor #(.\type ("n")) transistor_36 (.in(1'b0), .out(_269), .gate(not_18_out));
  Pull_Resistor #(.pull(1)) pull_resistor_5 (.node(_65));
  Transistor #(.\type ("n")) transistor_37 (.in(1'b0), .out(_65), .gate(H8));
  Transistor #(.\type ("n")) transistor_38 (.in(1'b0), .out(_65), .gate(H7));
  Transistor #(.\type ("n")) transistor_39 (.in(1'b0), .out(_65), .gate(not_3_out));
  Transistor #(.\type ("n")) transistor_40 (.in(1'b0), .out(_65), .gate(H5));
  Transistor #(.\type ("n")) transistor_41 (.in(1'b0), .out(_65), .gate(H4));
  Transistor #(.\type ("n")) transistor_42 (.in(1'b0), .out(_65), .gate(H3));
  Transistor #(.\type ("n")) transistor_43 (.in(1'b0), .out(_65), .gate(H2));
  Transistor #(.\type ("n")) transistor_44 (.in(1'b0), .out(_65), .gate(H1));
  Transistor #(.\type ("n")) transistor_45 (.in(1'b0), .out(_65), .gate(not_9_out));
  Transistor #(.\type ("n")) transistor_46 (.in(1'b0), .out(_65), .gate(BLNK));
  Pull_Resistor #(.pull(1)) pull_resistor_6 (.node(_1));
  Transistor #(.\type ("n")) transistor_47 (.in(1'b0), .out(_1), .gate(V8));
  Transistor #(.\type ("n")) transistor_48 (.in(1'b0), .out(_1), .gate(V7));
  Transistor #(.\type ("n")) transistor_49 (.in(1'b0), .out(_1), .gate(V6));
  Transistor #(.\type ("n")) transistor_50 (.in(1'b0), .out(_1), .gate(V5));
  Transistor #(.\type ("n")) transistor_51 (.in(1'b0), .out(_1), .gate(V4));
  Transistor #(.\type ("n")) transistor_52 (.in(1'b0), .out(_1), .gate(V3));
  Transistor #(.\type ("n")) transistor_53 (.in(1'b0), .out(_1), .gate(V2));
  Transistor #(.\type ("n")) transistor_54 (.in(1'b0), .out(_1), .gate(V1));
  Transistor #(.\type ("n")) transistor_55 (.in(1'b0), .out(_1), .gate(not_18_out));
  Pull_Resistor #(.pull(1)) pull_resistor_7 (.node(_0_7__256_263));
  Transistor #(.\type ("n")) transistor_56 (.in(1'b0), .out(_0_7__256_263), .gate(H7));
  Transistor #(.\type ("n")) transistor_57 (.in(1'b0), .out(_0_7__256_263), .gate(H6));
  Transistor #(.\type ("n")) transistor_58 (.in(1'b0), .out(_0_7__256_263), .gate(H5));
  Transistor #(.\type ("n")) transistor_59 (.in(1'b0), .out(_0_7__256_263), .gate(H4));
  Transistor #(.\type ("n")) transistor_60 (.in(1'b0), .out(_0_7__256_263), .gate(H3));
  Pull_Resistor #(.pull(1)) pull_resistor_8 (.node(_240));
  Transistor #(.\type ("n")) transistor_61 (.in(1'b0), .out(_240), .gate(not_11_out));
  Transistor #(.\type ("n")) transistor_62 (.in(1'b0), .out(_240), .gate(not_12_out));
  Transistor #(.\type ("n")) transistor_63 (.in(1'b0), .out(_240), .gate(not_13_out));
  Transistor #(.\type ("n")) transistor_64 (.in(1'b0), .out(_240), .gate(not_14_out));
  Transistor #(.\type ("n")) transistor_65 (.in(1'b0), .out(_240), .gate(V3));
  Transistor #(.\type ("n")) transistor_66 (.in(1'b0), .out(_240), .gate(V2));
  Transistor #(.\type ("n")) transistor_67 (.in(1'b0), .out(_240), .gate(V1));
  Transistor #(.\type ("n")) transistor_68 (.in(1'b0), .out(_240), .gate(V0));
  Pull_Resistor #(.pull(1)) pull_resistor_9 (.node(_0_255));
  Pull_Resistor #(.pull(1)) pull_resistor_10 (.node(_339));
  Transistor #(.\type ("n")) transistor_69 (.in(1'b0), .out(_0_255), .gate(H8));
  Transistor #(.\type ("n")) transistor_70 (.in(1'b0), .out(_339), .gate(not_1_out));
  Transistor #(.\type ("n")) transistor_71 (.in(1'b0), .out(_339), .gate(H7));
  Transistor #(.\type ("n")) transistor_72 (.in(1'b0), .out(_339), .gate(not_3_out));
  Transistor #(.\type ("n")) transistor_73 (.in(1'b0), .out(_339), .gate(H5));
  Transistor #(.\type ("n")) transistor_74 (.in(1'b0), .out(_339), .gate(not_5_out));
  Transistor #(.\type ("n")) transistor_75 (.in(1'b0), .out(_339), .gate(H3));
  Transistor #(.\type ("n")) transistor_76 (.in(1'b0), .out(_339), .gate(H2));
  Transistor #(.\type ("n")) transistor_77 (.in(1'b0), .out(_339), .gate(not_8_out));
  Transistor #(.\type ("n")) transistor_78 (.in(1'b0), .out(_339), .gate(not_9_out));
  Transistor #(.\type ("n")) transistor_79 (.in(1'b0), .out(_0_255), .gate(VB));
  Transistor #(.\type ("n")) transistor_80 (.in(1'b0), .out(_339), .gate(BLNK));
  Pull_Resistor #(.pull(1)) pull_resistor_11 (.node(_241));
  Pull_Resistor #(.pull(1)) pull_resistor_12 (.node(_0));
  Transistor #(.\type ("n")) transistor_81 (.in(1'b0), .out(_0), .gate(V8));
  Transistor #(.\type ("n")) transistor_82 (.in(1'b0), .out(_0), .gate(V7));
  Transistor #(.\type ("n")) transistor_83 (.in(1'b0), .out(_241), .gate(not_11_out));
  Transistor #(.\type ("n")) transistor_84 (.in(1'b0), .out(_0), .gate(V6));
  Transistor #(.\type ("n")) transistor_85 (.in(1'b0), .out(_241), .gate(not_12_out));
  Transistor #(.\type ("n")) transistor_86 (.in(1'b0), .out(_0), .gate(V5));
  Transistor #(.\type ("n")) transistor_87 (.in(1'b0), .out(_241), .gate(not_13_out));
  Transistor #(.\type ("n")) transistor_88 (.in(1'b0), .out(_0), .gate(V4));
  Transistor #(.\type ("n")) transistor_89 (.in(1'b0), .out(_241), .gate(not_14_out));
  Transistor #(.\type ("n")) transistor_90 (.in(1'b0), .out(_241), .gate(V3));
  Transistor #(.\type ("n")) transistor_91 (.in(1'b0), .out(_0), .gate(V3));
  Transistor #(.\type ("n")) transistor_92 (.in(1'b0), .out(_0), .gate(V2));
  Transistor #(.\type ("n")) transistor_93 (.in(1'b0), .out(_241), .gate(V2));
  Transistor #(.\type ("n")) transistor_94 (.in(1'b0), .out(_0), .gate(V1));
  Transistor #(.\type ("n")) transistor_95 (.in(1'b0), .out(_241), .gate(V1));
  Transistor #(.\type ("n")) transistor_96 (.in(1'b0), .out(_0), .gate(V0));
  Transistor #(.\type ("n")) transistor_97 (.in(1'b0), .out(_241), .gate(not_18_out));
  Pull_Resistor #(.pull(1)) pull_resistor_13 (.node(_63));
  Transistor #(.\type ("n")) transistor_98 (.in(1'b0), .out(_63), .gate(H8));
  Transistor #(.\type ("n")) transistor_99 (.in(1'b0), .out(_63), .gate(H7));
  Transistor #(.\type ("n")) transistor_100 (.in(1'b0), .out(_63), .gate(H6));
  Transistor #(.\type ("n")) transistor_101 (.in(1'b0), .out(_63), .gate(not_4_out));
  Transistor #(.\type ("n")) transistor_102 (.in(1'b0), .out(_63), .gate(not_5_out));
  Transistor #(.\type ("n")) transistor_103 (.in(1'b0), .out(_63), .gate(not_6_out));
  Transistor #(.\type ("n")) transistor_104 (.in(1'b0), .out(_63), .gate(not_7_out));
  Transistor #(.\type ("n")) transistor_105 (.in(1'b0), .out(_63), .gate(not_8_out));
  Transistor #(.\type ("n")) transistor_106 (.in(1'b0), .out(_63), .gate(not_9_out));
  Transistor #(.\type ("n")) transistor_107 (.in(1'b0), .out(_63), .gate(BLNK));
  Pull_Resistor #(.pull(1)) pull_resistor_14 (.node(_240_2));
  Transistor #(.\type ("n")) transistor_108 (.in(1'b0), .out(_240_2), .gate(not_11_out));
  Transistor #(.\type ("n")) transistor_109 (.in(1'b0), .out(_240_2), .gate(not_12_out));
  Transistor #(.\type ("n")) transistor_110 (.in(1'b0), .out(_240_2), .gate(not_13_out));
  Transistor #(.\type ("n")) transistor_111 (.in(1'b0), .out(_240_2), .gate(not_14_out));
  Transistor #(.\type ("n")) transistor_112 (.in(1'b0), .out(_240_2), .gate(V3));
  Transistor #(.\type ("n")) transistor_113 (.in(1'b0), .out(_240_2), .gate(V2));
  Transistor #(.\type ("n")) transistor_114 (.in(1'b0), .out(_240_2), .gate(V1));
  Transistor #(.\type ("n")) transistor_115 (.in(1'b0), .out(_240_2), .gate(V0));
  Pull_Resistor #(.pull(1)) pull_resistor_15 (.node(_255));
  Transistor #(.\type ("n")) transistor_116 (.in(1'b0), .out(_255), .gate(not_2_out));
  Transistor #(.\type ("n")) transistor_117 (.in(1'b0), .out(_255), .gate(not_3_out));
  Transistor #(.\type ("n")) transistor_118 (.in(1'b0), .out(_255), .gate(not_4_out));
  Transistor #(.\type ("n")) transistor_119 (.in(1'b0), .out(_255), .gate(not_5_out));
  Transistor #(.\type ("n")) transistor_120 (.in(1'b0), .out(_255), .gate(not_6_out));
  Transistor #(.\type ("n")) transistor_121 (.in(1'b0), .out(_255), .gate(not_7_out));
  Transistor #(.\type ("n")) transistor_122 (.in(1'b0), .out(_255), .gate(not_8_out));
  Transistor #(.\type ("n")) transistor_123 (.in(1'b0), .out(_255), .gate(not_9_out));
  Transistor #(.\type ("n")) transistor_124 (.in(1'b0), .out(_255), .gate(BLNK));
  Pull_Resistor #(.pull(1)) pull_resistor_16 (.node(_311));
  Transistor #(.\type ("n")) transistor_125 (.in(1'b0), .out(_311), .gate(not_10_out));
  Transistor #(.\type ("n")) transistor_126 (.in(1'b0), .out(_311), .gate(V7));
  Transistor #(.\type ("n")) transistor_127 (.in(1'b0), .out(_311), .gate(V6));
  Transistor #(.\type ("n")) transistor_128 (.in(1'b0), .out(_311), .gate(not_13_out));
  Transistor #(.\type ("n")) transistor_129 (.in(1'b0), .out(_311), .gate(not_14_out));
  Transistor #(.\type ("n")) transistor_130 (.in(1'b0), .out(_311), .gate(V3));
  Transistor #(.\type ("n")) transistor_131 (.in(1'b0), .out(_311), .gate(not_16_out));
  Transistor #(.\type ("n")) transistor_132 (.in(1'b0), .out(_311), .gate(not_17_out));
  Transistor #(.\type ("n")) transistor_133 (.in(1'b0), .out(_311), .gate(not_18_out));
  Pull_Resistor #(.pull(1)) pull_resistor_17 (.node(_0_63));
  Transistor #(.\type ("n")) transistor_134 (.in(1'b0), .out(_0_63), .gate(H8));
  Transistor #(.\type ("n")) transistor_135 (.in(1'b0), .out(_0_63), .gate(H7));
  Transistor #(.\type ("n")) transistor_136 (.in(1'b0), .out(_0_63), .gate(H6));
  Transistor #(.\type ("n")) transistor_137 (.in(1'b0), .out(_0_63), .gate(BLNK));
  Pull_Resistor #(.pull(1)) pull_resistor_18 (.node(_311_2));
  Transistor #(.\type ("n")) transistor_138 (.in(1'b0), .out(_311_2), .gate(not_10_out));
  Transistor #(.\type ("n")) transistor_139 (.in(1'b0), .out(_311_2), .gate(V7));
  Transistor #(.\type ("n")) transistor_140 (.in(1'b0), .out(_311_2), .gate(V6));
  Transistor #(.\type ("n")) transistor_141 (.in(1'b0), .out(_311_2), .gate(not_13_out));
  Transistor #(.\type ("n")) transistor_142 (.in(1'b0), .out(_311_2), .gate(not_14_out));
  Transistor #(.\type ("n")) transistor_143 (.in(1'b0), .out(_311_2), .gate(V3));
  Transistor #(.\type ("n")) transistor_144 (.in(1'b0), .out(_311_2), .gate(not_16_out));
  Transistor #(.\type ("n")) transistor_145 (.in(1'b0), .out(_311_2), .gate(not_17_out));
  Transistor #(.\type ("n")) transistor_146 (.in(1'b0), .out(_311_2), .gate(not_18_out));
  Pull_Resistor #(.pull(1)) pull_resistor_19 (.node(_256_319));
  Transistor #(.\type ("n")) transistor_147 (.in(1'b0), .out(_256_319), .gate(not_1_out));
  Transistor #(.\type ("n")) transistor_148 (.in(1'b0), .out(_256_319), .gate(H7));
  Transistor #(.\type ("n")) transistor_149 (.in(1'b0), .out(_256_319), .gate(H6));
  Transistor #(.\type ("n")) transistor_150 (.in(1'b0), .out(_256_319), .gate(BLNK));
  Pull_Resistor #(.pull(1)) pull_resistor_20 (.node(_265));
  Transistor #(.\type ("n")) transistor_151 (.in(1'b0), .out(_265), .gate(not_10_out));
  Transistor #(.\type ("n")) transistor_152 (.in(1'b0), .out(_265), .gate(V7));
  Transistor #(.\type ("n")) transistor_153 (.in(1'b0), .out(_265), .gate(V6));
  Transistor #(.\type ("n")) transistor_154 (.in(1'b0), .out(_265), .gate(V5));
  Transistor #(.\type ("n")) transistor_155 (.in(1'b0), .out(_265), .gate(V4));
  Transistor #(.\type ("n")) transistor_156 (.in(1'b0), .out(_265), .gate(not_15_out));
  Transistor #(.\type ("n")) transistor_157 (.in(1'b0), .out(_265), .gate(V2));
  Transistor #(.\type ("n")) transistor_158 (.in(1'b0), .out(_265), .gate(V1));
  Transistor #(.\type ("n")) transistor_159 (.in(1'b0), .out(_265), .gate(not_18_out));
  Pull_Resistor #(.pull(1)) pull_resistor_21 (.node(_0_255_2));
  Transistor #(.\type ("n")) transistor_160 (.in(1'b0), .out(_0_255_2), .gate(H8));
  Transistor #(.\type ("n")) transistor_161 (.in(1'b0), .out(_0_255_2), .gate(VB));
  Transistor #(.\type ("n")) transistor_162 (.in(1'b0), .out(_0_255_2), .gate(BLNK));
  Pull_Resistor #(.pull(1)) pull_resistor_22 (.node(_0_1));
  Transistor #(.\type ("n")) transistor_163 (.in(1'b0), .out(_0_1), .gate(H2));
  Transistor #(.\type ("n")) transistor_164 (.in(1'b0), .out(_0_1), .gate(H1));
  Transistor #(.\type ("n")) transistor_165 (.in(1'b0), .out(_0_1), .gate(BLNK));
  Pull_Resistor #(.pull(1)) pull_resistor_23 (.node(_6_7));
  Pull_Resistor #(.pull(1)) pull_resistor_24 (.node(_4_5));
  Transistor #(.\type ("n")) transistor_166 (.in(1'b0), .out(_4_5), .gate(not_7_out));
  Transistor #(.\type ("n")) transistor_167 (.in(1'b0), .out(_6_7), .gate(not_7_out));
  Transistor #(.\type ("n")) transistor_168 (.in(1'b0), .out(_4_5), .gate(H1));
  Transistor #(.\type ("n")) transistor_169 (.in(1'b0), .out(_6_7), .gate(not_8_out));
  Pull_Resistor #(.pull(1)) pull_resistor_25 (.node(_320_355));
  Transistor #(.\type ("n")) transistor_170 (.in(1'b0), .out(_320_355), .gate(not_1_out));
  Transistor #(.\type ("n")) transistor_171 (.in(1'b0), .out(_320_355), .gate(not_3_out));
  Transistor #(.\type ("n")) transistor_172 (.in(1'b0), .out(_320_355), .gate(H5));
  Transistor #(.\type ("n")) transistor_173 (.in(1'b0), .out(_320_355), .gate(H4));
  Transistor #(.\type ("n")) transistor_174 (.in(1'b0), .out(_320_355), .gate(BLNK));
  Pull_Resistor #(.pull(1)) pull_resistor_26 (.node(_0___255));
  Transistor #(.\type ("n")) transistor_175 (.in(1'b0), .out(_0___255), .gate(H8));
  Transistor #(.\type ("n")) transistor_176 (.in(1'b0), .out(_0___255), .gate(BLNK));
  Pull_Resistor #(.pull(1)) pull_resistor_27 (.node(_2_3));
  Transistor #(.\type ("n")) transistor_177 (.in(1'b0), .out(_2_3), .gate(H2));
  Transistor #(.\type ("n")) transistor_178 (.in(1'b0), .out(_2_3), .gate(not_8_out));
  Pull_Resistor #(.pull(1)) pull_resistor_28 (.node(_256_2));
  Transistor #(.\type ("n")) transistor_179 (.in(1'b0), .out(_256_2), .gate(not_1_out));
  Transistor #(.\type ("n")) transistor_180 (.in(1'b0), .out(_256_2), .gate(H7));
  Transistor #(.\type ("n")) transistor_181 (.in(1'b0), .out(_256_2), .gate(H6));
  Transistor #(.\type ("n")) transistor_182 (.in(1'b0), .out(_256_2), .gate(H5));
  Transistor #(.\type ("n")) transistor_183 (.in(1'b0), .out(_256_2), .gate(H4));
  Transistor #(.\type ("n")) transistor_184 (.in(1'b0), .out(_256_2), .gate(H3));
  Transistor #(.\type ("n")) transistor_185 (.in(1'b0), .out(_256_2), .gate(H2));
  Transistor #(.\type ("n")) transistor_186 (.in(1'b0), .out(_256_2), .gate(H1));
  Transistor #(.\type ("n")) transistor_187 (.in(1'b0), .out(_256_2), .gate(H0));
  Pull_Resistor #(.pull(1)) pull_resistor_29 (.node(_4));
  Transistor #(.\type ("n")) transistor_188 (.in(1'b0), .out(_4), .gate(H8));
  Transistor #(.\type ("n")) transistor_189 (.in(1'b0), .out(_4), .gate(H7));
  Transistor #(.\type ("n")) transistor_190 (.in(1'b0), .out(_4), .gate(H6));
  Transistor #(.\type ("n")) transistor_191 (.in(1'b0), .out(_4), .gate(H5));
  Transistor #(.\type ("n")) transistor_192 (.in(1'b0), .out(_4), .gate(H4));
  Transistor #(.\type ("n")) transistor_193 (.in(1'b0), .out(_4), .gate(H3));
  Transistor #(.\type ("n")) transistor_194 (.in(1'b0), .out(_4), .gate(not_7_out));
  Transistor #(.\type ("n")) transistor_195 (.in(1'b0), .out(_4), .gate(H1));
  Transistor #(.\type ("n")) transistor_196 (.in(1'b0), .out(_4), .gate(H0));
  Pull_Resistor #(.pull(1)) pull_resistor_30 (.node(_277_2));
  Transistor #(.\type ("n")) transistor_197 (.in(1'b0), .out(_277_2), .gate(not_1_out));
  Transistor #(.\type ("n")) transistor_198 (.in(1'b0), .out(_277_2), .gate(H7));
  Transistor #(.\type ("n")) transistor_199 (.in(1'b0), .out(_277_2), .gate(H6));
  Transistor #(.\type ("n")) transistor_200 (.in(1'b0), .out(_277_2), .gate(H5));
  Transistor #(.\type ("n")) transistor_201 (.in(1'b0), .out(_277_2), .gate(not_5_out));
  Transistor #(.\type ("n")) transistor_202 (.in(1'b0), .out(_277_2), .gate(H3));
  Transistor #(.\type ("n")) transistor_203 (.in(1'b0), .out(_277_2), .gate(not_7_out));
  Transistor #(.\type ("n")) transistor_204 (.in(1'b0), .out(_277_2), .gate(H1));
  Transistor #(.\type ("n")) transistor_205 (.in(1'b0), .out(_277_2), .gate(not_9_out));
  Pull_Resistor #(.pull(1)) pull_resistor_31 (.node(_302));
  Pull_Resistor #(.pull(1)) pull_resistor_32 (.node(_321));
  Transistor #(.\type ("n")) transistor_206 (.in(1'b0), .out(_321), .gate(not_1_out));
  Transistor #(.\type ("n")) transistor_207 (.in(1'b0), .out(_302), .gate(not_1_out));
  Transistor #(.\type ("n")) transistor_208 (.in(1'b0), .out(_302), .gate(H7));
  Transistor #(.\type ("n")) transistor_209 (.in(1'b0), .out(_321), .gate(H7));
  Transistor #(.\type ("n")) transistor_210 (.in(1'b0), .out(_302), .gate(H6));
  Transistor #(.\type ("n")) transistor_211 (.in(1'b0), .out(_321), .gate(not_3_out));
  Transistor #(.\type ("n")) transistor_212 (.in(1'b0), .out(_321), .gate(H5));
  Transistor #(.\type ("n")) transistor_213 (.in(1'b0), .out(_302), .gate(not_4_out));
  Transistor #(.\type ("n")) transistor_214 (.in(1'b0), .out(_302), .gate(H4));
  Transistor #(.\type ("n")) transistor_215 (.in(1'b0), .out(_321), .gate(H4));
  Transistor #(.\type ("n")) transistor_216 (.in(1'b0), .out(_321), .gate(H3));
  Transistor #(.\type ("n")) transistor_217 (.in(1'b0), .out(_302), .gate(not_6_out));
  Transistor #(.\type ("n")) transistor_218 (.in(1'b0), .out(_321), .gate(H2));
  Transistor #(.\type ("n")) transistor_219 (.in(1'b0), .out(_302), .gate(not_7_out));
  Transistor #(.\type ("n")) transistor_220 (.in(1'b0), .out(_321), .gate(H1));
  Transistor #(.\type ("n")) transistor_221 (.in(1'b0), .out(_302), .gate(not_8_out));
  Transistor #(.\type ("n")) transistor_222 (.in(1'b0), .out(_302), .gate(H0));
  Transistor #(.\type ("n")) transistor_223 (.in(1'b0), .out(_321), .gate(not_9_out));
  Pull_Resistor #(.pull(1)) pull_resistor_33 (.node(_306));
  Transistor #(.\type ("n")) transistor_224 (.in(1'b0), .out(_306), .gate(not_1_out));
  Transistor #(.\type ("n")) transistor_225 (.in(1'b0), .out(_306), .gate(H7));
  Transistor #(.\type ("n")) transistor_226 (.in(1'b0), .out(_306), .gate(H6));
  Transistor #(.\type ("n")) transistor_227 (.in(1'b0), .out(_306), .gate(not_4_out));
  Transistor #(.\type ("n")) transistor_228 (.in(1'b0), .out(_306), .gate(not_5_out));
  Transistor #(.\type ("n")) transistor_229 (.in(1'b0), .out(_306), .gate(H3));
  Transistor #(.\type ("n")) transistor_230 (.in(1'b0), .out(_306), .gate(H2));
  Transistor #(.\type ("n")) transistor_231 (.in(1'b0), .out(_306), .gate(not_8_out));
  Transistor #(.\type ("n")) transistor_232 (.in(1'b0), .out(_306), .gate(H0));
  Pull_Resistor #(.pull(1)) pull_resistor_34 (.node(_340));
  Transistor #(.\type ("n")) transistor_233 (.in(1'b0), .out(_340), .gate(not_1_out));
  Transistor #(.\type ("n")) transistor_234 (.in(1'b0), .out(_340), .gate(H7));
  Transistor #(.\type ("n")) transistor_235 (.in(1'b0), .out(_340), .gate(not_3_out));
  Transistor #(.\type ("n")) transistor_236 (.in(1'b0), .out(_340), .gate(H5));
  Transistor #(.\type ("n")) transistor_237 (.in(1'b0), .out(_340), .gate(not_5_out));
  Transistor #(.\type ("n")) transistor_238 (.in(1'b0), .out(_340), .gate(H3));
  Transistor #(.\type ("n")) transistor_239 (.in(1'b0), .out(_340), .gate(not_7_out));
  Transistor #(.\type ("n")) transistor_240 (.in(1'b0), .out(_340), .gate(H1));
  Transistor #(.\type ("n")) transistor_241 (.in(1'b0), .out(_340), .gate(H0));

  assign Hnn = {H5, H4, H3, H2, H1, H0};
  assign VPOS = {V7, V6, V5, V4, V3, V2, V1, V0};

  // Notes on the sheet:
  //   H8
  //   H7
  //   H6
  //   H5
  //   H4
  //   H3
  //   H2
  //   H1
  //   H0
endmodule

module REGISTER_SELECT (
  input  nDBE,
  input  RC,
  input  RS0,
  input  RS1,
  input  RS2,
  input  R_W,
  output nW6_1,
  output nW6_2,
  output nW5_1,
  output nW5_2,
  output nR7,
  output nW7,
  output nW4,
  output nW3,
  output nR2,
  output nW1,
  output nW0,
  output nR4
);

  wire _3_out, _4_out, _6_out, multiplexer_1_out, multiplexer_2_out, nor_1_out, nor_2_out, nor_3_out,
       nor_4_out, nor_5_out, nor_6_out, nor_7_out, nor_8_out, nor_9_out, nor_10_out, nor_11_out, nor_12_out,
       nor_13_out, nor_14_out, nor_15_out, not_1_out, not_2_out, not_3_out, not_4_out, not_5_out;

  not not_1 (not_1_out, R_W);
  not not_2 (not_2_out, RS2);
  not not_3 (not_3_out, RS0);
  not not_4 (not_4_out, RS1);
  Multiplexer #(.enable("false")) multiplexer_1 (
    .in0(not_5_out), .in1(_3_out), .out(multiplexer_1_out), .sel(nor_14_out));
  Multiplexer #(.enable("false")) multiplexer_2 (
    .in0(not_5_out), .in1(_6_out), .out(multiplexer_2_out), .sel(nor_14_out));
  nor nor_1 (nor_1_out, R_W, RS0, not_4_out, not_2_out, _6_out);
  nor nor_2 (nor_2_out, R_W, RS0, not_4_out, not_2_out, _3_out);
  nor nor_3 (nor_3_out, R_W, _6_out, RS0, not_4_out, RS2);
  nor nor_4 (nor_4_out, R_W, RS0, not_4_out, RS2, _3_out);
  nor nor_5 (nor_5_out, not_1_out, not_3_out, not_4_out, not_2_out);
  nor nor_6 (nor_6_out, R_W, not_3_out, not_4_out, not_2_out);
  nor nor_7 (nor_7_out, R_W, RS0, RS1, not_2_out);
  nor nor_8 (nor_8_out, R_W, not_3_out, not_4_out, RS2);
  nor nor_9 (nor_9_out, not_1_out, RS0, not_3_out, RS2);
  nor nor_10 (nor_10_out, R_W, not_3_out, RS1, RS2);
  nor nor_11 (nor_11_out, R_W, RS0, RS1, RS2);
  nor nor_12 (nor_12_out, not_1_out, RS0, RS1, not_2_out);
  not not_5 (not_5_out, _4_out);
  nor _4 (_4_out, RC, nor_13_out, multiplexer_1_out);
  nor _3 (_3_out, nor_13_out, RC, multiplexer_2_out);
  not _6 (_6_out, _3_out);
  nor nor_13 (nor_13_out, nDBE, nR2);
  nor nor_14 (nor_14_out, nDBE, nor_15_out);
  nor nor_15 (nor_15_out, nor_1_out, nor_2_out, nor_3_out, nor_4_out);
  not not_6 (nW6_1, nor_1_out);
  not not_7 (nW6_2, nor_2_out);
  not not_8 (nW5_1, nor_3_out);
  not not_9 (nW5_2, nor_4_out);
  not not_10 (nR7, nor_5_out);
  not not_11 (nW7, nor_6_out);
  not not_12 (nW4, nor_7_out);
  not not_13 (nW3, nor_8_out);
  not not_14 (nR2, nor_9_out);
  not not_15 (nW1, nor_10_out);
  not not_16 (nW0, nor_11_out);
  not not_17 (nR4, nor_12_out);

  // Notes on the sheet:
  //   2ND
  //   1ST
  //   1
  //   2
  //   5
  //   $2005/$2006 first/second write latch
  //   R2
  //   W5/6
endmodule

module VIDEO_OUT_NTSC (
  input  nCLK,
  input  RES,
  input  nTR,
  input  nTG,
  input  nTB,
  input  PCLK,
  input  nCC0,
  input  nCC1,
  input  nCC2,
  input  nCC3,
  input  PICTURE,
  input  SYNC,
  input  BURST,
  input  nLL0,
  input  nLL1,
  output [10:0] out_16
);

  wire _1_out, _2_out, _3_out, _4_out, _5_out, _6_out, _7_out, _8_out, _9_out, _10_out, _11_out, _12_out,
       _13_out, d_latch_1_not_q, d_latch_2_not_q, d_latch_3_not_q, d_latch_4_not_q, d_latch_5_not_q,
       d_latch_6_not_q, d_latch_7_not_q, d_latch_8_q, d_latch_9_q, d_latch_10_not_q, d_latch_11_not_q,
       d_latch_12_not_q, d_latch_13_not_q, d_latch_14_q, d_latch_15_q, d_latch_16_q, d_latch_17_not_q,
       d_latch_18_q, d_latch_19_not_q, d_latch_20_q, d_latch_21_not_q, d_latch_22_q, d_latch_23_not_q,
       d_latch_24_q, d_latch_25_not_q, nor_1_out, nor_2_out, nor_3_out, nor_4_out, nor_5_out, nor_6_out,
       nor_7_out, nor_8_out, nor_9_out, nor_10_out, nor_11_out, nor_12_out, nor_13_out, nor_14_out,
       nor_15_out, nor_16_out, nor_17_out, nor_18_out, nor_19_out, nor_20_out, nor_21_out, nor_22_out,
       nor_23_out, nor_24_out, nor_25_out, nor_26_out, nor_27_out, nor_28_out, nor_29_out, nor_30_out,
       not_1_out, not_2_out, not_3_out, not_4_out, not_5_out, not_6_out, not_7_out, not_8_out, not_9_out,
       not_10_out, not_12_out, not_14_out, not_15_out, not_16_out, not_17_out, not_20_out, not_23_out,
       not_26_out, not_27_out, or_1_out;

  not not_1 (not_1_out, PCLK);
  D_latch d_latch_1 (.EN(PCLK), .D(nCC0), .NOT_Q(d_latch_1_not_q));  // open: Q
  D_latch d_latch_2 (.EN(PCLK), .D(nCC1), .NOT_Q(d_latch_2_not_q));  // open: Q
  D_latch d_latch_3 (.EN(PCLK), .D(nCC2), .NOT_Q(d_latch_3_not_q));  // open: Q
  D_latch d_latch_4 (.EN(PCLK), .D(nCC3), .NOT_Q(d_latch_4_not_q));  // open: Q
  or or_1 (or_1_out, SYNC, BURST, nor_6_out);
  not not_2 (not_2_out, SYNC);
  nor nor_1 (nor_1_out, nor_12_out, nTR, d_latch_11_not_q);
  nor nor_2 (nor_2_out, d_latch_11_not_q, nTG, nor_27_out);
  nor nor_3 (nor_3_out, d_latch_11_not_q, nTB, nor_21_out);
  D_latch d_latch_5 (.EN(not_1_out), .D(d_latch_1_not_q), .NOT_Q(d_latch_5_not_q));  // open: Q
  D_latch d_latch_6 (.EN(not_1_out), .D(d_latch_2_not_q), .NOT_Q(d_latch_6_not_q));  // open: Q
  D_latch d_latch_7 (.EN(not_1_out), .D(d_latch_3_not_q), .NOT_Q(d_latch_7_not_q));  // open: Q
  D_latch d_latch_8 (.EN(not_1_out), .D(d_latch_4_not_q), .Q(d_latch_8_q));  // open: NOT_Q
  D_latch d_latch_9 (.EN(not_1_out), .D(or_1_out), .Q(d_latch_9_q));  // open: NOT_Q
  D_latch d_latch_10 (.EN(not_1_out), .D(or_1_out), .NOT_Q(d_latch_10_not_q));  // open: Q
  D_latch d_latch_11 (.EN(not_1_out), .D(nor_6_out), .NOT_Q(d_latch_11_not_q));  // open: Q
  D_latch d_latch_12 (.EN(not_1_out), .D(not_2_out), .NOT_Q(d_latch_12_not_q));  // open: Q
  D_latch d_latch_13 (.EN(not_1_out), .D(BURST), .NOT_Q(d_latch_13_not_q));  // open: Q
  nor nor_4 (nor_4_out, nor_1_out, nor_2_out, nor_3_out);
  nor nor_5 (nor_5_out, d_latch_8_q, d_latch_9_q);
  nor nor_6 (nor_6_out, PICTURE, nor_7_out);
  not not_3 (not_3_out, nLL0);
  not not_4 (not_4_out, nor_4_out);
  nor nor_7 (nor_7_out, nor_5_out, d_latch_7_not_q, d_latch_6_not_q);
  not not_5 (not_5_out, nLL1);
  not not_6 (not_6_out, nCLK);
  nor nor_8 (nor_8_out, d_latch_11_not_q, not_3_out, not_5_out);
  nor nor_9 (nor_9_out, d_latch_11_not_q, nLL0, nLL1);
  nor nor_10 (nor_10_out, d_latch_11_not_q, nLL0, not_5_out);
  nor nor_11 (nor_11_out, d_latch_11_not_q, not_3_out, nLL1);
  D_latch d_latch_14 (.EN(not_6_out), .D(not_20_out), .Q(d_latch_14_q));  // open: NOT_Q
  not not_7 (not_7_out, d_latch_5_not_q);
  not not_8 (not_8_out, d_latch_6_not_q);
  not not_9 (not_9_out, d_latch_7_not_q);
  not not_10 (not_10_out, nor_5_out);
  not not_11 (out_16[0], not_4_out);
  not not_12 (not_12_out, d_latch_10_not_q);
  not not_13 (out_16[10], d_latch_12_not_q);
  not not_14 (not_14_out, nor_8_out);
  not not_15 (not_15_out, nor_9_out);
  not not_16 (not_16_out, nor_10_out);
  not not_17 (not_17_out, nor_11_out);
  nor nor_12 (nor_12_out, d_latch_14_q, RES);
  nor _1 (_1_out, not_7_out, not_8_out, d_latch_7_not_q, nor_5_out, nor_12_out);
  D_latch d_latch_15 (.EN(nCLK), .D(nor_12_out), .Q(d_latch_15_q));  // open: NOT_Q
  nor nor_13 (nor_13_out, not_20_out, d_latch_17_not_q);
  nor _2 (_2_out, d_latch_5_not_q, not_8_out, d_latch_7_not_q, not_10_out, nor_14_out);
  nor nor_14 (nor_14_out, d_latch_15_q, nor_13_out);
  nor _3 (_3_out, not_7_out, d_latch_6_not_q, not_9_out, nor_5_out, d_latch_17_not_q);
  nor _4 (_4_out, d_latch_5_not_q, d_latch_6_not_q, not_9_out, not_10_out, nor_17_out);
  nor nor_15 (nor_15_out, nor_18_out, d_latch_13_not_q);
  not not_18 (out_16[6], nor_15_out);
  not not_19 (out_16[9], nor_16_out);
  nor nor_16 (nor_16_out, nor_15_out, d_latch_13_not_q);
  D_latch d_latch_16 (.EN(not_6_out), .D(nor_14_out), .Q(d_latch_16_q));  // open: NOT_Q
  nor nor_17 (nor_17_out, d_latch_16_q, RES);
  nor _5 (_5_out, not_7_out, not_8_out, not_9_out, nor_5_out, nor_21_out);
  or or_2 (out_16[7], not_12_out, not_26_out);
  D_latch d_latch_17 (.EN(nCLK), .D(nor_17_out), .NOT_Q(d_latch_17_not_q));  // open: Q
  not not_20 (not_20_out, d_latch_19_not_q);
  nor _6 (_6_out, d_latch_5_not_q, not_8_out, not_9_out, not_10_out, d_latch_19_not_q);
  D_latch d_latch_18 (.EN(not_6_out), .D(d_latch_17_not_q), .Q(d_latch_18_q));  // open: NOT_Q
  nor _7 (_7_out, not_7_out, not_8_out, not_9_out, not_10_out);
  nor nor_18 (nor_18_out, _1_out, _2_out, _3_out, _4_out, _5_out, _6_out, _7_out, _8_out, _9_out, _10_out, _11_out, _12_out, _13_out);
  nor nor_19 (nor_19_out, nor_18_out, not_14_out);
  not not_21 (out_16[4], nor_19_out);
  not not_22 (out_16[8], nor_20_out);
  nor nor_20 (nor_20_out, nor_19_out, not_14_out);
  nor nor_21 (nor_21_out, d_latch_18_q, RES);
  nor _8 (_8_out, not_7_out, d_latch_6_not_q, d_latch_7_not_q, not_10_out, nor_27_out);
  D_latch d_latch_19 (.EN(nCLK), .D(nor_21_out), .NOT_Q(d_latch_19_not_q));  // open: Q
  nor _9 (_9_out, d_latch_5_not_q, d_latch_6_not_q, not_9_out, nor_5_out, nor_24_out);
  nor nor_22 (nor_22_out, nor_18_out, not_15_out);
  nor nor_23 (nor_23_out, nor_22_out, not_15_out);
  D_latch d_latch_20 (.EN(not_6_out), .D(d_latch_19_not_q), .Q(d_latch_20_q));  // open: NOT_Q
  nor nor_24 (nor_24_out, d_latch_20_q, RES);
  nor _10 (_10_out, not_7_out, not_8_out, d_latch_7_not_q, not_10_out, d_latch_21_not_q);
  not not_23 (not_23_out, nor_22_out);
  not not_24 (out_16[2], nor_23_out);
  or or_3 (out_16[1], not_23_out, not_27_out);
  D_latch d_latch_21 (.EN(nCLK), .D(nor_24_out), .NOT_Q(d_latch_21_not_q));  // open: Q
  nor _12 (_12_out, not_7_out, d_latch_6_not_q, not_9_out, not_10_out, nor_30_out);
  nor _11 (_11_out, d_latch_5_not_q, not_8_out, not_9_out, nor_5_out, d_latch_23_not_q);
  D_latch d_latch_22 (.EN(not_6_out), .D(d_latch_21_not_q), .Q(d_latch_22_q));  // open: NOT_Q
  nor _13 (_13_out, d_latch_5_not_q, d_latch_6_not_q, d_latch_7_not_q, not_10_out, d_latch_25_not_q);
  nor nor_25 (nor_25_out, nor_18_out, not_16_out);
  not not_25 (out_16[3], nor_25_out);
  not not_26 (not_26_out, nor_26_out);
  nor nor_26 (nor_26_out, nor_25_out, not_16_out);
  nor nor_27 (nor_27_out, d_latch_22_q, RES);
  D_latch d_latch_23 (.EN(nCLK), .D(nor_27_out), .NOT_Q(d_latch_23_not_q));  // open: Q
  nor nor_28 (nor_28_out, nor_18_out, not_17_out);
  nor nor_29 (nor_29_out, nor_28_out, not_17_out);
  D_latch d_latch_24 (.EN(not_6_out), .D(d_latch_23_not_q), .Q(d_latch_24_q));  // open: NOT_Q
  nor nor_30 (nor_30_out, d_latch_24_q, RES);
  not not_27 (not_27_out, nor_28_out);
  not not_28 (out_16[5], nor_29_out);
  D_latch d_latch_25 (.EN(nCLK), .D(nor_30_out), .NOT_Q(d_latch_25_not_q));  // open: Q

  // Notes on the sheet:
  //   Emphasis
  //   TINT
  //   P123
  //   /POUT
  //   /PR
  //   /PB
  //   /PG
  //   0
  //   1
  //   2
  //   3
  //   Color 1D (black)
  //   Synch
  //   /POUT
  //   TINT
  //   Color burst
  //   /LU3
  //   /LU0
  //   /LU2
  //   /LU1
  //   NTSC
  //   /PZ
endmodule

module VIDEO_OUT_PAL (
  input  nCLK,
  input  RES,
  input  nTR,
  input  nTG,
  input  nTB,
  input  V0,
  input  PCLK,
  input  nCC0,
  input  nCC1,
  input  nCC2,
  input  nCC3,
  input  PICTURE,
  input  SYNC,
  input  BURST,
  input  nLL0,
  input  nLL1,
  output [10:0] out_17
);

  wire _1_out, _2_out, _3_out, _4_out, _5_out, _6_out, _7_out, _8_out, _9_out, _10_out, _11_out, _12_out,
       _13_out, _14_out, _15_out, _16_2_out, _16_out, _17_out, _18_out, _19_out, _20_out, _21_out, _22_out,
       _23_out, _24_2_out, _24_out, _25_out, _31_out, _32_out, _33_out, _34_out, _42_out, _44_out,
       d_latch_1_not_q, d_latch_2_not_q, d_latch_3_not_q, d_latch_4_not_q, d_latch_5_not_q, d_latch_6_not_q,
       d_latch_7_not_q, d_latch_8_not_q, d_latch_9_not_q, d_latch_10_q, d_latch_11_q, d_latch_12_q,
       d_latch_13_not_q, d_latch_14_not_q, d_latch_15_not_q, d_latch_16_not_q, d_latch_17_q, d_latch_18_q,
       d_latch_19_q, d_latch_20_not_q, d_latch_21_q, d_latch_22_not_q, d_latch_23_q, d_latch_24_not_q,
       d_latch_25_q, d_latch_26_not_q, d_latch_27_q, d_latch_28_not_q, multiplexer_1_out, multiplexer_2_out,
       nor_1_out, nor_2_out, nor_3_out, nor_4_out, nor_5_out, nor_6_out, nor_7_out, nor_8_out, nor_9_out,
       nor_10_out, nor_11_out, nor_12_out, nor_13_out, nor_14_out, nor_15_out, nor_16_out, nor_17_out,
       nor_18_out, nor_19_out, nor_20_out, nor_21_out, nor_22_out, nor_23_out, not_1_out, not_2_out,
       not_3_out, not_4_out, not_5_out, not_6_out, not_7_out, not_8_out, not_9_out, not_10_out, not_11_out,
       not_12_out, not_13_out, not_14_out, not_15_out, not_16_out, not_17_out, not_18_out, not_20_out,
       not_26_out, not_27_out, not_30_out, not_31_out;

  not not_1 (not_1_out, PICTURE);
  not not_2 (not_2_out, PCLK);
  D_latch d_latch_1 (.EN(PCLK), .D(nCC0), .NOT_Q(d_latch_1_not_q));  // open: Q
  D_latch d_latch_2 (.EN(PCLK), .D(nCC1), .NOT_Q(d_latch_2_not_q));  // open: Q
  D_latch d_latch_3 (.EN(PCLK), .D(nCC2), .NOT_Q(d_latch_3_not_q));  // open: Q
  D_latch d_latch_4 (.EN(PCLK), .D(nCC3), .NOT_Q(d_latch_4_not_q));  // open: Q
  D_latch d_latch_5 (.EN(not_2_out), .D(not_1_out), .NOT_Q(d_latch_5_not_q));  // open: Q
  or _42 (_42_out, _44_out, SYNC, BURST);
  not not_3 (not_3_out, SYNC);
  nor _31 (_31_out, not_6_out, nTR, d_latch_13_not_q);
  nor _32 (_32_out, d_latch_13_not_q, nTG, not_7_out);
  nor _33 (_33_out, d_latch_13_not_q, nTB, nor_15_out);
  D_latch d_latch_6 (.EN(not_2_out), .D(V0), .NOT_Q(d_latch_6_not_q));  // open: Q
  D_latch d_latch_7 (.EN(not_2_out), .D(d_latch_1_not_q), .NOT_Q(d_latch_7_not_q));  // open: Q
  D_latch d_latch_8 (.EN(not_2_out), .D(d_latch_2_not_q), .NOT_Q(d_latch_8_not_q));  // open: Q
  D_latch d_latch_9 (.EN(not_2_out), .D(d_latch_3_not_q), .NOT_Q(d_latch_9_not_q));  // open: Q
  D_latch d_latch_10 (.EN(not_2_out), .D(d_latch_4_not_q), .Q(d_latch_10_q));  // open: NOT_Q
  D_latch d_latch_11 (.EN(PCLK), .D(d_latch_5_not_q), .Q(d_latch_11_q));  // open: NOT_Q
  D_latch d_latch_12 (.EN(not_2_out), .D(_42_out), .Q(d_latch_12_q));  // open: NOT_Q
  D_latch d_latch_13 (.EN(not_2_out), .D(_44_out), .NOT_Q(d_latch_13_not_q));  // open: Q
  D_latch d_latch_14 (.EN(not_2_out), .D(_42_out), .NOT_Q(d_latch_14_not_q));  // open: Q
  D_latch d_latch_15 (.EN(not_2_out), .D(not_3_out), .NOT_Q(d_latch_15_not_q));  // open: Q
  D_latch d_latch_16 (.EN(not_2_out), .D(BURST), .NOT_Q(d_latch_16_not_q));  // open: Q
  not not_4 (not_4_out, _34_out);
  nor _34 (_34_out, _31_out, _32_out, _33_out);
  nor nor_1 (nor_1_out, d_latch_10_q, d_latch_12_q);
  nor _44 (_44_out, d_latch_11_q, _24_out);
  not not_5 (not_5_out, nLL0);
  not not_6 (not_6_out, multiplexer_1_out);
  not not_7 (not_7_out, multiplexer_2_out);
  nor _24 (_24_out, nor_1_out, d_latch_9_not_q, d_latch_8_not_q);
  not not_8 (not_8_out, nLL1);
  Multiplexer #(.enable("false")) multiplexer_1 (
    .in0(nor_18_out), .in1(nor_10_out), .out(multiplexer_1_out), .sel(d_latch_6_not_q));
  Multiplexer #(.enable("false")) multiplexer_2 (
    .in0(nor_10_out), .in1(nor_18_out), .out(multiplexer_2_out), .sel(d_latch_6_not_q));
  nor nor_2 (nor_2_out, d_latch_13_not_q, not_5_out, not_8_out);
  nor nor_3 (nor_3_out, d_latch_13_not_q, nLL0, nLL1);
  nor nor_4 (nor_4_out, d_latch_13_not_q, nLL0, not_8_out);
  nor nor_5 (nor_5_out, d_latch_13_not_q, not_5_out, nLL1);
  not not_9 (not_9_out, d_latch_6_not_q);
  not not_10 (not_10_out, d_latch_7_not_q);
  not not_11 (not_11_out, d_latch_8_not_q);
  not not_12 (not_12_out, d_latch_9_not_q);
  not not_13 (not_13_out, nor_1_out);
  nor _1 (_1_out, d_latch_6_not_q, d_latch_7_not_q, not_11_out, d_latch_9_not_q, not_13_out, nor_6_out);
  not not_14 (not_14_out, nor_2_out);
  not not_15 (not_15_out, nor_3_out);
  not not_16 (not_16_out, nor_4_out);
  not not_17 (not_17_out, nor_5_out);
  not not_18 (not_18_out, nCLK);
  nor _2 (_2_out, not_9_out, not_10_out, not_11_out, d_latch_9_not_q, nor_1_out, nor_6_out);
  D_latch d_latch_17 (.EN(not_18_out), .D(not_26_out), .Q(d_latch_17_q));  // open: NOT_Q
  not not_19 (out_17[0], not_4_out);
  not not_20 (not_20_out, d_latch_14_not_q);
  not not_21 (out_17[10], d_latch_15_not_q);
  nor nor_6 (nor_6_out, RES, d_latch_17_q);
  nor _3 (_3_out, d_latch_6_not_q, not_10_out, not_11_out, d_latch_9_not_q, nor_1_out, nor_9_out);
  nor nor_7 (nor_7_out, nor_19_out, d_latch_16_not_q);
  nor nor_8 (nor_8_out, nor_7_out, d_latch_16_not_q);
  D_latch d_latch_18 (.EN(nCLK), .D(nor_6_out), .Q(d_latch_18_q));  // open: NOT_Q
  nor _16 (_16_out, not_26_out, d_latch_20_not_q);
  nor _4 (_4_out, not_9_out, d_latch_7_not_q, not_11_out, d_latch_9_not_q, not_13_out, nor_9_out);
  not not_22 (out_17[6], nor_7_out);
  not not_23 (out_17[9], nor_8_out);
  nor nor_9 (nor_9_out, d_latch_18_q, _16_out);
  nor _5 (_5_out, d_latch_6_not_q, d_latch_7_not_q, d_latch_8_not_q, d_latch_9_not_q, not_13_out, nor_10_out);
  or or_1 (out_17[7], not_20_out, not_30_out);
  D_latch d_latch_19 (.EN(not_18_out), .D(nor_9_out), .Q(d_latch_19_q));  // open: NOT_Q
  nor _6 (_6_out, not_9_out, not_10_out, d_latch_8_not_q, not_12_out, nor_1_out, nor_10_out);
  nor nor_10 (nor_10_out, RES, d_latch_19_q);
  nor _7 (_7_out, d_latch_6_not_q, not_10_out, d_latch_8_not_q, not_12_out, not_13_out, d_latch_20_not_q);
  not not_24 (out_17[4], nor_11_out);
  nor nor_11 (nor_11_out, nor_19_out, not_14_out);
  not not_25 (out_17[8], nor_12_out);
  nor nor_12 (nor_12_out, nor_11_out, not_14_out);
  D_latch d_latch_20 (.EN(nCLK), .D(nor_10_out), .NOT_Q(d_latch_20_not_q));  // open: Q
  nor _8 (_8_out, not_9_out, d_latch_7_not_q, d_latch_8_not_q, not_12_out, not_13_out, d_latch_20_not_q);
  D_latch d_latch_21 (.EN(not_18_out), .D(d_latch_20_not_q), .Q(d_latch_21_q));  // open: NOT_Q
  nor _9 (_9_out, d_latch_6_not_q, d_latch_7_not_q, not_11_out, not_12_out, nor_1_out, nor_15_out);
  nor nor_13 (nor_13_out, nor_19_out, not_15_out);
  nor nor_14 (nor_14_out, nor_13_out, not_15_out);
  nor nor_15 (nor_15_out, RES, d_latch_21_q);
  not not_26 (not_26_out, d_latch_22_not_q);
  nor _10 (_10_out, not_9_out, not_10_out, not_11_out, not_12_out, nor_1_out, nor_15_out);
  not not_27 (not_27_out, nor_13_out);
  not not_28 (out_17[2], nor_14_out);
  or or_2 (out_17[1], not_27_out, not_31_out);
  D_latch d_latch_22 (.EN(nCLK), .D(nor_15_out), .NOT_Q(d_latch_22_not_q));  // open: Q
  D_latch d_latch_23 (.EN(not_18_out), .D(d_latch_22_not_q), .Q(d_latch_23_q));  // open: NOT_Q
  nor _11 (_11_out, not_10_out, not_11_out, not_12_out, not_13_out);
  nor nor_16 (nor_16_out, nor_19_out, not_16_out);
  nor nor_17 (nor_17_out, nor_16_out, not_16_out);
  nor nor_18 (nor_18_out, RES, d_latch_23_q);
  nor _12 (_12_out, d_latch_6_not_q, not_10_out, not_11_out, d_latch_9_not_q, not_13_out, d_latch_22_not_q);
  not not_29 (out_17[3], nor_16_out);
  not not_30 (not_30_out, nor_17_out);
  D_latch d_latch_24 (.EN(nCLK), .D(nor_18_out), .NOT_Q(d_latch_24_not_q));  // open: Q
  nor _13 (_13_out, not_9_out, d_latch_7_not_q, not_11_out, not_12_out, not_13_out, d_latch_22_not_q);
  nor nor_19 (nor_19_out, _1_out, _2_out, _3_out, _4_out, _5_out, _6_out, _7_out, _8_out, _9_out, _10_out, _11_out, _12_out, _13_out, _14_out, _15_out, _16_2_out, _17_out, _18_out, _19_out, _20_out, _21_out, _22_out, _23_out, _24_2_out, _25_out);
  nor nor_20 (nor_20_out, nor_19_out, not_17_out);
  nor nor_21 (nor_21_out, nor_20_out, not_17_out);
  D_latch d_latch_25 (.EN(not_18_out), .D(d_latch_24_not_q), .Q(d_latch_25_q));  // open: NOT_Q
  nor _14 (_14_out, d_latch_6_not_q, d_latch_7_not_q, d_latch_8_not_q, not_12_out, nor_1_out, nor_18_out);
  not not_31 (not_31_out, nor_20_out);
  not not_32 (out_17[5], nor_21_out);
  D_latch d_latch_26 (.EN(nCLK), .D(nor_22_out), .NOT_Q(d_latch_26_not_q));  // open: Q
  nor nor_22 (nor_22_out, RES, d_latch_25_q);
  nor _15 (_15_out, not_9_out, not_10_out, d_latch_8_not_q, d_latch_9_not_q, not_13_out, nor_18_out);
  D_latch d_latch_27 (.EN(not_18_out), .D(d_latch_26_not_q), .Q(d_latch_27_q));  // open: NOT_Q
  nor _16_2 (_16_2_out, d_latch_6_not_q, not_10_out, d_latch_8_not_q, d_latch_9_not_q, not_13_out, d_latch_24_not_q);
  nor nor_23 (nor_23_out, RES, d_latch_27_q);
  nor _17 (_17_out, not_9_out, d_latch_7_not_q, d_latch_8_not_q, not_12_out, nor_1_out, d_latch_24_not_q);
  D_latch d_latch_28 (.EN(nCLK), .D(nor_23_out), .NOT_Q(d_latch_28_not_q));  // open: Q
  nor _18 (_18_out, d_latch_6_not_q, d_latch_7_not_q, not_11_out, not_12_out, not_13_out, nor_22_out);
  nor _19 (_19_out, not_9_out, not_10_out, not_11_out, d_latch_9_not_q, not_13_out, nor_22_out);
  nor _20 (_20_out, d_latch_6_not_q, not_10_out, not_11_out, not_12_out, nor_1_out, d_latch_26_not_q);
  nor _21 (_21_out, not_9_out, d_latch_7_not_q, not_11_out, not_12_out, nor_1_out, d_latch_26_not_q);
  nor _22 (_22_out, d_latch_6_not_q, d_latch_7_not_q, d_latch_8_not_q, not_12_out, not_13_out, nor_23_out);
  nor _23 (_23_out, not_9_out, not_10_out, d_latch_8_not_q, not_12_out, not_13_out, nor_23_out);
  nor _24_2 (_24_2_out, d_latch_6_not_q, not_10_out, d_latch_8_not_q, not_12_out, nor_1_out, d_latch_28_not_q);
  nor _25 (_25_out, not_9_out, d_latch_7_not_q, d_latch_8_not_q, d_latch_9_not_q, not_13_out, d_latch_28_not_q);

  // Notes on the sheet:
  //   Emphasis
  //   50
  //   !
  //   51
  //   !
  //   41
  //   52
  //   !
  //   45
  //   47
  //   46
  //   48
  //   /PR
  //   /PG
  //   35
  //   /POUT
  //   14
  //   13
  //   TINT
  //   /PB
  //   /POUT
  //   P123
  //   /V0'
  //   0
  //   1
  //   2
  //   3
  //   /POUT
  //   /LU3
  //   /LU0
  //   /LU2
  //   /LU1
  //   49
  //   TINT
  //   Color 1D (black)
  //   Synch
  //   Color burst
  //   1
  //   /PZ
  //   2
  //   3
  //   4
  //   5
  //   PAL
  //   6
  //   15
  //   7
  //   /V0
  //   0
  //   1
  //   2
  //   3
  //   8
  //   9
  //   /PZ
  //   10
  //   11
  //   12
  //   /V0
  //   0
  //   1
  //   2
  //   3
endmodule
module VIDEO_OUT_RGB (
  input  PCLK,
  input  PICTURE,
  input  nTR,
  input  nTG,
  input  nTB,
  input  nCC0,
  input  nCC1,
  input  nCC2,
  input  nCC3,
  input  nLL0,
  input  nLL1,
  input  SYNC,
  output R0,
  output R1,
  output R2,
  output R3,
  output R4,
  output R5,
  output R6,
  output R7,
  output G0,
  output G1,
  output G2,
  output G3,
  output G4,
  output G5,
  output G6,
  output G7,
  output B0,
  output B1,
  output B2,
  output B3,
  output B4,
  output B5,
  output B6,
  output B7,
  output SYNC_2
);

  wire and_1_out, and_2_out, and_3_out, and_4_out, and_5_out, and_6_out, and_7_out, and_8_out, and_9_out,
       d_latch_1_not_q, d_latch_2_not_q, d_latch_3_not_q, d_latch_4_not_q, d_latch_5_not_q, d_latch_6_not_q,
       d_latch_7_not_q, nor_1_out, nor_2_out, nor_3_out, nor_4_out, nor_5_out, nor_6_out, nor_7_out,
       nor_8_out, nor_9_out, nor_10_out, nor_11_out, nor_12_out, nor_13_out, nor_14_out, nor_15_out,
       nor_16_out, nor_17_out, nor_18_out, nor_19_out, nor_20_out, nor_21_out, nor_22_out, nor_23_out,
       nor_24_out, nor_25_out, nor_26_out, not_1_out, not_2_out, not_3_out, not_4_out, not_5_out, not_6_out,
       not_7_out, not_8_out, not_9_out, not_10_out, undriven, undriven_2, undriven_3, undriven_4, undriven_5,
       undriven_6, undriven_7, undriven_8, undriven_9;

  D_latch d_latch_1 (.EN(not_1_out), .D(SYNC), .NOT_Q(d_latch_1_not_q));  // open: Q
  not not_1 (not_1_out, PCLK);
  D_latch d_latch_2 (.EN(PCLK), .D(d_latch_1_not_q), .NOT_Q(d_latch_2_not_q));  // open: Q
  D_latch d_latch_3 (.EN(not_1_out), .D(nCC0), .NOT_Q(d_latch_3_not_q));  // open: Q
  D_latch d_latch_4 (.EN(not_1_out), .D(nCC1), .NOT_Q(d_latch_4_not_q));  // open: Q
  D_latch d_latch_5 (.EN(not_1_out), .D(nCC2), .NOT_Q(d_latch_5_not_q));  // open: Q
  D_latch d_latch_6 (.EN(not_1_out), .D(nCC3), .NOT_Q(d_latch_6_not_q));  // open: Q
  D_latch d_latch_7 (.EN(not_1_out), .D(d_latch_2_not_q), .NOT_Q(d_latch_7_not_q));  // open: Q
  nor nor_1 (nor_1_out, not_1_out, d_latch_3_not_q);
  nor nor_2 (nor_2_out, not_1_out, d_latch_4_not_q);
  and and_1 (and_1_out, ~PICTURE, undriven);  // AND_Gate
  and and_2 (and_2_out, ~PICTURE, undriven_2);  // AND_Gate
  and and_3 (and_3_out, ~PICTURE, undriven_3);  // AND_Gate
  and and_4 (and_4_out, ~PICTURE, undriven_4);  // AND_Gate
  and and_5 (and_5_out, ~PICTURE, undriven_5);  // AND_Gate
  and and_6 (and_6_out, ~PICTURE, undriven_6);  // AND_Gate
  and and_7 (and_7_out, ~PICTURE, undriven_7);  // AND_Gate
  and and_8 (and_8_out, ~PICTURE, undriven_8);  // AND_Gate
  and and_9 (and_9_out, ~PICTURE, undriven_9);  // AND_Gate
  not not_2 (not_2_out, and_3_out);
  not not_3 (not_3_out, and_2_out);
  not not_4 (not_4_out, and_5_out);
  not not_5 (not_5_out, and_6_out);
  not not_6 (not_6_out, and_9_out);
  not not_7 (not_7_out, and_8_out);
  not not_8 (not_8_out, and_1_out);
  not not_9 (not_9_out, and_4_out);
  not not_10 (not_10_out, and_7_out);
  nor nor_3 (nor_3_out, and_1_out, and_2_out, and_3_out);
  nor nor_4 (nor_4_out, not_8_out, and_2_out, and_3_out);
  nor nor_5 (nor_5_out, and_1_out, not_3_out, and_3_out);
  nor nor_6 (nor_6_out, not_8_out, not_3_out, and_3_out);
  nor nor_7 (nor_7_out, and_1_out, and_2_out, not_2_out);
  nor nor_8 (nor_8_out, not_8_out, and_2_out, not_2_out);
  nor nor_9 (nor_9_out, and_1_out, not_3_out, not_2_out);
  nor nor_10 (nor_10_out, not_8_out, not_3_out, not_2_out);
  nor nor_11 (nor_11_out, and_4_out, and_5_out, and_6_out);
  nor nor_12 (nor_12_out, not_9_out, and_5_out, and_6_out);
  nor nor_13 (nor_13_out, and_4_out, not_4_out, and_6_out);
  nor nor_14 (nor_14_out, not_9_out, not_4_out, and_6_out);
  nor nor_15 (nor_15_out, and_4_out, and_5_out, not_5_out);
  nor nor_16 (nor_16_out, not_9_out, and_5_out, not_5_out);
  nor nor_17 (nor_17_out, and_4_out, not_4_out, not_5_out);
  nor nor_18 (nor_18_out, not_9_out, not_4_out, not_5_out);
  nor nor_19 (nor_19_out, and_7_out, and_8_out, and_9_out);
  nor nor_20 (nor_20_out, not_10_out, and_8_out, and_9_out);
  nor nor_21 (nor_21_out, and_7_out, not_7_out, and_9_out);
  nor nor_22 (nor_22_out, not_10_out, not_7_out, and_9_out);
  nor nor_23 (nor_23_out, and_7_out, and_8_out, not_6_out);
  nor nor_24 (nor_24_out, not_10_out, and_8_out, not_6_out);
  nor nor_25 (nor_25_out, and_7_out, not_7_out, not_6_out);
  nor nor_26 (nor_26_out, not_10_out, not_7_out, not_6_out);
  D_latch d_latch_8 (.EN(not_1_out), .D(nor_3_out), .Q(R0));  // open: NOT_Q
  D_latch d_latch_9 (.EN(not_1_out), .D(nor_4_out), .Q(R1));  // open: NOT_Q
  D_latch d_latch_10 (.EN(not_1_out), .D(nor_5_out), .Q(R2));  // open: NOT_Q
  D_latch d_latch_11 (.EN(not_1_out), .D(nor_6_out), .Q(R3));  // open: NOT_Q
  D_latch d_latch_12 (.EN(not_1_out), .D(nor_7_out), .Q(R4));  // open: NOT_Q
  D_latch d_latch_13 (.EN(not_1_out), .D(nor_8_out), .Q(R5));  // open: NOT_Q
  D_latch d_latch_14 (.EN(not_1_out), .D(nor_9_out), .Q(R6));  // open: NOT_Q
  D_latch d_latch_15 (.EN(not_1_out), .D(nor_10_out), .Q(R7));  // open: NOT_Q
  D_latch d_latch_16 (.EN(not_1_out), .D(nor_11_out), .Q(G0));  // open: NOT_Q
  D_latch d_latch_17 (.EN(not_1_out), .D(nor_12_out), .Q(G1));  // open: NOT_Q
  D_latch d_latch_18 (.EN(not_1_out), .D(nor_13_out), .Q(G2));  // open: NOT_Q
  D_latch d_latch_19 (.EN(not_1_out), .D(nor_14_out), .Q(G3));  // open: NOT_Q
  D_latch d_latch_20 (.EN(not_1_out), .D(nor_15_out), .Q(G4));  // open: NOT_Q
  D_latch d_latch_21 (.EN(not_1_out), .D(nor_16_out), .Q(G5));  // open: NOT_Q
  D_latch d_latch_22 (.EN(not_1_out), .D(nor_17_out), .Q(G6));  // open: NOT_Q
  D_latch d_latch_23 (.EN(not_1_out), .D(nor_18_out), .Q(G7));  // open: NOT_Q
  D_latch d_latch_24 (.EN(not_1_out), .D(nor_19_out), .Q(B0));  // open: NOT_Q
  D_latch d_latch_25 (.EN(not_1_out), .D(nor_20_out), .Q(B1));  // open: NOT_Q
  D_latch d_latch_26 (.EN(not_1_out), .D(nor_21_out), .Q(B2));  // open: NOT_Q
  D_latch d_latch_27 (.EN(not_1_out), .D(nor_22_out), .Q(B3));  // open: NOT_Q
  D_latch d_latch_28 (.EN(not_1_out), .D(nor_23_out), .Q(B4));  // open: NOT_Q
  D_latch d_latch_29 (.EN(not_1_out), .D(nor_24_out), .Q(B5));  // open: NOT_Q
  D_latch d_latch_30 (.EN(not_1_out), .D(nor_25_out), .Q(B6));  // open: NOT_Q
  D_latch d_latch_31 (.EN(not_1_out), .D(nor_26_out), .Q(B7));  // open: NOT_Q
  not not_11 (SYNC_2, d_latch_7_not_q);

  // Notes on the sheet:
  //   0
  //   1
  //   2
  //   0
  //   1
  //   2
  //   0
  //   1
  //   2
  //   R
  //   G
  //   B
endmodule

module RW_CONTROL (
  input  R_W,
  input  nDBE,
  output nRD,
  output nWR
);

  wire nor_1_out, nor_2_out, not_1_out;

  not not_1 (not_1_out, R_W);
  nor nor_1 (nor_1_out, not_1_out, nDBE);
  nor nor_2 (nor_2_out, R_W, nDBE);
  not not_2 (nRD, nor_1_out);
  not not_3 (nWR, nor_2_out);

  // Notes on the sheet:
  //   R/W = 0: write data to PPU
  //   /RD = 0: CPU read data from PPU
  //   /WR = 0: CPU write data to PPU
endmodule

module CPU_DATA_PAD (
  input  nRD,
  input  nWR,
  input  PPU_CPU,
  input  PPU_data_in,
  output PPU_ADRESS_OUT,
  output CPU_PPU
);

  wire not_1_out, not_2_out;

  not not_1 (not_1_out, nRD);
  not not_2 (not_2_out, nWR);
  assign PPU_ADRESS_OUT = not_1_out ? PPU_CPU : 1'bz;  // Controlled_Buffer controlled_buffer_1
  assign CPU_PPU = not_2_out ? PPU_data_in : 1'bz;  // Controlled_Buffer controlled_buffer_2

  // Notes on the sheet:
  //   /RD = 0: CPU read data from PPU
  //   /WR = 0: CPU write data to PPU
endmodule

module INTERRUPT_CONTROL (
  input  VBL_EN,
  input  VSET,
  input  VCLR,
  input  nDBE,
  input  nR2,
  output INT,
  output DB7
);

  wire d_latch_1_q, nor_1_out, not_1_out, or_1_out, s_r_ff_1_q;

  nor nor_1 (nor_1_out, nDBE, nR2);
  or or_1 (or_1_out, VCLR, nor_1_out);
  not not_1 (not_1_out, nor_1_out);
  S_R_Flip_Flop #(.trigger("high")) s_r_ff_1 (
    .S(VSET), .clk(1'b1), .R(or_1_out), .Q(s_r_ff_1_q));  // open: Qn, preset, reset, en
  and and_1 (INT, VBL_EN, s_r_ff_1_q);
  D_latch d_latch_1 (.EN(not_1_out), .D(s_r_ff_1_q), .Q(d_latch_1_q));  // open: NOT_Q
  Multiplexer multiplexer_1 (.in0(1'b0), .in1(1'b1), .out(DB7), .sel(d_latch_1_q), .en(nor_1_out));

  // Notes on the sheet:
  //   R2_EN
  //   VBLANK FLIP/FLOP
  //   TRI-STATE
endmodule

module COLOR_IO (
  input  PCLK,
  input  DB_CB,
  input  CB_DB,
  input  nBW,
  input  RAM_CB0,
  input  DB0,
  input  RAM_CB1,
  input  DB1,
  input  RAM_CB2,
  input  DB2,
  input  RAM_CB3,
  input  DB3,
  input  RAM_CB4,
  input  DB4,
  input  RAM_CB5,
  input  DB5,
  output nout0,
  output DB0_2,
  output CB_RAM0,
  output nout1,
  output DB1_2,
  output CB_RAM1,
  output nout2,
  output DB2_2,
  output CB_RAM2,
  output nout3,
  output DB3_2,
  output CB_RAM3,
  output nout4,
  output DB4_2,
  output CB_RAM4,
  output nout5,
  output DB5_2,
  output CB_RAM5
);

  wire _11_2_out, _11_3_out, _11_4_out, _11_5_out, _11_6_out, _11_out, d_ff_1_q, d_ff_2_q, d_ff_3_q,
       d_ff_4_q, d_ff_5_q, d_ff_6_q, d_latch_5_not_q, d_latch_6_not_q, d_latch_7_not_q, d_latch_8_not_q,
       d_latch_9_not_q, d_latch_10_not_q, d_latch_11_not_q, d_latch_12_not_q, d_latch_13_not_q,
       d_latch_14_not_q, d_latch_15_not_q, d_latch_16_not_q, d_latch_17_not_q, d_latch_18_not_q,
       d_latch_20_not_q, d_latch_22_not_q, nor_1_out, nor_2_out, nor_3_out, nor_4_out, nor_5_out, nor_6_out,
       not_1_out, not_2_out, not_3_out, not_4_out, not_5_out, not_6_out, not_7_out, not_8_out, not_9_out,
       not_10_out, not_11_out, not_12_out, not_13_out;

  D_Flip_Flop d_ff_1 (.clk(PCLK), .D(RAM_CB0), .Q(d_ff_1_q));  // open: Qn, preset, en, reset
  D_Flip_Flop d_ff_2 (.clk(PCLK), .D(RAM_CB1), .Q(d_ff_2_q));  // open: Qn, preset, en, reset
  D_Flip_Flop d_ff_3 (.clk(PCLK), .D(RAM_CB2), .Q(d_ff_3_q));  // open: Qn, preset, en, reset
  D_Flip_Flop d_ff_4 (.clk(PCLK), .D(RAM_CB3), .Q(d_ff_4_q));  // open: Qn, preset, en, reset
  D_Flip_Flop d_ff_5 (.clk(PCLK), .D(RAM_CB4), .Q(d_ff_5_q));  // open: Qn, preset, en, reset
  D_Flip_Flop d_ff_6 (.clk(PCLK), .D(RAM_CB5), .Q(d_ff_6_q));  // open: Qn, preset, en, reset
  nand _11 (_11_out, d_ff_1_q, nBW);
  nand _11_2 (_11_2_out, d_ff_2_q, nBW);
  nand _11_3 (_11_3_out, d_ff_3_q, nBW);
  nand _11_4 (_11_4_out, d_ff_4_q, nBW);
  nand _11_5 (_11_5_out, d_ff_5_q, 1'b1);
  nand _11_6 (_11_6_out, d_ff_6_q, 1'b1);
  not not_1 (not_1_out, PCLK);
  not not_2 (not_2_out, _11_out);
  not not_3 (not_3_out, DB0);
  not not_4 (not_4_out, _11_2_out);
  not not_5 (not_5_out, DB1);
  not not_6 (not_6_out, _11_3_out);
  not not_7 (not_7_out, DB2);
  not not_8 (not_8_out, _11_4_out);
  not not_9 (not_9_out, DB3);
  not not_10 (not_10_out, _11_5_out);
  not not_11 (not_11_out, DB4);
  not not_12 (not_12_out, _11_6_out);
  not not_13 (not_13_out, DB5);
  D_latch d_latch_1 (.EN(not_1_out), .D(not_2_out), .NOT_Q(nout0));  // open: Q
  D_latch d_latch_2 (.EN(not_1_out), .D(not_4_out), .NOT_Q(nout1));  // open: Q
  D_latch d_latch_3 (.EN(not_1_out), .D(not_6_out), .NOT_Q(nout2));  // open: Q
  D_latch d_latch_4 (.EN(not_1_out), .D(not_8_out), .NOT_Q(nout3));  // open: Q
  D_latch d_latch_5 (.EN(not_1_out), .D(not_10_out), .NOT_Q(d_latch_5_not_q));  // open: Q
  D_latch d_latch_6 (.EN(not_1_out), .D(not_12_out), .NOT_Q(d_latch_6_not_q));  // open: Q
  D_latch d_latch_7 (.EN(PCLK), .D(not_2_out), .NOT_Q(d_latch_7_not_q));  // open: Q
  D_latch d_latch_8 (.EN(PCLK), .D(not_4_out), .NOT_Q(d_latch_8_not_q));  // open: Q
  D_latch d_latch_9 (.EN(PCLK), .D(not_6_out), .NOT_Q(d_latch_9_not_q));  // open: Q
  D_latch d_latch_10 (.EN(PCLK), .D(not_8_out), .NOT_Q(d_latch_10_not_q));  // open: Q
  D_latch d_latch_11 (.EN(PCLK), .D(d_latch_5_not_q), .NOT_Q(d_latch_11_not_q));  // open: Q
  D_latch d_latch_12 (.EN(PCLK), .D(not_10_out), .NOT_Q(d_latch_12_not_q));  // open: Q
  D_latch d_latch_13 (.EN(PCLK), .D(d_latch_6_not_q), .NOT_Q(d_latch_13_not_q));  // open: Q
  D_latch d_latch_14 (.EN(PCLK), .D(not_12_out), .NOT_Q(d_latch_14_not_q));  // open: Q
  D_latch d_latch_15 (.EN(not_1_out), .D(d_latch_7_not_q), .NOT_Q(d_latch_15_not_q));  // open: Q
  D_latch d_latch_16 (.EN(not_1_out), .D(d_latch_8_not_q), .NOT_Q(d_latch_16_not_q));  // open: Q
  D_latch d_latch_17 (.EN(not_1_out), .D(d_latch_9_not_q), .NOT_Q(d_latch_17_not_q));  // open: Q
  D_latch d_latch_18 (.EN(not_1_out), .D(d_latch_10_not_q), .NOT_Q(d_latch_18_not_q));  // open: Q
  D_latch d_latch_19 (.EN(not_1_out), .D(d_latch_11_not_q), .NOT_Q(nout4));  // open: Q
  D_latch d_latch_20 (.EN(not_1_out), .D(d_latch_12_not_q), .NOT_Q(d_latch_20_not_q));  // open: Q
  D_latch d_latch_21 (.EN(not_1_out), .D(d_latch_13_not_q), .NOT_Q(nout5));  // open: Q
  D_latch d_latch_22 (.EN(not_1_out), .D(d_latch_14_not_q), .NOT_Q(d_latch_22_not_q));  // open: Q
  nor nor_1 (nor_1_out, d_latch_15_not_q, CB_DB);
  nor nor_2 (nor_2_out, d_latch_16_not_q, CB_DB);
  nor nor_3 (nor_3_out, d_latch_17_not_q, CB_DB);
  nor nor_4 (nor_4_out, d_latch_18_not_q, CB_DB);
  nor nor_5 (nor_5_out, d_latch_20_not_q, CB_DB);
  nor nor_6 (nor_6_out, d_latch_22_not_q, CB_DB);
  not not_14 (DB0_2, nor_1_out);
  nor nor_7 (CB_RAM0, DB_CB, not_3_out);
  not not_15 (DB1_2, nor_2_out);
  nor nor_8 (CB_RAM1, DB_CB, not_5_out);
  not not_16 (DB2_2, nor_3_out);
  nor nor_9 (CB_RAM2, DB_CB, not_7_out);
  not not_17 (DB3_2, nor_4_out);
  nor nor_10 (CB_RAM3, DB_CB, not_9_out);
  not not_18 (DB4_2, nor_5_out);
  nor nor_11 (CB_RAM4, DB_CB, not_11_out);
  not not_19 (DB5_2, nor_6_out);
  nor nor_12 (CB_RAM5, DB_CB, not_13_out);

  // Notes on the sheet:
  //   14
  //   6
  //   14
  //   6
  //   14
  //   6
  //   14
  //   6
  //   14
  //   6
  //   14
  //   6
  //   4
  //   4
  //   4
  //   4
  //   7
  //   4
  //   7
  //   4
  //   3
  //   3
  //   3
  //   3
  //   8
  //   3
  //   8
  //   3
endmodule

module COLOR_CONTROL (
  input  PCLK,
  input  DB_PAR,
  input  TH_MUX,
  input  nR7,
  input  nDBE,
  input  PICTURE,
  input  BW,
  output DB_CB,
  output CB_DB,
  output COLOR_EN
);

  wire d_latch_1_q, nand_1_out, nor_1_out, not_1_out, not_3_out;

  D_latch d_latch_1 (.EN(PCLK), .D(DB_PAR), .Q(d_latch_1_q));  // open: NOT_Q
  not not_1 (not_1_out, TH_MUX);
  not not_2 (CB_DB, nor_1_out);
  nor nor_1 (nor_1_out, not_1_out, nR7, nDBE);
  nand nand_1 (nand_1_out, CB_DB, PICTURE);
  not not_3 (not_3_out, BW);
  nand nand_2 (DB_CB, d_latch_1_q, TH_MUX);
  and and_1 (COLOR_EN, nand_1_out, not_3_out);
endmodule

module CONTROL_REGS (
  input  RC,
  input  nDBE,
  input  nW0,
  input  DB0,
  input  DB1,
  input  DB2,
  input  DB3,
  input  DB4,
  input  DB5,
  input  DB6,
  input  DB7,
  input  nW1,
  input  PCLK,
  input  nVIS,
  input  CLIP_B,
  input  CLIP_O,
  output I1_32,
  output OBSEL,
  output BGSEL,
  output O8_16,
  output nSLAVE,
  output VBL,
  output BW,
  output nBGCLIP,
  output nOBCLIP,
  output CLPB,
  output CLPO,
  output nTR,
  output nTG,
  output nTB,
  output BLACK
);

  wire d_ff_1_q, d_ff_2_q, d_ff_3_q, d_ff_4_q, d_ff_5_q, d_ff_6_q, d_ff_7_q, d_ff_8_q, d_ff_9_q, d_ff_10_q,
       d_ff_11_q, d_ff_12_q, d_ff_13_q, d_ff_14_q, d_ff_15_q, d_ff_16_q, d_latch_7_q, d_latch_8_q,
       d_latch_11_q, d_latch_12_q, d_latch_13_not_q, nor_1_out, nor_2_out, nor_3_out, nor_5_out, not_1_out,
       not_2_out, not_3_out, not_4_out, not_5_out, not_8_out, not_10_out;

  not not_1 (not_1_out, PCLK);
  D_Flip_Flop #(.trigger("low")) d_ff_1 (.clk(PCLK), .D(nor_3_out), .Q(d_ff_1_q));  // open: Qn, preset, en, reset
  nor nor_1 (nor_1_out, nDBE, nW0);
  nor nor_2 (nor_2_out, nDBE, nW1);
  D_Flip_Flop #(.trigger("low")) d_ff_2 (.clk(not_1_out), .D(d_ff_1_q), .Q(d_ff_2_q));  // open: Qn, preset, en, reset
  not not_2 (not_2_out, nor_1_out);
  D_Flip_Flop #(.trigger("high")) d_ff_3 (.clk(nor_1_out), .D(DB2), .Q(d_ff_3_q), .reset(RC));  // open: Qn, preset, en
  D_Flip_Flop #(.trigger("high")) d_ff_4 (.clk(nor_1_out), .D(DB3), .Q(d_ff_4_q), .reset(RC));  // open: Qn, preset, en
  D_Flip_Flop #(.trigger("high")) d_ff_5 (.clk(nor_1_out), .D(DB4), .Q(d_ff_5_q), .reset(RC));  // open: Qn, preset, en
  D_Flip_Flop #(.trigger("high")) d_ff_6 (.clk(nor_1_out), .D(DB5), .Q(d_ff_6_q), .reset(RC));  // open: Qn, preset, en
  D_Flip_Flop #(.trigger("high")) d_ff_7 (.clk(nor_1_out), .D(DB6), .Q(d_ff_7_q), .reset(RC));  // open: Qn, preset, en
  D_Flip_Flop #(.trigger("high")) d_ff_8 (.clk(nor_1_out), .D(DB7), .Q(d_ff_8_q), .reset(RC));  // open: Qn, preset, en
  not not_3 (not_3_out, nor_2_out);
  D_Flip_Flop #(.trigger("high")) d_ff_9 (.clk(nor_2_out), .D(DB0), .Q(d_ff_9_q), .reset(RC));  // open: Qn, preset, en
  D_Flip_Flop #(.trigger("high")) d_ff_10 (
    .clk(nor_2_out), .D(DB1), .Q(d_ff_10_q), .reset(RC));  // open: Qn, preset, en
  D_Flip_Flop #(.trigger("high")) d_ff_11 (
    .clk(nor_2_out), .D(DB2), .Q(d_ff_11_q), .reset(RC));  // open: Qn, preset, en
  D_Flip_Flop #(.trigger("high")) d_ff_12 (
    .clk(nor_2_out), .D(DB3), .Q(d_ff_12_q), .reset(RC));  // open: Qn, preset, en
  D_Flip_Flop #(.trigger("high")) d_ff_13 (
    .clk(nor_2_out), .D(DB4), .Q(d_ff_13_q), .reset(RC));  // open: Qn, preset, en
  D_Flip_Flop #(.trigger("high")) d_ff_14 (
    .clk(nor_2_out), .D(DB5), .Q(d_ff_14_q), .reset(RC));  // open: Qn, preset, en
  D_Flip_Flop #(.trigger("high")) d_ff_15 (
    .clk(nor_2_out), .D(DB6), .Q(d_ff_15_q), .reset(RC));  // open: Qn, preset, en
  D_Flip_Flop #(.trigger("high")) d_ff_16 (
    .clk(nor_2_out), .D(DB7), .Q(d_ff_16_q), .reset(RC));  // open: Qn, preset, en
  D_latch d_latch_1 (.EN(not_2_out), .D(d_ff_3_q), .NOT_Q(I1_32));  // open: Q
  D_latch d_latch_2 (.EN(not_2_out), .D(d_ff_4_q), .NOT_Q(OBSEL));  // open: Q
  D_latch d_latch_3 (.EN(not_2_out), .D(d_ff_5_q), .NOT_Q(BGSEL));  // open: Q
  D_latch d_latch_4 (.EN(not_2_out), .D(d_ff_6_q), .NOT_Q(O8_16));  // open: Q
  D_latch d_latch_5 (.EN(not_3_out), .D(d_ff_10_q), .Q(nBGCLIP));  // open: NOT_Q
  D_latch d_latch_6 (.EN(not_3_out), .D(d_ff_11_q), .Q(nOBCLIP));  // open: NOT_Q
  D_latch d_latch_7 (.EN(not_3_out), .D(d_ff_12_q), .Q(d_latch_7_q));  // open: NOT_Q
  D_latch d_latch_8 (.EN(not_3_out), .D(d_ff_13_q), .Q(d_latch_8_q));  // open: NOT_Q
  D_latch d_latch_9 (.EN(not_3_out), .D(d_ff_14_q), .NOT_Q(nTR));  // open: Q
  D_latch d_latch_10 (.EN(not_3_out), .D(d_ff_15_q), .NOT_Q(nTG));  // open: Q
  D_latch d_latch_11 (.EN(not_1_out), .D(nVIS), .Q(d_latch_11_q));  // open: NOT_Q
  D_latch d_latch_12 (.EN(not_1_out), .D(CLIP_B), .Q(d_latch_12_q));  // open: NOT_Q
  D_latch d_latch_13 (.EN(PCLK), .D(d_ff_2_q), .NOT_Q(d_latch_13_not_q));  // open: Q
  not not_4 (not_4_out, d_latch_7_q);
  nor nor_3 (nor_3_out, d_latch_7_q, d_latch_8_q);
  not not_5 (not_5_out, d_latch_8_q);
  not not_6 (nTB, d_ff_16_q);
  assign BLACK = not_1_out ? d_latch_13_not_q : 1'bz;  // Controlled_Buffer controlled_buffer_1
  not not_7 (nSLAVE, not_8_out);
  not not_8 (not_8_out, d_ff_7_q);
  assign VBL = nor_1_out ? d_ff_8_q : 1'bz;  // Controlled_Buffer controlled_buffer_2
  not not_9 (BW, not_10_out);
  not not_10 (not_10_out, d_ff_9_q);
  nor nor_4 (CLPB, d_latch_11_q, not_4_out, d_latch_12_q);
  nor nor_5 (nor_5_out, d_latch_11_q, not_5_out, CLIP_O);
  D_latch d_latch_14 (.EN(not_1_out), .D(nor_5_out), .NOT_Q(CLPO));  // open: Q

  // Notes on the sheet:
  //   bits 0 and 1 are in the PPU address generator circuit
  //   !
  //   !
  //   !!! INVERSE LOGIC PAL
  //   !!! INVERSE LOGIC PAL
  //   !
  //   !
  //   !
  //   $2000
  //   $2001
endmodule

module MUX (
  input  EXT3_IN,
  input  EXT2_IN,
  input  EXT1_IN,
  input  EXT0_IN,
  input  PCLK,
  input  BGC0,
  input  BGC1,
  input  BGC2,
  input  BGC3,
  input  nZCOL0,
  input  nZCOL1,
  input  ZCOL2,
  input  ZCOL3,
  input  nZPRIO,
  input  THO0,
  input  THO1,
  input  THO2,
  input  THO3,
  input  THO4,
  input  TH_MUX,
  input  nSPR0HIT,
  input  I2SEV,
  input  nVIS,
  input  RESCL,
  input  nDBE,
  input  nR2,
  output EXT0_OUT,
  output EXT1_OUT,
  output EXT2_OUT,
  output EXT3_OUT,
  output PAL0,
  output PAL1,
  output PAL2,
  output PAL3,
  output PAL4,
  output DB6
);

  wire and_1_out, d_latch_1_not_q, d_latch_2_not_q, d_latch_3_not_q, d_latch_4_not_q, d_latch_5_not_q,
       d_latch_6_not_q, d_latch_7_not_q, d_latch_8_not_q, d_latch_9_not_q, d_latch_10_not_q,
       d_latch_11_not_q, d_latch_12_not_q, d_latch_13_not_q, d_latch_14_not_q, d_latch_15_not_q,
       d_latch_16_q, d_latch_17_q, d_latch_18_not_q, d_latch_19_not_q, d_latch_20_not_q, d_latch_21_not_q,
       multiplexer_1_out, multiplexer_2_out, multiplexer_3_out, multiplexer_4_out, multiplexer_5_out,
       multiplexer_6_out, multiplexer_7_out, multiplexer_8_out, multiplexer_9_out, multiplexer_10_out,
       multiplexer_11_out, multiplexer_12_out, multiplexer_13_out, nor_1_out, nor_2_out, nor_3_out,
       nor_4_out, nor_5_out, nor_6_out, nor_7_out, not_1_out, not_2_out, not_3_out, not_4_out, not_9_out,
       or_1_out;

  not not_1 (not_1_out, ZCOL2);
  not not_2 (not_2_out, ZCOL3);
  not not_3 (not_3_out, nZPRIO);
  nor nor_1 (nor_1_out, nDBE, nR2);
  nor nor_2 (nor_2_out, BGC1, BGC0);
  D_latch d_latch_1 (.EN(PCLK), .D(nZCOL0), .NOT_Q(d_latch_1_not_q));  // open: Q
  D_latch d_latch_2 (.EN(PCLK), .D(nZCOL1), .NOT_Q(d_latch_2_not_q));  // open: Q
  D_latch d_latch_3 (.EN(PCLK), .D(not_1_out), .NOT_Q(d_latch_3_not_q));  // open: Q
  D_latch d_latch_4 (.EN(PCLK), .D(not_2_out), .NOT_Q(d_latch_4_not_q));  // open: Q
  D_latch d_latch_5 (.EN(PCLK), .D(not_3_out), .NOT_Q(d_latch_5_not_q));  // open: Q
  D_latch d_latch_6 (.EN(PCLK), .D(THO0), .NOT_Q(d_latch_6_not_q));  // open: Q
  D_latch d_latch_7 (.EN(PCLK), .D(THO1), .NOT_Q(d_latch_7_not_q));  // open: Q
  D_latch d_latch_8 (.EN(PCLK), .D(THO2), .NOT_Q(d_latch_8_not_q));  // open: Q
  D_latch d_latch_9 (.EN(PCLK), .D(THO3), .NOT_Q(d_latch_9_not_q));  // open: Q
  D_latch d_latch_10 (.EN(PCLK), .D(THO4), .NOT_Q(d_latch_10_not_q));  // open: Q
  Multiplexer #(.enable("false")) multiplexer_1 (
    .in0(BGC0), .in1(d_latch_1_not_q), .out(multiplexer_1_out), .sel(nor_6_out));
  Multiplexer #(.enable("false")) multiplexer_2 (
    .in0(BGC1), .in1(d_latch_2_not_q), .out(multiplexer_2_out), .sel(nor_6_out));
  Multiplexer #(.enable("false")) multiplexer_3 (
    .in0(BGC2), .in1(d_latch_3_not_q), .out(multiplexer_3_out), .sel(nor_6_out));
  Multiplexer #(.enable("false")) multiplexer_4 (
    .in0(BGC3), .in1(d_latch_4_not_q), .out(multiplexer_4_out), .sel(nor_6_out));
  not not_4 (not_4_out, nor_2_out);
  not not_5 (EXT0_OUT, multiplexer_1_out);
  not not_6 (EXT1_OUT, multiplexer_2_out);
  not not_7 (EXT2_OUT, multiplexer_3_out);
  not not_8 (EXT3_OUT, multiplexer_4_out);
  or or_1 (or_1_out, d_latch_1_not_q, d_latch_2_not_q);
  nor nor_3 (nor_3_out, nor_2_out, PCLK, nSPR0HIT, I2SEV, nVIS);
  and and_1 (and_1_out, not_4_out, d_latch_5_not_q);
  nor nor_4 (nor_4_out, nor_3_out, nor_5_out);
  nor nor_5 (nor_5_out, nor_4_out, RESCL);
  not not_9 (not_9_out, PCLK);
  nor nor_6 (nor_6_out, and_1_out, or_1_out);
  D_latch d_latch_11 (.EN(not_9_out), .D(EXT0_OUT), .NOT_Q(d_latch_11_not_q));  // open: Q
  D_latch d_latch_12 (.EN(not_9_out), .D(EXT1_OUT), .NOT_Q(d_latch_12_not_q));  // open: Q
  D_latch d_latch_13 (.EN(not_9_out), .D(EXT2_OUT), .NOT_Q(d_latch_13_not_q));  // open: Q
  D_latch d_latch_14 (.EN(not_9_out), .D(EXT3_OUT), .NOT_Q(d_latch_14_not_q));  // open: Q
  D_latch d_latch_15 (.EN(not_9_out), .D(nor_6_out), .NOT_Q(d_latch_15_not_q));  // open: Q
  D_latch d_latch_16 (.EN(not_9_out), .D(not_4_out), .Q(d_latch_16_q));  // open: NOT_Q
  D_latch d_latch_17 (.EN(not_9_out), .D(or_1_out), .Q(d_latch_17_q));  // open: NOT_Q
  nor nor_7 (nor_7_out, d_latch_16_q, d_latch_17_q);
  Multiplexer #(.enable("false")) multiplexer_5 (
    .in0(d_latch_11_not_q), .in1(EXT0_IN), .out(multiplexer_5_out), .sel(nor_7_out));
  Multiplexer #(.enable("false")) multiplexer_6 (
    .in0(d_latch_12_not_q), .in1(EXT1_IN), .out(multiplexer_6_out), .sel(nor_7_out));
  Multiplexer #(.enable("false")) multiplexer_7 (
    .in0(d_latch_13_not_q), .in1(EXT2_IN), .out(multiplexer_7_out), .sel(nor_7_out));
  Multiplexer #(.enable("false")) multiplexer_8 (
    .in0(d_latch_14_not_q), .in1(EXT3_IN), .out(multiplexer_8_out), .sel(nor_7_out));
  D_latch d_latch_18 (.EN(PCLK), .D(multiplexer_5_out), .NOT_Q(d_latch_18_not_q));  // open: Q
  D_latch d_latch_19 (.EN(PCLK), .D(multiplexer_6_out), .NOT_Q(d_latch_19_not_q));  // open: Q
  D_latch d_latch_20 (.EN(PCLK), .D(multiplexer_7_out), .NOT_Q(d_latch_20_not_q));  // open: Q
  D_latch d_latch_21 (.EN(PCLK), .D(multiplexer_8_out), .NOT_Q(d_latch_21_not_q));  // open: Q
  Multiplexer #(.enable("false")) multiplexer_9 (
    .in0(d_latch_18_not_q), .in1(d_latch_6_not_q), .out(multiplexer_9_out), .sel(TH_MUX));
  Multiplexer #(.enable("false")) multiplexer_10 (
    .in0(d_latch_19_not_q), .in1(d_latch_7_not_q), .out(multiplexer_10_out), .sel(TH_MUX));
  Multiplexer #(.enable("false")) multiplexer_11 (
    .in0(d_latch_20_not_q), .in1(d_latch_8_not_q), .out(multiplexer_11_out), .sel(TH_MUX));
  Multiplexer #(.enable("false")) multiplexer_12 (
    .in0(d_latch_21_not_q), .in1(d_latch_9_not_q), .out(multiplexer_12_out), .sel(TH_MUX));
  Multiplexer #(.enable("false")) multiplexer_13 (
    .in0(d_latch_15_not_q), .in1(d_latch_10_not_q), .out(multiplexer_13_out), .sel(TH_MUX));
  Multiplexer multiplexer_14 (.in0(1'b0), .in1(1'b1), .out(DB6), .sel(nor_5_out), .en(nor_1_out));
  D_latch d_latch_22 (.EN(PCLK), .D(multiplexer_13_out), .NOT_Q(PAL4));  // open: Q
  not not_10 (PAL0, multiplexer_9_out);
  not not_11 (PAL1, multiplexer_10_out);
  not not_12 (PAL2, multiplexer_11_out);
  not not_13 (PAL3, multiplexer_12_out);

  // Notes on the sheet:
  //   TH contain directly loaded color
  //   R2'
  //   Sprite/background
  //    strike test
  //   MUX - select one of 4 sources for final color output
  //   OCOL
  //   External/Prev
  //   EXT
  //   Direct/Prev
  //   TRI-STATE
endmodule

module OAM_EVAL (
  input  PCLK,
  input  F_NT,
  input  H0_prime_prime,
  input  I_OAM2,
  input  nVIS,
  input  SPR_OV,
  input  S_EV,
  input  PAR_O,
  input  O8_16,
  input  OB0,
  input  OB1,
  input  OB2,
  input  OB3,
  input  OB4,
  input  OB5,
  input  OB6,
  input  OB7,
  input  V0,
  input  V1,
  input  V2,
  input  V3,
  input  V4,
  input  V5,
  input  V6,
  input  V7,
  output _0_FIFO,
  output OMFG,
  output I2SEV,
  output OV0,
  output OV1,
  output OV2,
  output OV3
);

  wire _2_out, _3_out, _10_out, _14_out, _18_out, _19_out, _20_out, _24_out, _29_out, d_ff_1_qn,
       d_latch_1_not_q, d_latch_2_not_q, d_latch_3_q, d_latch_4_not_q, d_latch_5_not_q, d_latch_6_not_q,
       d_latch_7_not_q, d_latch_8_not_q, d_latch_9_not_q, nor_1_out, not_1_out, not_2_out, not_3_out,
       not_4_out, not_6_out, not_7_out, nPCLK, OVZ, undriven, undriven_2, undriven_3, undriven_4;

  not not_1 (not_1_out, H0_prime_prime);
  not not_2 (not_2_out, S_EV);
  not not_3 (not_3_out, PAR_O);
  not not_4 (not_4_out, O8_16);
  not not_5 (nPCLK, PCLK);
  nor _29 (_29_out, I_OAM2, nVIS, SPR_OV, OVZ);
  nor _20 (_20_out, F_NT, not_1_out);
  nor _19 (_19_out, PCLK, not_1_out);
  nor _24 (_24_out, not_2_out, PCLK);
  nor _2 (_2_out, PCLK, not_3_out);
  not not_6 (not_6_out, _20_out);
  D_latch d_latch_1 (.EN(_19_out), .D(_29_out), .NOT_Q(d_latch_1_not_q));  // open: Q
  D_latch d_latch_2 (.EN(PCLK), .D(OB7), .NOT_Q(d_latch_2_not_q));  // open: Q
  D_latch d_latch_3 (.EN(nPCLK), .D(not_6_out), .Q(d_latch_3_q));  // open: NOT_Q
  D_latch d_latch_4 (.EN(PCLK), .D(d_latch_1_not_q), .NOT_Q(d_latch_4_not_q));  // open: Q
  D_Flip_Flop #(.trigger("low")) d_ff_1 (
    .clk(PCLK), .D(_29_out), .Qn(d_ff_1_qn), .en(_24_out));  // open: Q, preset, reset
  nor _18 (_18_out, nPCLK, d_latch_3_q);
  D_latch d_latch_5 (.EN(_19_out), .D(d_latch_4_not_q), .NOT_Q(d_latch_5_not_q));  // open: Q
  nor _14 (_14_out, d_latch_2_not_q, V7);
  D_latch d_latch_6 (.EN(PCLK), .D(d_latch_5_not_q), .NOT_Q(d_latch_6_not_q));  // open: Q
  D_latch d_latch_7 (.EN(nPCLK), .D(OVZ), .NOT_Q(d_latch_7_not_q));  // open: Q
  D_latch d_latch_8 (.EN(_19_out), .D(d_latch_6_not_q), .NOT_Q(d_latch_8_not_q));  // open: Q
  D_Flip_Flop #(.trigger("low")) d_ff_2 (.clk(PCLK), .D(d_ff_1_qn), .Q(I2SEV), .en(_2_out));  // open: Qn, preset, reset
  D_Flip_Flop #(.trigger("low")) d_ff_3 (
    .clk(PCLK), .D(d_latch_7_not_q), .Q(_0_FIFO), .en(_18_out));  // open: Qn, preset, reset
  D_latch d_latch_9 (.EN(PCLK), .D(d_latch_8_not_q), .NOT_Q(d_latch_9_not_q));  // open: Q
  and _3 (_3_out, not_4_out, OV3);
  not not_7 (not_7_out, _10_out);
  nor _10 (_10_out, d_latch_9_not_q, d_latch_6_not_q, d_latch_4_not_q);
  Counter counter_1 (.count(1'b1), .clk(I2SEV));  // open: load, D, Q, carry, clr
  nor nor_1 (nor_1_out, not_7_out, _3_out, undriven, undriven_2, undriven_3, undriven_4, _14_out);
  Counter counter_2 (.count(1'b1), .clk(_0_FIFO));  // open: load, D, Q, carry, clr
  nor _12 (OMFG, not_7_out, _29_out);
  not not_8 (OVZ, nor_1_out);

  // Notes on the sheet:
  //   22
  //   23
  //   1
  //   3
  //   21
  //   DDD
  //   1
  //   /I2
  //   9
  //   2
  //   FF2
  //   7
  //   3
  //   4
  //   8
  //   5
  //   FF1
  //   6
  //   FF3
  //   11
  //   OVZ
  //   29
  //   SPTITE EVAL COPY SPRITE
  //   SPRITE 0  ON CURRENT SCANLINE
endmodule

module OAM_SUBSTRACTOR (
  input  PCLK,
  input  OB0,
  input  OB1,
  input  OB2,
  input  OB3,
  input  OB4,
  input  OB5,
  input  OB6,
  input  OB7,
  input  V0,
  input  V1,
  input  V2,
  input  V3,
  input  V4,
  input  V5,
  input  V6,
  input  V7,
  output OV0,
  output OV1,
  output OV2,
  output OV3,
  output OV4,
  output OV5,
  output OV6,
  output OV7
);

  wire d_latch_1_not_q, d_latch_2_not_q, d_latch_3_not_q, d_latch_4_not_q, d_latch_5_not_q, d_latch_6_not_q,
       d_latch_7_not_q, d_latch_8_not_q, nand_1_out, nand_2_out, nand_3_out, nand_4_out, nand_5_out,
       nand_6_out, nand_7_out, nand_8_out, nor_1_out, nor_2_out, nor_3_out, nor_4_out, nor_5_out, nor_6_out,
       nor_7_out, nor_8_out, nor_9_out, nor_10_out, nor_11_out, nor_12_out, nor_13_out, nor_14_out,
       nor_15_out, nor_16_out, nor_17_out, nor_18_out, nor_19_out, nor_20_out, nor_21_out, nor_22_out,
       nor_23_out, nor_24_out, nor_25_out, nor_26_out, nor_27_out, nor_28_out, nor_29_out, nor_30_out,
       nor_31_out, nor_32_out, nor_33_out, nor_34_out, nor_35_out, nor_36_out, not_1_out, not_2_out,
       not_3_out, not_4_out, not_5_out, not_6_out, not_7_out, not_8_out;

  D_latch d_latch_1 (.EN(PCLK), .D(OB0), .NOT_Q(d_latch_1_not_q));  // open: Q
  D_latch d_latch_2 (.EN(PCLK), .D(OB1), .NOT_Q(d_latch_2_not_q));  // open: Q
  D_latch d_latch_3 (.EN(PCLK), .D(OB2), .NOT_Q(d_latch_3_not_q));  // open: Q
  D_latch d_latch_4 (.EN(PCLK), .D(OB3), .NOT_Q(d_latch_4_not_q));  // open: Q
  D_latch d_latch_5 (.EN(PCLK), .D(OB4), .NOT_Q(d_latch_5_not_q));  // open: Q
  D_latch d_latch_6 (.EN(PCLK), .D(OB5), .NOT_Q(d_latch_6_not_q));  // open: Q
  D_latch d_latch_7 (.EN(PCLK), .D(OB6), .NOT_Q(d_latch_7_not_q));  // open: Q
  D_latch d_latch_8 (.EN(PCLK), .D(OB7), .NOT_Q(d_latch_8_not_q));  // open: Q
  nor nor_1 (nor_1_out, d_latch_1_not_q, V0);
  nand nand_1 (nand_1_out, V0, d_latch_1_not_q);
  nor nor_2 (nor_2_out, d_latch_2_not_q, V1);
  nand nand_2 (nand_2_out, V1, d_latch_2_not_q);
  nor nor_3 (nor_3_out, d_latch_3_not_q, V2);
  nand nand_3 (nand_3_out, V2, d_latch_3_not_q);
  nor nor_4 (nor_4_out, d_latch_4_not_q, V3);
  nand nand_4 (nand_4_out, V3, d_latch_4_not_q);
  nor nor_5 (nor_5_out, d_latch_5_not_q, V4);
  nand nand_5 (nand_5_out, V4, d_latch_5_not_q);
  nor nor_6 (nor_6_out, d_latch_6_not_q, V5);
  nand nand_6 (nand_6_out, V5, d_latch_6_not_q);
  nor nor_7 (nor_7_out, d_latch_7_not_q, V6);
  nand nand_7 (nand_7_out, V6, d_latch_7_not_q);
  nor nor_8 (nor_8_out, d_latch_8_not_q, V7);
  nand nand_8 (nand_8_out, V7, d_latch_8_not_q);
  not not_1 (not_1_out, nand_1_out);
  not not_2 (not_2_out, nand_3_out);
  not not_3 (not_3_out, nand_5_out);
  not not_4 (not_4_out, nand_7_out);
  nor nor_9 (nor_9_out, nor_1_out, not_1_out);
  not not_5 (not_5_out, nand_2_out);
  nor nor_10 (nor_10_out, nor_2_out, nand_1_out);
  nor nor_11 (nor_11_out, nor_2_out, 1'b0, nor_1_out);
  nor nor_12 (nor_12_out, nor_3_out, not_2_out);
  not not_6 (not_6_out, nand_4_out);
  nor nor_13 (nor_13_out, nor_4_out, nand_3_out);
  nor nor_14 (nor_14_out, nor_4_out, nor_30_out, nor_3_out);
  nor nor_15 (nor_15_out, nor_5_out, not_3_out);
  not not_7 (not_7_out, nand_6_out);
  nor nor_16 (nor_16_out, nor_6_out, nand_5_out);
  nor nor_17 (nor_17_out, nor_6_out, nor_32_out, nor_5_out);
  nor nor_18 (nor_18_out, nor_7_out, not_4_out);
  not not_8 (not_8_out, nand_8_out);
  nor nor_19 (nor_19_out, nor_8_out, nand_7_out);
  nor nor_20 (nor_20_out, nor_8_out, nor_34_out, nor_7_out);
  nor nor_21 (nor_21_out, 1'b0, nor_1_out);
  nor nor_22 (nor_22_out, nor_2_out, not_5_out);
  nor nor_23 (nor_23_out, nor_30_out, nor_3_out);
  nor nor_24 (nor_24_out, nor_4_out, not_6_out);
  nor nor_25 (nor_25_out, nor_32_out, nor_5_out);
  nor nor_26 (nor_26_out, nor_6_out, not_7_out);
  nor nor_27 (nor_27_out, nor_34_out, nor_7_out);
  nor nor_28 (nor_28_out, nor_8_out, not_8_out);
  xnor xnor_1 (OV0, nor_9_out, 1'b0);
  nor nor_29 (nor_29_out, nor_21_out, not_1_out);
  xnor xnor_2 (OV1, nor_29_out, nor_22_out);
  nor nor_30 (nor_30_out, not_5_out, nor_10_out, nor_11_out);
  xnor xnor_3 (OV2, nor_12_out, nor_30_out);
  nor nor_31 (nor_31_out, nor_23_out, not_2_out);
  xnor xnor_4 (OV3, nor_31_out, nor_24_out);
  nor nor_32 (nor_32_out, not_6_out, nor_13_out, nor_14_out);
  xnor xnor_5 (OV4, nor_15_out, nor_32_out);
  nor nor_33 (nor_33_out, nor_25_out, not_3_out);
  xnor xnor_6 (OV5, nor_33_out, nor_26_out);
  nor nor_34 (nor_34_out, not_7_out, nor_16_out, nor_17_out);
  xnor xnor_7 (OV6, nor_18_out, nor_34_out);
  nor nor_35 (nor_35_out, nor_27_out, not_4_out);
  xnor xnor_8 (OV7, nor_35_out, nor_28_out);
  nor nor_36 (nor_36_out, not_8_out, nor_19_out, nor_20_out);

  // Notes on the sheet:
  //   S=V-OB
  //   8-BIT SIGNED SUBTRACT
endmodule

module OAM_CONTROL (
  input  PCLK,
  input  OFETCH,
  input  ZOMG_PAL,
  input  BLNK,
  input  nVIS,
  input  H0_prime_prime,
  input  I_OAM2,
  input  OMFG,
  input  nDBE,
  input  nW3,
  input  PAR_O,
  input  DB0,
  input  DB1,
  input  DB2,
  input  DB3,
  input  DB4,
  input  DB5,
  input  DB6,
  input  DB7,
  input  EVAL,
  input  H2_prime,
  input  H0_prime,
  input  RESCL,
  input  nR2,
  output nOAM0,
  output nOAM1,
  output nOAM2,
  output nOAM3,
  output nOAM4,
  output nOAM5,
  output nOAM6,
  output nOAM7,
  output nOAM8,
  output SPR_OV,
  output OAMCTR2,
  output DB5_2
);

  wire _6_out, _8_out, _9_out, _10_out, _14_out, _23_out, _27_out, and_1_out, d_ff_1_qn, d_latch_1_not_q,
       d_latch_2_q, d_latch_3_not_q, d_latch_4_q, d_latch_5_q, d_latch_6_q, d_latch_7_q, d_latch_8_q,
       d_latch_9_not_q, d_latch_10_not_q, d_latch_11_q, d_latch_12_q, d_latch_13_not_q, d_latch_14_q,
       multiplexer_1_out, multiplexer_2_out, multiplexer_3_out, multiplexer_4_out, multiplexer_5_out,
       nand_1_out, nand_2_out, nand_3_out, nand_4_out, nor_1_out, nor_2_out, nor_3_out, nor_4_out, nor_5_out,
       nor_6_out, nor_7_out, nor_8_out, nor_9_out, nor_10_out, nor_11_out, nor_12_out, nor_13_out,
       nor_15_out, nor_16_out, not_2_out, not_3_out, not_4_out, not_5_out, not_6_out, not_7_out, nPCLK,
       or_1_out, or_2_out, undriven, undriven_2, undriven_3, undriven_4, undriven_5, undriven_6, undriven_7,
       undriven_8, undriven_9, undriven_10, undriven_11, undriven_12, undriven_13, undriven_14, undriven_15;

  not not_1 (nPCLK, PCLK);
  not not_2 (not_2_out, H2_prime);
  not not_3 (not_3_out, OMFG);
  not not_4 (not_4_out, BLNK);
  or or_1 (or_1_out, nVIS, H0_prime_prime);
  nor nor_1 (nor_1_out, nVIS, I_OAM2);
  nor nor_2 (nor_2_out, BLNK, not_5_out);
  not not_5 (not_5_out, OMFG);
  nor nor_3 (nor_3_out, nDBE, nW3);
  nand nand_1 (nand_1_out, EVAL, nor_16_out);
  and and_1 (and_1_out, PAR_O, not_2_out);
  D_latch d_latch_1 (.EN(nPCLK), .D(not_3_out), .NOT_Q(d_latch_1_not_q));  // open: Q
  D_latch d_latch_2 (.EN(nPCLK), .D(I_OAM2), .Q(d_latch_2_q));  // open: NOT_Q
  nor nor_4 (nor_4_out, nR2, nDBE);
  not not_6 (not_6_out, nor_4_out);
  D_latch d_latch_3 (.EN(nPCLK), .D(OFETCH), .NOT_Q(d_latch_3_not_q));  // open: Q
  nand nand_2 (nand_2_out, not_4_out, or_1_out);
  nand nand_3 (nand_3_out, H0_prime_prime, nor_1_out);
  D_latch d_latch_4 (.EN(nPCLK), .D(EVAL), .Q(d_latch_4_q));  // open: NOT_Q
  D_latch d_latch_5 (.EN(nPCLK), .D(nand_1_out), .Q(d_latch_5_q));  // open: NOT_Q
  nor nor_5 (nor_5_out, and_1_out, nor_9_out);
  nor nor_6 (nor_6_out, d_latch_1_not_q, d_latch_2_q);
  nor nor_7 (nor_7_out, nPCLK, d_latch_4_q);
  nor nor_8 (nor_8_out, nPCLK, d_latch_5_q, nor_5_out);
  nor nor_9 (nor_9_out, nor_6_out, H0_prime);
  nor nor_10 (nor_10_out, nPCLK, d_latch_3_not_q);
  D_latch d_latch_6 (.EN(nPCLK), .D(nand_3_out), .Q(d_latch_6_q));  // open: NOT_Q
  nor _23 (_23_out, nor_10_out, ZOMG_PAL);
  or or_2 (or_2_out, nPCLK, d_latch_6_q);
  nand nand_4 (nand_4_out, or_2_out, _23_out);
  nor _8 (_8_out, nor_3_out, _9_out);
  nor _9 (_9_out, _8_out, d_latch_13_not_q);
  D_latch d_latch_7 (.EN(nPCLK), .D(nor_16_out), .Q(d_latch_7_q));  // open: NOT_Q
  D_latch d_latch_8 (.EN(nPCLK), .D(OMFG), .Q(d_latch_8_q));  // open: NOT_Q
  nor _6 (_6_out, nor_3_out, _8_out);
  D_Flip_Flop #(.trigger("low")) d_ff_1 (.clk(PCLK), .D(_6_out), .Qn(d_ff_1_qn));  // open: Q, preset, en, reset
  nor nor_11 (nor_11_out, nPCLK, d_latch_7_q, d_latch_8_q, H0_prime);
  D_latch d_latch_9 (.EN(nPCLK), .D(d_ff_1_qn), .NOT_Q(d_latch_9_not_q));  // open: Q
  nor nor_12 (nor_12_out, nor_11_out, nor_13_out);
  nor nor_13 (nor_13_out, nor_12_out, RESCL);
  D_latch d_latch_10 (.EN(PCLK), .D(d_latch_9_not_q), .NOT_Q(d_latch_10_not_q));  // open: Q
  D_latch d_latch_11 (.EN(nPCLK), .D(undriven_9), .Q(d_latch_11_q));  // open: NOT_Q
  D_latch d_latch_12 (.EN(nPCLK), .D(undriven_14), .Q(d_latch_12_q));  // open: NOT_Q
  D_latch d_latch_13 (.EN(nPCLK), .D(d_latch_10_not_q), .NOT_Q(d_latch_13_not_q));  // open: Q
  Multiplexer #(.enable("false")) multiplexer_1 (
    .in0(undriven_15), .in1(undriven), .out(multiplexer_1_out), .sel(nand_2_out));
  Multiplexer #(.enable("false")) multiplexer_2 (
    .in0(undriven_10), .in1(undriven_2), .out(multiplexer_2_out), .sel(nand_2_out));
  Multiplexer #(.enable("false")) multiplexer_3 (
    .in0(undriven_11), .in1(undriven_3), .out(multiplexer_3_out), .sel(nand_2_out));
  Multiplexer #(.enable("false")) multiplexer_4 (
    .in0(undriven_12), .in1(undriven_4), .out(multiplexer_4_out), .sel(nand_2_out));
  Multiplexer #(.enable("false")) multiplexer_5 (
    .in0(undriven_13), .in1(undriven_5), .out(multiplexer_5_out), .sel(nand_2_out));
  and _27 (_27_out, nand_4_out, d_latch_11_q);
  and _14 (_14_out, d_latch_12_q, nor_8_out);
  not not_7 (not_7_out, not_6_out);
  D_latch d_latch_14 (.EN(PCLK), .D(d_latch_13_not_q), .Q(d_latch_14_q));  // open: NOT_Q
  not not_8 (nOAM0, multiplexer_1_out);
  not not_9 (nOAM1, multiplexer_2_out);
  not not_10 (nOAM2, multiplexer_3_out);
  not not_11 (nOAM3, multiplexer_4_out);
  not not_12 (nOAM4, multiplexer_5_out);
  not not_13 (nOAM5, undriven_6);
  not not_14 (nOAM6, undriven_7);
  not not_15 (nOAM7, undriven_8);
  not not_16 (nOAM8, nand_2_out);
  nor nor_14 (SPR_OV, I_OAM2, nor_15_out);
  nor nor_15 (nor_15_out, SPR_OV, _27_out, nor_11_out);
  nor nor_16 (nor_16_out, _14_out, OAMCTR2);
  nor nor_17 (OAMCTR2, nor_16_out, nor_7_out);
  nor _10 (_10_out, d_latch_14_q, d_latch_10_not_q);
  Multiplexer multiplexer_6 (.in0(1'b0), .in1(1'b1), .out(DB5_2), .sel(nor_13_out), .en(not_7_out));

  // Notes on the sheet:
  //   1
  //   6
  //   9
  //   8
  //   25
  //   10
  //   17
  //   20
  //   W3'
  //   4
  //   3
  //   4
  //   1
  //   2
  //   10
  //   21
  //   4
  //   2
  //   /R2'
  //   OAP
  //   8
  //   ORES
  //   7
  //   5
  //   3
  //   24
  //   !!! NOR PAL
  //   OMSTEP
  //   FF1
  //   5
  //   6
  //   FF2
  //   OMV
  //   OMV
  //   TMV
  //   13
  //   1
  //   W3 ENABLER
  //   9
  //   7
  //   Sprite overflow flag
  //   3
  //   2
  //   OMV'
  //   TMV'
  //   3
  //   4
  //   1
  //   2
  //   ASAP
  //   MILF
  //   TRI-STATE
endmodule

module OAM_COUNTER (
  input  POLY,
  input  STEP,
  input  LOAD,
  input  D0,
  input  RES,
  input  D1,
  input  D2,
  input  D3,
  input  D4,
  input  D5,
  input  D6,
  input  D7,
  output out0,
  output out1,
  output out2,
  output out3,
  output out4,
  output out5,
  output out6,
  output COUT,
  output out7
);

  wire _4_out, _5_out, _7_2_out, _7_out, _8_2_out, _8_out, _9_2_out, _9_out, _10_2_out, _10_out, _11_2_out,
       _11_out, controlled_buffer_1_out, controlled_buffer_2_out, controlled_buffer_3_out,
       controlled_buffer_4_out, controlled_buffer_5_out, controlled_buffer_6_out, controlled_buffer_7_out,
       controlled_buffer_8_out, d_latch_1_q, d_latch_2_q, d_latch_3_not_q, d_latch_4_not_q, d_latch_5_not_q,
       d_latch_6_not_q, d_latch_7_not_q, d_latch_8_not_q, d_latch_9_not_q, d_latch_10_not_q,
       d_latch_11_not_q, d_latch_12_not_q, d_latch_13_not_q, d_latch_14_not_q, d_latch_15_not_q,
       d_latch_16_not_q, multiplexer_1_out, multiplexer_2_out, multiplexer_3_out, multiplexer_4_out,
       multiplexer_5_out, multiplexer_6_out, multiplexer_7_out, multiplexer_8_out, nor_1_out, nor_2_out,
       nor_3_out, nor_4_out, nor_5_out, nor_6_out, nor_7_out, nor_8_out, nor_9_out, nor_10_out, nor_11_out,
       nor_12_out, nor_13_out, nor_14_out, nor_15_out, nor_16_out, nor_17_out, nor_18_out, not_1_out,
       not_2_out, not_3_out, not_4_out, not_5_out, not_6_out, not_7_out, not_8_out, not_9_out, not_10_out;

  nor nor_1 (nor_1_out, LOAD, STEP);
  nor nor_2 (nor_2_out, RES, d_latch_9_not_q);
  nor nor_3 (nor_3_out, RES, d_latch_10_not_q);
  nor nor_4 (nor_4_out, RES, d_latch_11_not_q);
  nor nor_5 (nor_5_out, RES, d_latch_12_not_q);
  nor nor_6 (nor_6_out, RES, d_latch_13_not_q);
  nor nor_7 (nor_7_out, RES, d_latch_14_not_q);
  nor nor_8 (nor_8_out, RES, d_latch_15_not_q);
  nor nor_9 (nor_9_out, RES, d_latch_16_not_q);
  Multiplexer #(.enable("false")) multiplexer_1 (
    .in0(d_latch_9_not_q), .in1(nor_2_out), .out(multiplexer_1_out), .sel(1'b1));
  assign controlled_buffer_1_out = nor_1_out ? nor_2_out : 1'bz;  // Controlled_Buffer controlled_buffer_1
  Multiplexer #(.enable("false")) multiplexer_2 (
    .in0(d_latch_10_not_q), .in1(nor_3_out), .out(multiplexer_2_out), .sel(nor_12_out));
  assign controlled_buffer_2_out = nor_1_out ? nor_3_out : 1'bz;  // Controlled_Buffer controlled_buffer_2
  Multiplexer #(.enable("false")) multiplexer_3 (
    .in0(d_latch_11_not_q), .in1(nor_4_out), .out(multiplexer_3_out), .sel(_5_out));
  assign controlled_buffer_3_out = nor_1_out ? nor_4_out : 1'bz;  // Controlled_Buffer controlled_buffer_3
  Multiplexer #(.enable("false")) multiplexer_4 (
    .in0(d_latch_12_not_q), .in1(nor_5_out), .out(multiplexer_4_out), .sel(_7_2_out));
  assign controlled_buffer_4_out = nor_1_out ? nor_5_out : 1'bz;  // Controlled_Buffer controlled_buffer_4
  Multiplexer #(.enable("false")) multiplexer_5 (
    .in0(d_latch_13_not_q), .in1(nor_6_out), .out(multiplexer_5_out), .sel(_8_2_out));
  assign controlled_buffer_5_out = nor_1_out ? nor_6_out : 1'bz;  // Controlled_Buffer controlled_buffer_5
  Multiplexer #(.enable("false")) multiplexer_6 (
    .in0(d_latch_14_not_q), .in1(nor_7_out), .out(multiplexer_6_out), .sel(_9_2_out));
  assign controlled_buffer_6_out = nor_1_out ? nor_7_out : 1'bz;  // Controlled_Buffer controlled_buffer_6
  Multiplexer #(.enable("false")) multiplexer_7 (
    .in0(d_latch_15_not_q), .in1(nor_8_out), .out(multiplexer_7_out), .sel(_10_2_out));
  assign controlled_buffer_7_out = nor_1_out ? nor_8_out : 1'bz;  // Controlled_Buffer controlled_buffer_7
  Multiplexer #(.enable("false")) multiplexer_8 (
    .in0(d_latch_16_not_q), .in1(nor_9_out), .out(multiplexer_8_out), .sel(_11_2_out));
  assign controlled_buffer_8_out = nor_1_out ? nor_9_out : 1'bz;  // Controlled_Buffer controlled_buffer_8
  D_latch d_latch_1 (.EN(nor_1_out), .D(multiplexer_1_out), .Q(d_latch_1_q));  // open: NOT_Q
  D_latch d_latch_2 (.EN(nor_1_out), .D(multiplexer_2_out), .Q(d_latch_2_q));  // open: NOT_Q
  D_latch d_latch_3 (.EN(nor_1_out), .D(multiplexer_3_out), .NOT_Q(d_latch_3_not_q));  // open: Q
  D_latch d_latch_4 (.EN(nor_1_out), .D(multiplexer_4_out), .NOT_Q(d_latch_4_not_q));  // open: Q
  D_latch d_latch_5 (.EN(nor_1_out), .D(multiplexer_5_out), .NOT_Q(d_latch_5_not_q));  // open: Q
  D_latch d_latch_6 (.EN(nor_1_out), .D(multiplexer_6_out), .NOT_Q(d_latch_6_not_q));  // open: Q
  D_latch d_latch_7 (.EN(nor_1_out), .D(multiplexer_7_out), .NOT_Q(d_latch_7_not_q));  // open: Q
  D_latch d_latch_8 (.EN(nor_1_out), .D(multiplexer_8_out), .NOT_Q(d_latch_8_not_q));  // open: Q
  assign controlled_buffer_1_out = LOAD ? D0 : 1'bz;  // Controlled_Buffer controlled_buffer_9
  nor nor_10 (nor_10_out, d_latch_1_q, POLY);
  assign controlled_buffer_2_out = LOAD ? D1 : 1'bz;  // Controlled_Buffer controlled_buffer_10
  nor nor_11 (nor_11_out, d_latch_2_q, POLY);
  assign controlled_buffer_3_out = LOAD ? D2 : 1'bz;  // Controlled_Buffer controlled_buffer_11
  assign controlled_buffer_4_out = LOAD ? D3 : 1'bz;  // Controlled_Buffer controlled_buffer_12
  assign controlled_buffer_5_out = LOAD ? D4 : 1'bz;  // Controlled_Buffer controlled_buffer_13
  assign controlled_buffer_6_out = LOAD ? D5 : 1'bz;  // Controlled_Buffer controlled_buffer_14
  assign controlled_buffer_7_out = LOAD ? D6 : 1'bz;  // Controlled_Buffer controlled_buffer_15
  assign controlled_buffer_8_out = LOAD ? D7 : 1'bz;  // Controlled_Buffer controlled_buffer_16
  assign controlled_buffer_1_out = STEP ? nor_10_out : 1'bz;  // Controlled_Buffer controlled_buffer_17
  assign controlled_buffer_2_out = STEP ? nor_11_out : 1'bz;  // Controlled_Buffer controlled_buffer_18
  assign controlled_buffer_3_out = STEP ? d_latch_3_not_q : 1'bz;  // Controlled_Buffer controlled_buffer_19
  assign controlled_buffer_4_out = STEP ? d_latch_4_not_q : 1'bz;  // Controlled_Buffer controlled_buffer_20
  assign controlled_buffer_5_out = STEP ? d_latch_5_not_q : 1'bz;  // Controlled_Buffer controlled_buffer_21
  assign controlled_buffer_6_out = STEP ? d_latch_6_not_q : 1'bz;  // Controlled_Buffer controlled_buffer_22
  assign controlled_buffer_7_out = STEP ? d_latch_7_not_q : 1'bz;  // Controlled_Buffer controlled_buffer_23
  assign controlled_buffer_8_out = STEP ? d_latch_8_not_q : 1'bz;  // Controlled_Buffer controlled_buffer_24
  not not_1 (not_1_out, POLY);
  D_latch d_latch_9 (.EN(1'b1), .D(controlled_buffer_1_out), .Q(out0), .NOT_Q(d_latch_9_not_q));
  D_latch d_latch_10 (.EN(1'b1), .D(controlled_buffer_2_out), .Q(out1), .NOT_Q(d_latch_10_not_q));
  D_latch d_latch_11 (.EN(1'b1), .D(controlled_buffer_3_out), .Q(out2), .NOT_Q(d_latch_11_not_q));
  D_latch d_latch_12 (.EN(1'b1), .D(controlled_buffer_4_out), .Q(out3), .NOT_Q(d_latch_12_not_q));
  D_latch d_latch_13 (.EN(1'b1), .D(controlled_buffer_5_out), .Q(out4), .NOT_Q(d_latch_13_not_q));
  D_latch d_latch_14 (.EN(1'b1), .D(controlled_buffer_6_out), .Q(out5), .NOT_Q(d_latch_14_not_q));
  D_latch d_latch_15 (.EN(1'b1), .D(controlled_buffer_7_out), .Q(out6), .NOT_Q(d_latch_15_not_q));
  D_latch d_latch_16 (.EN(1'b1), .D(controlled_buffer_8_out), .Q(out7), .NOT_Q(d_latch_16_not_q));
  nor _4 (_4_out, d_latch_9_not_q, d_latch_10_not_q);
  and _7 (_7_out, not_1_out, d_latch_10_not_q);
  and _8 (_8_out, not_1_out, d_latch_10_not_q);
  and _9 (_9_out, not_1_out, d_latch_10_not_q);
  and _10 (_10_out, not_1_out, d_latch_10_not_q);
  and _11 (_11_out, d_latch_10_not_q, not_1_out);
  not not_2 (not_2_out, 1'b1);
  not not_3 (not_3_out, nor_12_out);
  not not_4 (not_4_out, _4_out);
  not not_5 (not_5_out, _5_out);
  not not_6 (not_6_out, _7_2_out);
  not not_7 (not_7_out, _8_2_out);
  not not_8 (not_8_out, _9_2_out);
  not not_9 (not_9_out, _10_2_out);
  not not_10 (not_10_out, _11_2_out);
  nor nor_12 (nor_12_out, not_2_out, d_latch_9_not_q);
  nor nor_13 (nor_13_out, not_3_out, d_latch_10_not_q);
  nand _5 (_5_out, not_1_out, not_4_out);
  nor nor_14 (nor_14_out, not_5_out, d_latch_11_not_q);
  nor _7_2 (_7_2_out, _7_out, d_latch_11_not_q);
  nor nor_15 (nor_15_out, not_6_out, d_latch_12_not_q);
  nor _8_2 (_8_2_out, _8_out, d_latch_11_not_q, d_latch_12_not_q);
  nor nor_16 (nor_16_out, not_7_out, d_latch_13_not_q);
  nor _9_2 (_9_2_out, _9_out, d_latch_11_not_q, d_latch_12_not_q, d_latch_13_not_q);
  nor nor_17 (nor_17_out, not_8_out, d_latch_14_not_q);
  nor _10_2 (_10_2_out, _10_out, d_latch_11_not_q, d_latch_12_not_q, d_latch_13_not_q, d_latch_14_not_q);
  nor nor_18 (nor_18_out, not_9_out, d_latch_15_not_q);
  nor _11_2 (_11_2_out, _11_out, d_latch_11_not_q, d_latch_12_not_q, d_latch_13_not_q, d_latch_14_not_q, d_latch_15_not_q);
  nor nor_19 (COUT, not_10_out, d_latch_16_not_q);

  // Notes on the sheet:
  //   3
  //   6
  //   not used
  //   not used
  //   not used
  //   not used
  //   not used
  //   not used
endmodule

module OAM2_COUNTER (
  input  OSTEP,
  input  nPCLK,
  input  ORES,
  output nQ0,
  output nQ1,
  output nQ2,
  output nQ3,
  output nQ4,
  output CARRY_OUT
);

  wire [4:0] counter_1_q;

  Counter #(.width(5), .max('h1f), .ongoal("stay")) counter_1 (
    .count(OSTEP), .Q(counter_1_q), .carry(CARRY_OUT), .clk(nPCLK), .clr(ORES));  // open: load, D
  assign {nQ4, nQ3, nQ2, nQ1, nQ0} = ~counter_1_q;  // NOT_Gate not_1, 5 bits wide
endmodule

module OAM_BUF_CONTROL (
  input  PCLK,
  input  BLNK,
  input  SPR_OV,
  input  nVIS,
  input  OAMCTR2,
  input  H0_prime_prime,
  input  nW4,
  input  nDBE,
  output DB_OB,
  output nOE,
  output OFETCH
);

  wire _1_out, _4_out, _6_out, _8_out, _9_out, d_ff_1_qn, d_latch_1_not_q, d_latch_2_not_q, d_latch_3_not_q,
       d_latch_4_q, not_1_out, not_2_out;

  not not_1 (not_1_out, H0_prime_prime);
  not not_2 (not_2_out, PCLK);
  nor _1 (_1_out, nW4, nDBE);
  nor _7 (DB_OB, not_2_out, BLNK);
  nor _4 (_4_out, BLNK, PCLK, SPR_OV, nVIS, OAMCTR2, not_1_out);
  nor _8 (_8_out, _1_out, _9_out);
  nor _9 (_9_out, _8_out, d_latch_3_not_q);
  nor _6 (_6_out, _1_out, _8_out);
  D_Flip_Flop #(.trigger("low")) d_ff_1 (.clk(PCLK), .D(_6_out), .Qn(d_ff_1_qn));  // open: Q, preset, en, reset
  D_latch d_latch_1 (.EN(not_2_out), .D(d_ff_1_qn), .NOT_Q(d_latch_1_not_q));  // open: Q
  D_latch d_latch_2 (.EN(PCLK), .D(d_latch_1_not_q), .NOT_Q(d_latch_2_not_q));  // open: Q
  D_latch d_latch_3 (.EN(not_2_out), .D(d_latch_2_not_q), .NOT_Q(d_latch_3_not_q));  // open: Q
  D_latch d_latch_4 (.EN(PCLK), .D(d_latch_3_not_q), .Q(d_latch_4_q));  // open: NOT_Q
  nor _10 (OFETCH, d_latch_4_q, d_latch_2_not_q);
  nor _3 (nOE, _4_out, OFETCH);

  // Notes on the sheet:
  //   5
  //   FF1
  //   FF2
  //   1
  //   2
  //   3
  //   4
endmodule

module OAM_BUFFER_BIT (
  input  PCLK,
  input  nR4,
  input  I_OAM2,
  input  DB___OB,
  input  DB_OB,
  input  nOE,
  output OB___DB,
  output OB,
  output OR,
  output OW
);

  wire _7_out, _8_out, _12_out, d_latch_1_not_q, multiplexer_1_out, multiplexer_2_out, not_2_out, not_3_out,
       not_4_out, not_5_out;

  nor _8 (_8_out, I_OAM2, _7_out);
  Multiplexer #(.enable("false")) multiplexer_1 (.in0(_8_out), .in1(not_2_out), .out(multiplexer_1_out), .sel(PCLK));
  not not_1 (OB, multiplexer_1_out);
  not not_2 (not_2_out, OB);
  D_latch d_latch_1 (.EN(PCLK), .D(OB), .NOT_Q(d_latch_1_not_q));  // open: Q
  Multiplexer #(.enable("false")) multiplexer_2 (.in0(DB___OB), .in1(OB), .out(multiplexer_2_out), .sel(DB_OB));
  not not_3 (not_3_out, nR4);
  not not_4 (not_4_out, multiplexer_2_out);
  not not_5 (not_5_out, nOE);
  Multiplexer multiplexer_3 (.in0(1'b1), .in1(1'b0), .out(OB___DB), .sel(d_latch_1_not_q), .en(not_3_out));
  Multiplexer multiplexer_4 (.in0(1'b0), .in1(1'b1), .out(OR), .sel(not_4_out), .en(not_5_out));
  Multiplexer multiplexer_5 (.in0(1'b1), .in1(1'b0), .out(OW), .sel(not_4_out), .en(not_5_out));
  nor _12 (_12_out, OW, _7_out);
  nor _7 (_7_out, _12_out, OR);
  assign OR = PCLK ? 1'b1 : 1'bz;  // Controlled_Buffer controlled_buffer_1
  assign OW = PCLK ? 1'b1 : 1'bz;  // Controlled_Buffer controlled_buffer_2
  assign _7_out = PCLK ? _12_out : 1'bz;  // Controlled_Buffer controlled_buffer_3

  // Notes on the sheet:
  //   1
  //   1011
  //   9
  //   4
endmodule

module OAM_FIFO (
  input  PCLK,
  input  _0_HPOS,
  input  H3_prime_prime,
  input  H4_prime_prime,
  input  H5_prime_prime,
  input  nSH2,
  input  nSH3,
  input  nSH5,
  input  nSH7,
  input  nVIS,
  input  CLPO,
  input  OB0,
  input  OB1,
  input  OB2,
  input  OB3,
  input  OB4,
  input  OB5,
  input  OB6,
  input  OB7,
  input  T0,
  input  T1,
  input  T2,
  input  T3,
  input  T4,
  input  T5,
  input  T6,
  input  T7,
  output nSPR0HIT,
  output nZCOL0,
  output nZCOL1,
  output nZCOL2,
  output nZCOL3,
  output nZPRIO
);

  wire _0_H, and_1_out, and_2_out, and_3_out, and_4_out, and_5_out, and_6_out, and_7_out, and_8_out,
       d_latch_1_not_q, d_latch_2_not_q, nH3_prime_prime, nH4_prime_prime, nH5_prime_prime, nor_1_out,
       nor_2_out, nor_3_out, nor_4_out, nor_5_out, nor_6_out, nor_7_out, nor_8_out, nor_9_out, nor_10_out,
       nor_11_out, nor_12_out, nor_13_out, nor_14_out, nor_15_out, nor_16_out, nor_17_out, not_1_out,
       undriven, undriven_2, undriven_3, undriven_4, undriven_5, undriven_6, undriven_7, undriven_8,
       undriven_9, undriven_10, undriven_11, undriven_12, undriven_13, undriven_14, undriven_15, undriven_16,
       undriven_17, undriven_18, undriven_19, undriven_20, undriven_21, undriven_22, undriven_23,
       undriven_24, undriven_25, undriven_26, undriven_27, undriven_28, undriven_29, undriven_30,
       undriven_31, undriven_32, undriven_33, undriven_34, undriven_35, undriven_36, undriven_37,
       undriven_38, undriven_39, undriven_40, undriven_41, undriven_42, undriven_43, undriven_44,
       undriven_45, undriven_46, undriven_47, undriven_48;

  not not_1 (not_1_out, PCLK);
  not not_2 (nH3_prime_prime, H3_prime_prime);
  not not_3 (nH4_prime_prime, H4_prime_prime);
  not not_4 (nH5_prime_prime, H5_prime_prime);
  D_latch d_latch_1 (.EN(not_1_out), .D(_0_HPOS), .NOT_Q(d_latch_1_not_q));  // open: Q
  D_latch d_latch_2 (.EN(PCLK), .D(d_latch_1_not_q), .NOT_Q(d_latch_2_not_q));  // open: Q
  D_latch d_latch_3 (.EN(not_1_out), .D(d_latch_2_not_q), .NOT_Q(_0_H));  // open: Q
  nor nor_1 (nor_1_out, H3_prime_prime, H4_prime_prime, H5_prime_prime);
  nor nor_2 (nor_2_out, nH3_prime_prime, H4_prime_prime, H5_prime_prime);
  nor nor_3 (nor_3_out, H3_prime_prime, nH4_prime_prime, H5_prime_prime);
  nor nor_4 (nor_4_out, nH3_prime_prime, nH4_prime_prime, H5_prime_prime);
  nor nor_5 (nor_5_out, H3_prime_prime, H4_prime_prime, nH5_prime_prime);
  nor nor_6 (nor_6_out, nH3_prime_prime, H4_prime_prime, nH5_prime_prime);
  nor nor_7 (nor_7_out, H3_prime_prime, nH4_prime_prime, nH5_prime_prime);
  nor nor_8 (nor_8_out, nH3_prime_prime, nH4_prime_prime, nH5_prime_prime);
  and and_1 (and_1_out, undriven, undriven_2);
  and and_2 (and_2_out, undriven_6, undriven_7);
  and and_3 (and_3_out, undriven_12, undriven_13);
  and and_4 (and_4_out, undriven_18, undriven_48);
  and and_5 (and_5_out, undriven_23, undriven_24);
  and and_6 (and_6_out, undriven_28, undriven_29);
  and and_7 (and_7_out, undriven_34, undriven_35);
  and and_8 (and_8_out, undriven_39, undriven_40);
  nor nor_9 (nor_9_out, CLPO, undriven_44, and_1_out);
  nor nor_10 (nor_10_out, nor_9_out, CLPO, undriven_45, and_2_out);
  nor nor_11 (nor_11_out, nor_10_out, nor_9_out, CLPO, undriven_11, and_3_out);
  nor nor_12 (nor_12_out, nor_11_out, nor_10_out, nor_9_out, CLPO, undriven_17, and_4_out);
  nor nor_13 (nor_13_out, nor_12_out, nor_11_out, nor_10_out, nor_9_out, CLPO, undriven_22, and_5_out);
  nor nor_14 (nor_14_out, nor_13_out, nor_12_out, nor_11_out, nor_10_out, nor_9_out, CLPO, undriven_46, and_6_out);
  nor nor_15 (nor_15_out, nor_14_out, nor_13_out, nor_12_out, nor_11_out, nor_10_out, nor_9_out, CLPO, undriven_33, and_7_out);
  nor nor_16 (nor_16_out, nor_15_out, nor_14_out, nor_13_out, nor_12_out, nor_11_out, nor_10_out, nor_9_out, CLPO, undriven_47, and_8_out);
  nor nor_17 (nor_17_out, nor_16_out, nor_15_out, nor_14_out, nor_13_out, nor_12_out, nor_11_out, nor_10_out, nor_9_out);
  D_latch d_latch_4 (.EN(PCLK), .D(nor_9_out), .NOT_Q(nSPR0HIT));  // open: Q
  assign nZCOL0 = nor_9_out ? undriven : 1'bz;  // Controlled_Buffer controlled_buffer_1
  assign nZCOL1 = nor_9_out ? undriven_2 : 1'bz;  // Controlled_Buffer controlled_buffer_2
  assign nZCOL2 = nor_9_out ? undriven_3 : 1'bz;  // Controlled_Buffer controlled_buffer_3
  assign nZCOL3 = nor_9_out ? undriven_4 : 1'bz;  // Controlled_Buffer controlled_buffer_4
  assign nZPRIO = nor_9_out ? undriven_5 : 1'bz;  // Controlled_Buffer controlled_buffer_5
  assign nZCOL0 = nor_10_out ? undriven_6 : 1'bz;  // Controlled_Buffer controlled_buffer_6
  assign nZCOL1 = nor_10_out ? undriven_7 : 1'bz;  // Controlled_Buffer controlled_buffer_7
  assign nZCOL2 = nor_10_out ? undriven_8 : 1'bz;  // Controlled_Buffer controlled_buffer_8
  assign nZCOL3 = nor_10_out ? undriven_9 : 1'bz;  // Controlled_Buffer controlled_buffer_9
  assign nZPRIO = nor_10_out ? undriven_10 : 1'bz;  // Controlled_Buffer controlled_buffer_10
  assign nZCOL0 = nor_11_out ? undriven_12 : 1'bz;  // Controlled_Buffer controlled_buffer_11
  assign nZCOL1 = nor_11_out ? undriven_13 : 1'bz;  // Controlled_Buffer controlled_buffer_12
  assign nZCOL2 = nor_11_out ? undriven_14 : 1'bz;  // Controlled_Buffer controlled_buffer_13
  assign nZCOL3 = nor_11_out ? undriven_15 : 1'bz;  // Controlled_Buffer controlled_buffer_14
  assign nZPRIO = nor_11_out ? undriven_16 : 1'bz;  // Controlled_Buffer controlled_buffer_15
  assign nZCOL0 = nor_12_out ? undriven_18 : 1'bz;  // Controlled_Buffer controlled_buffer_16
  assign nZCOL1 = nor_12_out ? undriven_48 : 1'bz;  // Controlled_Buffer controlled_buffer_17
  assign nZCOL2 = nor_12_out ? undriven_19 : 1'bz;  // Controlled_Buffer controlled_buffer_18
  assign nZCOL3 = nor_12_out ? undriven_20 : 1'bz;  // Controlled_Buffer controlled_buffer_19
  assign nZPRIO = nor_12_out ? undriven_21 : 1'bz;  // Controlled_Buffer controlled_buffer_20
  assign nZCOL0 = nor_13_out ? undriven_23 : 1'bz;  // Controlled_Buffer controlled_buffer_21
  assign nZCOL1 = nor_13_out ? undriven_24 : 1'bz;  // Controlled_Buffer controlled_buffer_22
  assign nZCOL2 = nor_13_out ? undriven_25 : 1'bz;  // Controlled_Buffer controlled_buffer_23
  assign nZCOL3 = nor_13_out ? undriven_26 : 1'bz;  // Controlled_Buffer controlled_buffer_24
  assign nZPRIO = nor_13_out ? undriven_27 : 1'bz;  // Controlled_Buffer controlled_buffer_25
  assign nZCOL0 = nor_14_out ? undriven_28 : 1'bz;  // Controlled_Buffer controlled_buffer_26
  assign nZCOL1 = nor_14_out ? undriven_29 : 1'bz;  // Controlled_Buffer controlled_buffer_27
  assign nZCOL2 = nor_14_out ? undriven_30 : 1'bz;  // Controlled_Buffer controlled_buffer_28
  assign nZCOL3 = nor_14_out ? undriven_31 : 1'bz;  // Controlled_Buffer controlled_buffer_29
  assign nZPRIO = nor_14_out ? undriven_32 : 1'bz;  // Controlled_Buffer controlled_buffer_30
  assign nZCOL0 = nor_15_out ? undriven_34 : 1'bz;  // Controlled_Buffer controlled_buffer_31
  assign nZCOL1 = nor_15_out ? undriven_35 : 1'bz;  // Controlled_Buffer controlled_buffer_32
  assign nZCOL2 = nor_15_out ? undriven_36 : 1'bz;  // Controlled_Buffer controlled_buffer_33
  assign nZCOL3 = nor_15_out ? undriven_37 : 1'bz;  // Controlled_Buffer controlled_buffer_34
  assign nZPRIO = nor_15_out ? undriven_38 : 1'bz;  // Controlled_Buffer controlled_buffer_35
  assign nZCOL0 = nor_16_out ? undriven_39 : 1'bz;  // Controlled_Buffer controlled_buffer_36
  assign nZCOL1 = nor_16_out ? undriven_40 : 1'bz;  // Controlled_Buffer controlled_buffer_37
  assign nZCOL2 = nor_16_out ? undriven_41 : 1'bz;  // Controlled_Buffer controlled_buffer_38
  assign nZCOL3 = nor_16_out ? undriven_42 : 1'bz;  // Controlled_Buffer controlled_buffer_39
  assign nZPRIO = nor_16_out ? undriven_43 : 1'bz;  // Controlled_Buffer controlled_buffer_40
  assign nZCOL0 = nor_17_out ? 1'b1 : 1'bz;  // Controlled_Buffer controlled_buffer_41
  assign nZCOL1 = nor_17_out ? 1'b1 : 1'bz;  // Controlled_Buffer controlled_buffer_42

  // Other names for the same wires on the sheet: OBJ_BUS[7:0] = {OB7, OB6, OB5, OB4, OB3, OB2, OB1, OB0};
  //   T_BUS[7:0] = {T7, T6, T5, T4, T3, T2, T1, T0}
endmodule

module OAM_FIFO_PIPELINE (
  input  T0,
  input  T1,
  input  T2,
  input  T3,
  input  T4,
  input  T5,
  input  T6,
  input  T7,
  input  PCLK,
  input  nSH5,
  input  SEL,
  input  nSH7,
  input  nSH3,
  input  nSH2,
  input  _0_H,
  input  nVIS,
  input  OB0,
  input  OB1,
  input  OB2,
  input  OB3,
  input  OB4,
  input  OB5,
  input  OB6,
  input  OB7,
  output X_COL0,
  output X_COL1,
  output X_EN,
  output X_COL2,
  output X_COL3,
  output X_PRIO
);

  wire d_latch_1_not_q, d_latch_2_not_q, d_latch_3_not_q, d_latch_4_not_q, nor_1_out, nor_2_out, nor_3_out,
       nor_4_out, nor_5_out, not_1_out;

  nor nor_1 (nor_1_out, not_1_out, d_latch_1_not_q, nSH3);
  not not_1 (not_1_out, PCLK);
  D_latch d_latch_1 (.EN(not_1_out), .D(SEL), .NOT_Q(d_latch_1_not_q));  // open: Q
  nor nor_2 (nor_2_out, not_1_out, nSH5, d_latch_1_not_q);
  nor nor_3 (nor_3_out, not_1_out, d_latch_1_not_q, nSH7);
  nor nor_4 (nor_4_out, d_latch_1_not_q, not_1_out, nSH2);
  D_latch d_latch_2 (.EN(nor_4_out), .D(OB0), .NOT_Q(d_latch_2_not_q));  // open: Q
  D_latch d_latch_3 (.EN(nor_4_out), .D(OB1), .NOT_Q(d_latch_3_not_q));  // open: Q
  D_latch d_latch_4 (.EN(nor_4_out), .D(OB5), .NOT_Q(d_latch_4_not_q));  // open: Q
  nor nor_5 (nor_5_out, not_1_out, X_EN);
  D_latch d_latch_5 (.EN(not_1_out), .D(d_latch_2_not_q), .NOT_Q(X_COL2));  // open: Q
  D_latch d_latch_6 (.EN(not_1_out), .D(d_latch_3_not_q), .NOT_Q(X_COL3));  // open: Q
  D_latch d_latch_7 (.EN(not_1_out), .D(d_latch_4_not_q), .NOT_Q(X_PRIO));  // open: Q

  // Notes on the sheet:
  //   LOAD
  //   /PCLK
  //   LDAT
  //   T/SR0
  //   T/SR1
  //   /PCLK
  //   EN
endmodule

module OAM_FIFO_COUNTER (
  input  PCLK,
  input  nVIS,
  input  _0_H,
  input  LOAD,
  input  IN0,
  input  IN1,
  input  IN2,
  input  IN3,
  input  IN4,
  input  IN5,
  input  IN6,
  input  IN7,
  output X_EN
);

  wire and_1_out, controlled_inverter_1_out, controlled_inverter_2_out, controlled_inverter_3_out,
       controlled_inverter_4_out, controlled_inverter_5_out, controlled_inverter_6_out,
       controlled_inverter_7_out, controlled_inverter_8_out, d_latch_1_not_q, d_latch_2_not_q,
       d_latch_3_not_q, d_latch_4_not_q, d_latch_5_not_q, d_latch_6_not_q, d_latch_7_not_q, d_latch_8_not_q,
       d_latch_10_not_q, d_latch_10_q, d_latch_11_not_q, d_latch_11_q, d_latch_12_not_q, d_latch_12_q,
       d_latch_13_not_q, d_latch_13_q, d_latch_14_not_q, d_latch_14_q, d_latch_15_not_q, d_latch_15_q,
       d_latch_16_not_q, d_latch_16_q, d_latch_17_not_q, d_latch_17_q, nor_1_out, nor_2_out, nor_3_out,
       nor_4_out, nor_5_out, nor_6_out, nor_7_out, nor_8_out, nor_9_out, nor_10_out, nor_11_out, nor_12_out,
       nor_13_out, not_1_out, not_2_out, not_3_out, not_4_out, not_5_out, not_6_out, not_7_out, not_8_out,
       not_9_out, s_r_ff_1_q, s_r_ff_1_qn, xor_1_out, xor_2_out, xor_3_out, xor_4_out, xor_5_out, xor_6_out,
       xor_7_out, xor_8_out;

  nor nor_1 (nor_1_out, not_1_out, _0_H, nor_13_out);
  not not_1 (not_1_out, PCLK);
  and and_1 (and_1_out, PCLK, nor_13_out);
  xor xor_1 (xor_1_out, 1'b1, d_latch_10_not_q);
  xor xor_2 (xor_2_out, nor_6_out, d_latch_11_not_q);
  xor xor_3 (xor_3_out, nor_7_out, d_latch_12_not_q);
  xor xor_4 (xor_4_out, nor_8_out, d_latch_13_not_q);
  xor xor_5 (xor_5_out, nor_9_out, d_latch_14_not_q);
  xor xor_6 (xor_6_out, nor_5_out, d_latch_15_not_q);
  xor xor_7 (xor_7_out, nor_11_out, d_latch_16_not_q);
  xor xor_8 (xor_8_out, nor_12_out, d_latch_17_not_q);
  S_R_Flip_Flop s_r_ff_1 (
    .Q(s_r_ff_1_q), .Qn(s_r_ff_1_qn), .preset(nor_1_out), .reset(and_1_out));  // open: S, clk, R, en
  nor nor_2 (nor_2_out, nor_4_out, LOAD);
  D_latch d_latch_1 (.EN(nor_2_out), .D(xor_1_out), .NOT_Q(d_latch_1_not_q));  // open: Q
  assign controlled_inverter_1_out = nor_2_out ? ~d_latch_10_not_q : 1'bz;  // Controlled_Inverter controlled_inverter_1
  D_latch d_latch_2 (.EN(nor_2_out), .D(xor_2_out), .NOT_Q(d_latch_2_not_q));  // open: Q
  assign controlled_inverter_2_out = nor_2_out ? ~d_latch_11_not_q : 1'bz;  // Controlled_Inverter controlled_inverter_2
  D_latch d_latch_3 (.EN(nor_2_out), .D(xor_3_out), .NOT_Q(d_latch_3_not_q));  // open: Q
  assign controlled_inverter_3_out = nor_2_out ? ~d_latch_12_not_q : 1'bz;  // Controlled_Inverter controlled_inverter_3
  D_latch d_latch_4 (.EN(nor_2_out), .D(xor_4_out), .NOT_Q(d_latch_4_not_q));  // open: Q
  assign controlled_inverter_4_out = nor_2_out ? ~d_latch_13_not_q : 1'bz;  // Controlled_Inverter controlled_inverter_4
  D_latch d_latch_5 (.EN(nor_2_out), .D(xor_5_out), .NOT_Q(d_latch_5_not_q));  // open: Q
  assign controlled_inverter_5_out = nor_2_out ? ~d_latch_14_not_q : 1'bz;  // Controlled_Inverter controlled_inverter_5
  D_latch d_latch_6 (.EN(nor_2_out), .D(xor_6_out), .NOT_Q(d_latch_6_not_q));  // open: Q
  assign controlled_inverter_6_out = nor_2_out ? ~d_latch_15_not_q : 1'bz;  // Controlled_Inverter controlled_inverter_6
  D_latch d_latch_7 (.EN(nor_2_out), .D(xor_7_out), .NOT_Q(d_latch_7_not_q));  // open: Q
  assign controlled_inverter_7_out = nor_2_out ? ~d_latch_16_not_q : 1'bz;  // Controlled_Inverter controlled_inverter_7
  D_latch d_latch_8 (.EN(nor_2_out), .D(xor_8_out), .NOT_Q(d_latch_8_not_q));  // open: Q
  assign controlled_inverter_8_out = nor_2_out ? ~d_latch_17_not_q : 1'bz;  // Controlled_Inverter controlled_inverter_8
  nor nor_3 (nor_3_out, nVIS, s_r_ff_1_q);
  nor nor_4 (nor_4_out, PCLK, s_r_ff_1_qn);
  assign controlled_inverter_1_out = LOAD ? IN0 : 1'bz;  // Controlled_Buffer controlled_buffer_1
  assign controlled_inverter_1_out = nor_4_out ? d_latch_1_not_q : 1'bz;  // Controlled_Buffer controlled_buffer_2
  assign controlled_inverter_2_out = LOAD ? IN1 : 1'bz;  // Controlled_Buffer controlled_buffer_3
  assign controlled_inverter_2_out = nor_4_out ? d_latch_2_not_q : 1'bz;  // Controlled_Buffer controlled_buffer_4
  assign controlled_inverter_3_out = LOAD ? IN2 : 1'bz;  // Controlled_Buffer controlled_buffer_5
  assign controlled_inverter_3_out = nor_4_out ? d_latch_3_not_q : 1'bz;  // Controlled_Buffer controlled_buffer_6
  assign controlled_inverter_4_out = LOAD ? IN3 : 1'bz;  // Controlled_Buffer controlled_buffer_7
  assign controlled_inverter_4_out = nor_4_out ? d_latch_4_not_q : 1'bz;  // Controlled_Buffer controlled_buffer_8
  assign controlled_inverter_5_out = LOAD ? IN4 : 1'bz;  // Controlled_Buffer controlled_buffer_9
  assign controlled_inverter_5_out = nor_4_out ? d_latch_5_not_q : 1'bz;  // Controlled_Buffer controlled_buffer_10
  assign controlled_inverter_6_out = LOAD ? IN5 : 1'bz;  // Controlled_Buffer controlled_buffer_11
  assign controlled_inverter_6_out = nor_4_out ? d_latch_6_not_q : 1'bz;  // Controlled_Buffer controlled_buffer_12
  assign controlled_inverter_7_out = LOAD ? IN6 : 1'bz;  // Controlled_Buffer controlled_buffer_13
  assign controlled_inverter_7_out = nor_4_out ? d_latch_7_not_q : 1'bz;  // Controlled_Buffer controlled_buffer_14
  assign controlled_inverter_8_out = LOAD ? IN7 : 1'bz;  // Controlled_Buffer controlled_buffer_15
  assign controlled_inverter_8_out = nor_4_out ? d_latch_8_not_q : 1'bz;  // Controlled_Buffer controlled_buffer_16
  not not_2 (not_2_out, 1'b1);
  not not_3 (not_3_out, nor_6_out);
  not not_4 (not_4_out, nor_7_out);
  not not_5 (not_5_out, nor_8_out);
  not not_6 (not_6_out, nor_9_out);
  nor nor_5 (nor_5_out, d_latch_14_q, d_latch_13_q, d_latch_12_q, d_latch_11_q, d_latch_10_q);
  not not_7 (not_7_out, nor_5_out);
  not not_8 (not_8_out, nor_11_out);
  not not_9 (not_9_out, nor_12_out);
  D_latch d_latch_9 (.EN(not_1_out), .D(nor_3_out), .NOT_Q(X_EN));  // open: Q
  D_latch d_latch_10 (.EN(1'b1), .D(controlled_inverter_1_out), .Q(d_latch_10_q), .NOT_Q(d_latch_10_not_q));
  nor nor_6 (nor_6_out, d_latch_10_not_q, not_2_out);
  D_latch d_latch_11 (.EN(1'b1), .D(controlled_inverter_2_out), .Q(d_latch_11_q), .NOT_Q(d_latch_11_not_q));
  nor nor_7 (nor_7_out, d_latch_11_not_q, not_3_out);
  D_latch d_latch_12 (.EN(1'b1), .D(controlled_inverter_3_out), .Q(d_latch_12_q), .NOT_Q(d_latch_12_not_q));
  nor nor_8 (nor_8_out, d_latch_12_not_q, not_4_out);
  D_latch d_latch_13 (.EN(1'b1), .D(controlled_inverter_4_out), .Q(d_latch_13_q), .NOT_Q(d_latch_13_not_q));
  nor nor_9 (nor_9_out, d_latch_13_not_q, not_5_out);
  D_latch d_latch_14 (.EN(1'b1), .D(controlled_inverter_5_out), .Q(d_latch_14_q), .NOT_Q(d_latch_14_not_q));
  nor nor_10 (nor_10_out, d_latch_14_not_q, not_6_out);
  D_latch d_latch_15 (.EN(1'b1), .D(controlled_inverter_6_out), .Q(d_latch_15_q), .NOT_Q(d_latch_15_not_q));
  nor nor_11 (nor_11_out, d_latch_15_not_q, not_7_out);
  D_latch d_latch_16 (.EN(1'b1), .D(controlled_inverter_7_out), .Q(d_latch_16_q), .NOT_Q(d_latch_16_not_q));
  nor nor_12 (nor_12_out, d_latch_16_not_q, not_8_out);
  D_latch d_latch_17 (.EN(1'b1), .D(controlled_inverter_8_out), .Q(d_latch_17_q), .NOT_Q(d_latch_17_not_q));
  nor nor_13 (nor_13_out, d_latch_17_not_q, not_9_out);

  // Notes on the sheet:
  //   UPD
  //   STEP
  //   LOAD
  //   CARRY OUT
endmodule

module SELECT_2_3_5_7_PIXEL (
  input  PCLK,
  input  PAR_O,
  input  H0_prime_prime,
  input  H1_prime_prime,
  input  H2_prime_prime,
  output nSH2,
  output nSH3,
  output nSH5,
  output nSH7
);

  wire nor_1_out, nor_2_out, nor_3_out, nor_4_out, not_1_out, not_2_out, not_3_out, not_4_out, not_5_out;

  not not_1 (not_1_out, PCLK);
  not not_2 (not_2_out, PAR_O);
  not not_3 (not_3_out, H2_prime_prime);
  not not_4 (not_4_out, H1_prime_prime);
  not not_5 (not_5_out, H0_prime_prime);
  nor nor_1 (nor_1_out, not_2_out, H0_prime_prime, not_4_out, H2_prime_prime);
  nor nor_2 (nor_2_out, not_2_out, not_5_out, not_4_out, H2_prime_prime);
  nor nor_3 (nor_3_out, not_2_out, not_5_out, H1_prime_prime, not_3_out);
  nor nor_4 (nor_4_out, not_2_out, not_5_out, not_4_out, not_3_out);
  D_latch sh2_latch (.EN(not_1_out), .D(nor_1_out), .NOT_Q(nSH2));  // open: Q
  D_latch sh3_latch (.EN(not_1_out), .D(nor_2_out), .NOT_Q(nSH3));  // open: Q
  D_latch sh5_latch (.EN(not_1_out), .D(nor_3_out), .NOT_Q(nSH5));  // open: Q
  D_latch sh7_latch (.EN(not_1_out), .D(nor_4_out), .NOT_Q(nSH7));  // open: Q

  // Notes on the sheet:
  //   SPR Load FLAG (ATTRIBUTE)
  //   SPR Load X POSITION
  //   SPR Load Low Tile Byte
  //   SPR Load High Tile Byte
endmodule

module H_INVERSION (
  input  PCLK,
  input  nSH2,
  input  OB6,
  input  _0_FIFO,
  input  PD0,
  input  PD1,
  input  PD2,
  input  PD3,
  input  PD4,
  input  PD5,
  input  PD6,
  input  PD7,
  output T0,
  output T1,
  output T2,
  output T3,
  output T4,
  output T5,
  output T6,
  output T7
);

  wire d_ff_1_q, d_latch_1_q, d_latch_2_q, d_latch_3_q, d_latch_4_q, d_latch_5_q, d_latch_6_q, d_latch_7_q,
       d_latch_8_q, multiplexer_1_out, multiplexer_2_out, multiplexer_3_out, multiplexer_4_out,
       multiplexer_5_out, multiplexer_6_out, multiplexer_7_out, multiplexer_8_out, nor_1_out, not_1_out;

  not not_1 (not_1_out, PCLK);
  nor nor_1 (nor_1_out, not_1_out, nSH2);
  D_Flip_Flop #(.trigger("low")) d_ff_1 (.clk(nor_1_out), .D(OB6), .Q(d_ff_1_q));  // open: Qn, preset, en, reset
  Multiplexer #(.disabled(0), .enable("false")) multiplexer_1 (
    .in0(PD0), .in1(PD7), .out(multiplexer_1_out), .sel(d_ff_1_q));
  Multiplexer #(.disabled(0), .enable("false")) multiplexer_2 (
    .in0(PD1), .in1(PD6), .out(multiplexer_2_out), .sel(d_ff_1_q));
  Multiplexer #(.disabled(0), .enable("false")) multiplexer_3 (
    .in0(PD2), .in1(PD5), .out(multiplexer_3_out), .sel(d_ff_1_q));
  Multiplexer #(.disabled(0), .enable("false")) multiplexer_4 (
    .in0(PD3), .in1(PD4), .out(multiplexer_4_out), .sel(d_ff_1_q));
  Multiplexer #(.disabled(0), .enable("false")) multiplexer_5 (
    .in0(PD4), .in1(PD3), .out(multiplexer_5_out), .sel(d_ff_1_q));
  Multiplexer #(.disabled(0), .enable("false")) multiplexer_6 (
    .in0(PD5), .in1(PD2), .out(multiplexer_6_out), .sel(d_ff_1_q));
  Multiplexer #(.disabled(0), .enable("false")) multiplexer_7 (
    .in0(PD6), .in1(PD1), .out(multiplexer_7_out), .sel(d_ff_1_q));
  Multiplexer #(.disabled(0), .enable("false")) multiplexer_8 (
    .in0(PD7), .in1(PD0), .out(multiplexer_8_out), .sel(d_ff_1_q));
  D_latch d_latch_1 (.EN(not_1_out), .D(multiplexer_1_out), .Q(d_latch_1_q));  // open: NOT_Q
  D_latch d_latch_2 (.EN(not_1_out), .D(multiplexer_2_out), .Q(d_latch_2_q));  // open: NOT_Q
  D_latch d_latch_3 (.EN(not_1_out), .D(multiplexer_3_out), .Q(d_latch_3_q));  // open: NOT_Q
  D_latch d_latch_4 (.EN(not_1_out), .D(multiplexer_4_out), .Q(d_latch_4_q));  // open: NOT_Q
  D_latch d_latch_5 (.EN(not_1_out), .D(multiplexer_5_out), .Q(d_latch_5_q));  // open: NOT_Q
  D_latch d_latch_6 (.EN(not_1_out), .D(multiplexer_6_out), .Q(d_latch_6_q));  // open: NOT_Q
  D_latch d_latch_7 (.EN(not_1_out), .D(multiplexer_7_out), .Q(d_latch_7_q));  // open: NOT_Q
  D_latch d_latch_8 (.EN(not_1_out), .D(multiplexer_8_out), .Q(d_latch_8_q));  // open: NOT_Q
  nand nand_1 (T0, _0_FIFO, d_latch_1_q);
  nand nand_2 (T1, _0_FIFO, d_latch_2_q);
  nand nand_3 (T2, _0_FIFO, d_latch_3_q);
  nand nand_4 (T3, _0_FIFO, d_latch_4_q);
  nand nand_5 (T4, _0_FIFO, d_latch_5_q);
  nand nand_6 (T5, _0_FIFO, d_latch_6_q);
  nand nand_7 (T6, _0_FIFO, d_latch_7_q);
  nand nand_8 (T7, _0_FIFO, d_latch_8_q);

  // Notes on the sheet:
  //   HINV
endmodule

module VRAM_BUS_CONTROL (
  input  PCLK,
  input  nR7,
  input  nDBE,
  input  nW7,
  input  BLNK,
  input  H0_prime,
  input  nPA8,
  input  nPA9,
  input  nPA10,
  input  nPA11,
  input  nPA12,
  input  nPA13,
  output TSTEP,
  output PD_RB,
  output DB_PAR,
  output nALE,
  output RD,
  output WR,
  output XRB,
  output TH_MUX
);

  wire and_1_out, d_ff_1_q, d_ff_2_q, d_latch_1_not_q, d_latch_2_not_q, d_latch_3_not_q, d_latch_4_not_q,
       d_latch_4_q, d_latch_5_not_q, d_latch_6_not_q, d_latch_7_not_q, d_latch_7_q, d_latch_8_not_q,
       d_latch_8_q, d_latch_9_q, d_latch_10_q, d_latch_11_q, nand_1_out, nor_1_out, nor_2_out, nor_4_out,
       nor_5_out, nor_7_out, nor_9_out, nor_10_out, nor_12_out, nor_14_out, not_1_out, not_2_out, not_3_out,
       not_4_out, not_5_out, s_r_ff_1_q, s_r_ff_2_q;

  not not_1 (not_1_out, PCLK);
  nor nor_1 (nor_1_out, nR7, nDBE);
  nor nor_2 (nor_2_out, nDBE, nW7);
  nor nor_3 (TH_MUX, d_latch_1_not_q, nPA8, nPA9, nPA10, nPA11, nPA12, nPA13);
  S_R_Flip_Flop #(.trigger("high")) s_r_ff_1 (
    .Q(s_r_ff_1_q), .preset(d_latch_6_not_q), .reset(nor_1_out));  // open: S, clk, R, Qn, en
  S_R_Flip_Flop #(.trigger("high")) s_r_ff_2 (
    .Q(s_r_ff_2_q), .preset(d_latch_7_not_q), .reset(nor_2_out));  // open: S, clk, R, Qn, en
  nor nor_4 (nor_4_out, s_r_ff_1_q, nor_1_out);
  nor nor_5 (nor_5_out, s_r_ff_2_q, nor_2_out);
  D_Flip_Flop #(.trigger("low")) d_ff_1 (.clk(PCLK), .D(nor_4_out), .Q(d_ff_1_q));  // open: Qn, preset, en, reset
  D_Flip_Flop #(.trigger("low")) d_ff_2 (.clk(PCLK), .D(nor_5_out), .Q(d_ff_2_q));  // open: Qn, preset, en, reset
  D_latch d_latch_1 (.EN(PCLK), .D(BLNK), .NOT_Q(d_latch_1_not_q));  // open: Q
  D_latch d_latch_2 (.EN(not_1_out), .D(d_ff_1_q), .NOT_Q(d_latch_2_not_q));  // open: Q
  D_latch d_latch_3 (.EN(not_1_out), .D(d_ff_2_q), .NOT_Q(d_latch_3_not_q));  // open: Q
  D_latch d_latch_4 (.EN(PCLK), .D(d_latch_2_not_q), .Q(d_latch_4_q), .NOT_Q(d_latch_4_not_q));
  D_latch d_latch_5 (.EN(PCLK), .D(d_latch_3_not_q), .NOT_Q(d_latch_5_not_q));  // open: Q
  D_latch d_latch_6 (.EN(not_1_out), .D(d_latch_4_not_q), .NOT_Q(d_latch_6_not_q));  // open: Q
  D_latch d_latch_7 (.EN(not_1_out), .D(d_latch_5_not_q), .Q(d_latch_7_q), .NOT_Q(d_latch_7_not_q));
  D_latch d_latch_8 (.EN(PCLK), .D(d_latch_6_not_q), .Q(d_latch_8_q), .NOT_Q(d_latch_8_not_q));
  D_latch d_latch_9 (.EN(PCLK), .D(d_latch_7_not_q), .Q(d_latch_9_q));  // open: NOT_Q
  D_latch d_latch_10 (.EN(PCLK), .D(H0_prime), .Q(d_latch_10_q));  // open: NOT_Q
  nor nor_6 (PD_RB, d_latch_4_q, d_latch_8_not_q);
  nor nor_7 (nor_7_out, d_latch_8_q, d_latch_4_not_q);
  nor nor_8 (DB_PAR, d_latch_3_not_q, d_latch_7_q);
  nor nor_9 (nor_9_out, d_latch_9_q, d_latch_5_not_q);
  nor nor_10 (nor_10_out, not_1_out, H0_prime, BLNK);
  not not_2 (not_2_out, BLNK);
  nor nor_11 (nALE, nor_7_out, nor_9_out, nor_10_out);
  nand nand_1 (nand_1_out, not_2_out, d_latch_10_q);
  D_latch d_latch_11 (.EN(PCLK), .D(DB_PAR), .Q(d_latch_11_q));  // open: NOT_Q
  nor nor_12 (nor_12_out, d_latch_11_q, PD_RB);
  not not_3 (not_3_out, PD_RB);
  and and_1 (and_1_out, not_3_out, nand_1_out);
  not not_4 (not_4_out, DB_PAR);
  nor nor_13 (WR, not_4_out, TH_MUX);
  not not_5 (not_5_out, nor_1_out);
  nor nor_14 (nor_14_out, not_5_out, TH_MUX);
  not not_6 (TSTEP, nor_12_out);
  not not_7 (RD, and_1_out);
  not not_8 (XRB, nor_14_out);

  // Notes on the sheet:
  //   R7_EN
  //   W7_EN
  //   /PCLK
  //   /PCLK
  //   PCLK
  //   PCLK
  //   /PCLK
  //   /PCLK
  //   H0'
  //   PCLK
  //   PCLK
  //   H0'
  //   BLNK
  //   H0''
  //   PD/RB
  //   DB/PAR
  //   /ALE
endmodule

module READ__2007 (
  input  XRB,
  input  RC,
  input  PD_RB,
  input  PD0,
  input  PD1,
  input  PD2,
  input  PD3,
  input  PD4,
  input  PD5,
  input  PD6,
  input  PD7,
  output DB0,
  output DB1,
  output DB2,
  output DB3,
  output DB4,
  output DB5,
  output DB6,
  output DB7
);

  wire multiplexer_1_out, multiplexer_2_out, multiplexer_3_out, multiplexer_4_out, multiplexer_5_out,
       multiplexer_6_out, multiplexer_7_out, multiplexer_8_out, nor_1_out, nor_2_out, nor_3_out, nor_4_out,
       nor_5_out, nor_6_out, nor_7_out, nor_8_out, not_1_out, not_2_out, not_3_out, not_4_out, not_5_out,
       not_6_out, not_7_out, not_8_out, not_9_out;

  not not_1 (not_1_out, XRB);
  Multiplexer #(.enable("false")) multiplexer_1 (.in0(nor_1_out), .in1(PD0), .out(multiplexer_1_out), .sel(PD_RB));
  not not_2 (not_2_out, multiplexer_1_out);
  not not_3 (not_3_out, multiplexer_2_out);
  Multiplexer #(.enable("false")) multiplexer_2 (.in0(nor_2_out), .in1(PD1), .out(multiplexer_2_out), .sel(PD_RB));
  Multiplexer #(.enable("false")) multiplexer_3 (.in0(nor_3_out), .in1(PD2), .out(multiplexer_3_out), .sel(PD_RB));
  not not_4 (not_4_out, multiplexer_3_out);
  not not_5 (not_5_out, multiplexer_4_out);
  Multiplexer #(.enable("false")) multiplexer_4 (.in0(nor_4_out), .in1(PD3), .out(multiplexer_4_out), .sel(PD_RB));
  Multiplexer #(.enable("false")) multiplexer_5 (.in0(nor_5_out), .in1(PD4), .out(multiplexer_5_out), .sel(PD_RB));
  not not_6 (not_6_out, multiplexer_5_out);
  not not_7 (not_7_out, multiplexer_6_out);
  Multiplexer #(.enable("false")) multiplexer_6 (.in0(nor_6_out), .in1(PD5), .out(multiplexer_6_out), .sel(PD_RB));
  Multiplexer #(.enable("false")) multiplexer_7 (.in0(nor_7_out), .in1(PD6), .out(multiplexer_7_out), .sel(PD_RB));
  not not_8 (not_8_out, multiplexer_7_out);
  Multiplexer #(.enable("false")) multiplexer_8 (.in0(nor_8_out), .in1(PD7), .out(multiplexer_8_out), .sel(PD_RB));
  not not_9 (not_9_out, multiplexer_8_out);
  nor nor_1 (nor_1_out, not_2_out, RC);
  nor nor_2 (nor_2_out, not_3_out, RC);
  nor nor_3 (nor_3_out, not_4_out, RC);
  nor nor_4 (nor_4_out, not_5_out, RC);
  nor nor_5 (nor_5_out, not_6_out, RC);
  nor nor_6 (nor_6_out, not_7_out, RC);
  nor nor_7 (nor_7_out, not_8_out, RC);
  nor nor_8 (nor_8_out, not_9_out, RC);
  Multiplexer multiplexer_9 (.in0(1'b0), .in1(1'b1), .out(DB0), .sel(nor_1_out), .en(not_1_out));
  Multiplexer multiplexer_10 (.in0(1'b0), .in1(1'b1), .out(DB1), .sel(nor_2_out), .en(not_1_out));
  Multiplexer multiplexer_11 (.in0(1'b0), .in1(1'b1), .out(DB2), .sel(nor_3_out), .en(not_1_out));
  Multiplexer multiplexer_12 (.in0(1'b0), .in1(1'b1), .out(DB3), .sel(nor_4_out), .en(not_1_out));
  Multiplexer multiplexer_13 (.in0(1'b0), .in1(1'b1), .out(DB4), .sel(nor_5_out), .en(not_1_out));
  Multiplexer multiplexer_14 (.in0(1'b0), .in1(1'b1), .out(DB5), .sel(nor_6_out), .en(not_1_out));
  Multiplexer multiplexer_15 (.in0(1'b0), .in1(1'b1), .out(DB6), .sel(nor_7_out), .en(not_1_out));
  Multiplexer multiplexer_16 (.in0(1'b0), .in1(1'b1), .out(DB7), .sel(nor_8_out), .en(not_1_out));
endmodule
module PICTURE_ADDRESS_GEN (
  input  PCLK,
  input  F_AT,
  input  F_NT,
  input  PAR_O,
  input  nSH2,
  input  O8_16,
  input  OBSEL,
  input  BGSEL,
  input  H2_prime,
  input  H1_prime,
  input  SC_CNT,
  input  RESCL,
  input  E_EV,
  input  TSTEP,
  input  F_TB,
  input  H0_prime_prime,
  input  BLNK,
  input  l1_32,
  input  PD0,
  input  PD1,
  input  PD2,
  input  PD3,
  input  PD4,
  input  PD5,
  input  PD6,
  input  PD7,
  input  OB0,
  input  OB1,
  input  OB2,
  input  OB3,
  input  OB4,
  input  OB5,
  input  OB6,
  input  OB7,
  input  OV0,
  input  OV1,
  input  OV2,
  input  OV3,
  input  DB0,
  input  DB1,
  input  DB2,
  input  DB3,
  input  DB4,
  input  DB5,
  input  DB6,
  input  DB7,
  input  nW0,
  input  nW5_2,
  input  nW6_1,
  input  nW5_1,
  input  nW6_2,
  input  nDBE,
  input  RC,
  output THO0,
  output THO1,
  output THO2,
  output THO3,
  output THO4,
  output TVO1,
  output nPA0,
  output nPA1,
  output nPA2,
  output nPA3,
  output nPA4,
  output nPA5,
  output nPA6,
  output nPA7,
  output nPA8,
  output nPA9,
  output nPA10,
  output nPA11,
  output nPA12,
  output FH0,
  output nPA13,
  output FH1,
  output FH2
);

  wire _3_2_out, _3_out, _4_out, _6_out, _11_out, _14_out, _15_out, and_1_out, and_2_out,
       controlled_buffer_1_out, controlled_buffer_2_out, controlled_buffer_3_out, controlled_buffer_4_out,
       controlled_buffer_5_out, controlled_buffer_6_out, controlled_buffer_8_out, controlled_buffer_10_out,
       controlled_buffer_12_out, controlled_buffer_14_out, controlled_buffer_16_out,
       controlled_buffer_18_out, controlled_buffer_20_out, controlled_buffer_22_out,
       controlled_buffer_24_out, controlled_buffer_28_out, controlled_buffer_30_out,
       controlled_buffer_32_out, d_ff_1_qn, d_latch_1_q, d_latch_2_not_q, d_latch_3_not_q, d_latch_4_not_q,
       d_latch_5_q, d_latch_6_q, d_latch_7_q, DBE, multiplexer_1_out, multiplexer_2_out, multiplexer_3_out,
       multiplexer_4_out, multiplexer_5_out, multiplexer_6_out, multiplexer_7_out, multiplexer_8_out,
       multiplexer_9_out, multiplexer_10_out, multiplexer_11_out, multiplexer_12_out, multiplexer_13_out,
       multiplexer_14_out, multiplexer_15_out, multiplexer_16_out, multiplexer_17_out, multiplexer_18_out,
       multiplexer_19_out, multiplexer_20_out, multiplexer_21_out, multiplexer_22_out, multiplexer_23_out,
       multiplexer_24_out, multiplexer_25_out, multiplexer_26_out, multiplexer_27_out, multiplexer_28_out,
       multiplexer_29_out, multiplexer_30_out, multiplexer_31_out, multiplexer_32_out, multiplexer_33_out,
       multiplexer_34_out, multiplexer_35_out, multiplexer_36_out, multiplexer_37_out, multiplexer_38_out,
       multiplexer_39_out, multiplexer_40_out, multiplexer_41_out, multiplexer_42_out, nand_1_out, nor_1_out,
       nor_2_out, nor_8_out, nor_9_out, nor_13_out, nor_14_out, nor_15_out, nor_16_out, nor_17_out,
       nor_18_out, nor_19_out, nor_20_out, nor_21_out, nor_22_out, nor_23_out, nor_24_out, nor_25_out,
       nor_26_out, nor_27_out, nor_28_out, nor_29_out, nor_30_out, nor_31_out, nor_32_out, nor_33_out,
       nor_34_out, not_2_out, not_4_out, not_5_out, not_6_out, not_7_out, not_8_out, not_9_out, not_10_out,
       not_11_out, not_12_out, not_13_out, not_14_out, not_15_out, not_17_out, not_18_out, not_19_out,
       not_20_out, not_21_out, not_22_out, not_23_out, not_24_out, not_25_out, not_26_out, nPCLK, nW0_prime,
       nW5_1_prime, nW5_2_prime, nW6_1_prime, nW6_2_prime, s_r_ff_1_q, undriven, undriven_2, undriven_3,
       undriven_4, undriven_5, undriven_6, undriven_7, undriven_8, undriven_9, undriven_10, undriven_11,
       undriven_12, undriven_13, undriven_14, undriven_15, undriven_16, undriven_17, undriven_18,
       undriven_19, undriven_20, undriven_21, undriven_22, undriven_23, undriven_24, undriven_25,
       undriven_26, undriven_27, undriven_28;
  wire [0:0] undriven_29;

  not not_1 (nPCLK, PCLK);
  D_latch d_latch_1 (.EN(PCLK), .D(SC_CNT), .Q(d_latch_1_q));  // open: NOT_Q
  D_latch d_latch_2 (.EN(nPCLK), .D(E_EV), .NOT_Q(d_latch_2_not_q));  // open: Q
  nor nor_1 (nor_1_out, E_EV, TSTEP);
  nor nor_2 (nor_2_out, TSTEP, and_1_out);
  and and_1 (and_1_out, F_TB, H0_prime_prime);
  not not_2 (not_2_out, l1_32);
  nor nor_3 (nW0_prime, nW0, nDBE);
  nor nor_4 (nW5_2_prime, nW5_2, nDBE);
  nor nor_5 (nW6_1_prime, nW6_1, nDBE);
  nor nor_6 (nW5_1_prime, nW5_1, nDBE);
  nor nor_7 (nW6_2_prime, nW6_2, nDBE);
  not not_3 (DBE, nDBE);
  and _3 (_3_out, d_latch_1_q, RESCL);
  D_latch d_latch_3 (.EN(PCLK), .D(d_latch_2_not_q), .NOT_Q(d_latch_3_not_q));  // open: Q
  nor nor_8 (nor_8_out, nor_1_out, PCLK);
  nor nor_9 (nor_9_out, PCLK, nor_2_out);
  assign controlled_buffer_1_out = nW5_1_prime ? DB0 : 1'bz;  // Controlled_Buffer controlled_buffer_1
  assign controlled_buffer_2_out = nW5_1_prime ? DB1 : 1'bz;  // Controlled_Buffer controlled_buffer_2
  assign controlled_buffer_3_out = nW5_1_prime ? DB2 : 1'bz;  // Controlled_Buffer controlled_buffer_3
  Multiplexer #(.disabled(0), .enable("false")) multiplexer_1 (
    .in0(FH0), .in1(controlled_buffer_1_out), .out(multiplexer_1_out), .sel(DBE));
  Multiplexer #(.disabled(0), .enable("false")) multiplexer_2 (
    .in0(FH1), .in1(controlled_buffer_2_out), .out(multiplexer_2_out), .sel(DBE));
  Multiplexer #(.disabled(0), .enable("false")) multiplexer_3 (
    .in0(FH2), .in1(controlled_buffer_3_out), .out(multiplexer_3_out), .sel(DBE));
  not not_4 (not_4_out, nor_8_out);
  D_latch d_latch_4 (.EN(PCLK), .D(undriven_5), .NOT_Q(d_latch_4_not_q));  // open: Q
  nor nor_10 (FH0, RC, ~multiplexer_1_out);  // NOR_Gate
  Pull_Resistor pull_resistor_1 (.node(multiplexer_1_out));
  nor nor_11 (FH1, RC, ~multiplexer_2_out);  // NOR_Gate
  Pull_Resistor pull_resistor_2 (.node(multiplexer_2_out));
  nor nor_12 (FH2, RC, ~multiplexer_3_out);  // NOR_Gate
  Pull_Resistor pull_resistor_3 (.node(multiplexer_3_out));
  and _6 (_6_out, nPCLK, d_latch_7_q);
  D_latch d_latch_5 (.EN(nPCLK), .D(not_4_out), .Q(d_latch_5_q));  // open: NOT_Q
  D_latch d_latch_6 (.EN(nPCLK), .D(d_latch_4_not_q), .Q(d_latch_6_q));  // open: NOT_Q
  S_R_Flip_Flop s_r_ff_1 (.Q(s_r_ff_1_q), .preset(nW6_2_prime), .reset(_6_out));  // open: S, clk, R, Qn, en
  and and_2 (and_2_out, not_2_out, BLNK);
  nor nor_13 (nor_13_out, d_latch_5_q, d_latch_6_q);
  nor _11 (_11_out, s_r_ff_1_q, nW6_2_prime);
  nand nand_1 (nand_1_out, BLNK, not_2_out);
  D_Flip_Flop #(.trigger("low")) d_ff_1 (.clk(nPCLK), .D(_11_out), .Qn(d_ff_1_qn));  // open: Q, preset, en, reset
  not not_5 (not_5_out, nor_14_out);
  nor nor_14 (nor_14_out, undriven, and_2_out, undriven_2);
  assign controlled_buffer_4_out = nW0_prime ? DB0 : 1'bz;  // Controlled_Buffer controlled_buffer_4
  assign controlled_buffer_5_out = nW0_prime ? DB1 : 1'bz;  // Controlled_Buffer controlled_buffer_5
  D_latch d_latch_7 (.EN(PCLK), .D(d_ff_1_qn), .Q(d_latch_7_q));  // open: NOT_Q
  assign controlled_buffer_6_out = nW6_2_prime ? DB0 : 1'bz;  // Controlled_Buffer controlled_buffer_6
  assign controlled_buffer_6_out = nW5_1_prime ? DB3 : 1'bz;  // Controlled_Buffer controlled_buffer_7
  assign controlled_buffer_8_out = nW6_2_prime ? DB1 : 1'bz;  // Controlled_Buffer controlled_buffer_8
  assign controlled_buffer_8_out = nW5_1_prime ? DB4 : 1'bz;  // Controlled_Buffer controlled_buffer_9
  assign controlled_buffer_10_out = nW6_2_prime ? DB2 : 1'bz;  // Controlled_Buffer controlled_buffer_10
  assign controlled_buffer_10_out = nW5_1_prime ? DB5 : 1'bz;  // Controlled_Buffer controlled_buffer_11
  assign controlled_buffer_12_out = nW6_2_prime ? DB3 : 1'bz;  // Controlled_Buffer controlled_buffer_12
  assign controlled_buffer_12_out = nW5_1_prime ? DB6 : 1'bz;  // Controlled_Buffer controlled_buffer_13
  assign controlled_buffer_14_out = nW6_2_prime ? DB4 : 1'bz;  // Controlled_Buffer controlled_buffer_14
  assign controlled_buffer_14_out = nW5_1_prime ? DB7 : 1'bz;  // Controlled_Buffer controlled_buffer_15
  assign controlled_buffer_16_out = nW6_2_prime ? DB5 : 1'bz;  // Controlled_Buffer controlled_buffer_16
  assign controlled_buffer_16_out = nW5_2_prime ? DB3 : 1'bz;  // Controlled_Buffer controlled_buffer_17
  assign controlled_buffer_18_out = nW6_2_prime ? DB6 : 1'bz;  // Controlled_Buffer controlled_buffer_18
  assign controlled_buffer_18_out = nW5_2_prime ? DB4 : 1'bz;  // Controlled_Buffer controlled_buffer_19
  assign controlled_buffer_20_out = nW6_2_prime ? DB7 : 1'bz;  // Controlled_Buffer controlled_buffer_20
  assign controlled_buffer_20_out = nW5_2_prime ? DB5 : 1'bz;  // Controlled_Buffer controlled_buffer_21
  assign controlled_buffer_22_out = nW6_1_prime ? DB0 : 1'bz;  // Controlled_Buffer controlled_buffer_22
  assign controlled_buffer_22_out = nW5_2_prime ? DB6 : 1'bz;  // Controlled_Buffer controlled_buffer_23
  assign controlled_buffer_24_out = nW6_1_prime ? DB1 : 1'bz;  // Controlled_Buffer controlled_buffer_24
  assign controlled_buffer_24_out = nW5_2_prime ? DB7 : 1'bz;  // Controlled_Buffer controlled_buffer_25
  assign controlled_buffer_4_out = nW6_1_prime ? DB2 : 1'bz;  // Controlled_Buffer controlled_buffer_26
  assign controlled_buffer_5_out = nW6_1_prime ? DB3 : 1'bz;  // Controlled_Buffer controlled_buffer_27
  assign controlled_buffer_28_out = nW6_1_prime ? DB4 : 1'bz;  // Controlled_Buffer controlled_buffer_28
  assign controlled_buffer_28_out = nW5_2_prime ? DB0 : 1'bz;  // Controlled_Buffer controlled_buffer_29
  assign controlled_buffer_30_out = nW6_1_prime ? DB5 : 1'bz;  // Controlled_Buffer controlled_buffer_30
  assign controlled_buffer_30_out = nW5_2_prime ? DB1 : 1'bz;  // Controlled_Buffer controlled_buffer_31
  assign controlled_buffer_32_out = nW6_1_prime ? 1'b0 : 1'bz;  // Controlled_Buffer controlled_buffer_32
  assign controlled_buffer_32_out = nW5_2_prime ? DB2 : 1'bz;  // Controlled_Buffer controlled_buffer_33
  Multiplexer #(.disabled(0), .enable("false")) multiplexer_4 (
    .in0(nor_15_out), .in1(controlled_buffer_6_out), .out(multiplexer_4_out), .sel(DBE));
  Multiplexer #(.disabled(0), .enable("false")) multiplexer_5 (
    .in0(nor_16_out), .in1(controlled_buffer_8_out), .out(multiplexer_5_out), .sel(DBE));
  Multiplexer #(.disabled(0), .enable("false")) multiplexer_6 (
    .in0(nor_17_out), .in1(controlled_buffer_10_out), .out(multiplexer_6_out), .sel(DBE));
  Multiplexer #(.disabled(0), .enable("false")) multiplexer_7 (
    .in0(nor_18_out), .in1(controlled_buffer_12_out), .out(multiplexer_7_out), .sel(DBE));
  Multiplexer #(.enable("false")) multiplexer_8 (
    .in0(nor_19_out), .in1(controlled_buffer_14_out), .out(multiplexer_8_out), .sel(DBE));
  Multiplexer #(.enable("false")) multiplexer_9 (
    .in0(nor_20_out), .in1(controlled_buffer_16_out), .out(multiplexer_9_out), .sel(DBE));
  Multiplexer #(.enable("false")) multiplexer_10 (
    .in0(nor_21_out), .in1(controlled_buffer_18_out), .out(multiplexer_10_out), .sel(DBE));
  Multiplexer #(.enable("false")) multiplexer_11 (
    .in0(nor_22_out), .in1(controlled_buffer_20_out), .out(multiplexer_11_out), .sel(DBE));
  Multiplexer #(.enable("false")) multiplexer_12 (
    .in0(nor_23_out), .in1(controlled_buffer_22_out), .out(multiplexer_12_out), .sel(DBE));
  Multiplexer #(.enable("false")) multiplexer_13 (
    .in0(nor_24_out), .in1(controlled_buffer_24_out), .out(multiplexer_13_out), .sel(DBE));
  Multiplexer #(.enable("false")) multiplexer_14 (
    .in0(nor_25_out), .in1(controlled_buffer_4_out), .out(multiplexer_14_out), .sel(DBE));
  Multiplexer #(.enable("false")) multiplexer_15 (
    .in0(nor_26_out), .in1(controlled_buffer_5_out), .out(multiplexer_15_out), .sel(DBE));
  Multiplexer #(.enable("false")) multiplexer_16 (
    .in0(nor_27_out), .in1(controlled_buffer_28_out), .out(multiplexer_16_out), .sel(DBE));
  Multiplexer #(.disabled(0), .enable("false")) multiplexer_17 (
    .in0(nor_28_out), .in1(controlled_buffer_30_out), .out(multiplexer_17_out), .sel(DBE));
  Multiplexer #(.disabled(0), .enable("false")) multiplexer_18 (
    .in0(nor_29_out), .in1(controlled_buffer_32_out), .out(multiplexer_18_out), .sel(DBE));
  nor _3_2 (_3_2_out, _3_out, d_latch_7_q);
  nor _14 (_14_out, d_latch_7_q, d_latch_3_not_q);
  nor nor_15 (nor_15_out, RC, ~multiplexer_4_out);  // NOR_Gate
  Pull_Resistor pull_resistor_4 (.node(multiplexer_4_out));
  nor nor_16 (nor_16_out, RC, ~multiplexer_5_out);  // NOR_Gate
  Pull_Resistor pull_resistor_5 (.node(multiplexer_5_out));
  nor nor_17 (nor_17_out, RC, ~multiplexer_6_out);  // NOR_Gate
  Pull_Resistor pull_resistor_6 (.node(multiplexer_6_out));
  nor nor_18 (nor_18_out, RC, ~multiplexer_7_out);  // NOR_Gate
  Pull_Resistor pull_resistor_7 (.node(multiplexer_7_out));
  nor nor_19 (nor_19_out, RC, ~multiplexer_8_out);  // NOR_Gate
  Pull_Resistor pull_resistor_8 (.node(multiplexer_8_out));
  nor nor_20 (nor_20_out, RC, ~multiplexer_9_out);  // NOR_Gate
  Pull_Resistor pull_resistor_9 (.node(multiplexer_9_out));
  nor nor_21 (nor_21_out, RC, ~multiplexer_10_out);  // NOR_Gate
  Pull_Resistor pull_resistor_10 (.node(multiplexer_10_out));
  nor nor_22 (nor_22_out, RC, ~multiplexer_11_out);  // NOR_Gate
  Pull_Resistor pull_resistor_11 (.node(multiplexer_11_out));
  nor nor_23 (nor_23_out, RC, ~multiplexer_12_out);  // NOR_Gate
  Pull_Resistor pull_resistor_12 (.node(multiplexer_12_out));
  nor nor_24 (nor_24_out, RC, ~multiplexer_13_out);  // NOR_Gate
  Pull_Resistor pull_resistor_13 (.node(multiplexer_13_out));
  nor nor_25 (nor_25_out, RC, ~multiplexer_14_out);  // NOR_Gate
  Pull_Resistor pull_resistor_14 (.node(multiplexer_14_out));
  nor nor_26 (nor_26_out, RC, ~multiplexer_15_out);  // NOR_Gate
  Pull_Resistor pull_resistor_15 (.node(multiplexer_15_out));
  nor nor_27 (nor_27_out, RC, ~multiplexer_16_out);  // NOR_Gate
  Pull_Resistor pull_resistor_16 (.node(multiplexer_16_out));
  nor nor_28 (nor_28_out, RC, ~multiplexer_17_out);  // NOR_Gate
  Pull_Resistor pull_resistor_17 (.node(multiplexer_17_out));
  nor nor_29 (nor_29_out, RC, ~multiplexer_18_out);  // NOR_Gate
  Pull_Resistor pull_resistor_18 (.node(multiplexer_18_out));
  nor _4 (_4_out, PCLK, _3_2_out);
  nor _15 (_15_out, PCLK, _14_out);
  not not_6 (not_6_out, nor_32_out);
  not not_7 (not_7_out, BLNK);
  not not_8 (not_8_out, nor_30_out);
  nor nor_30 (nor_30_out, undriven_4, undriven_3);
  not not_9 (not_9_out, nor_31_out);
  nor nor_31 (nor_31_out, undriven_10, undriven_5);
  nor nor_32 (nor_32_out, undriven_12, not_7_out);
  nor nor_33 (nor_33_out, undriven_29[0], not_7_out);
  nor nor_34 (nor_34_out, not_7_out, undriven_13);
  not not_10 (not_10_out, nor_34_out);
  Multiplexer #(.enable("false")) multiplexer_19 (.in0(THO0), .in1(THO2), .out(multiplexer_19_out), .sel(F_AT));
  Multiplexer #(.enable("false")) multiplexer_20 (.in0(THO1), .in1(THO3), .out(multiplexer_20_out), .sel(F_AT));
  Multiplexer #(.enable("false")) multiplexer_21 (.in0(THO2), .in1(THO4), .out(multiplexer_21_out), .sel(F_AT));
  Multiplexer #(.enable("false")) multiplexer_22 (.in0(THO3), .in1(undriven_7), .out(multiplexer_22_out), .sel(F_AT));
  Multiplexer #(.enable("false")) multiplexer_23 (.in0(THO4), .in1(undriven_8), .out(multiplexer_23_out), .sel(F_AT));
  Multiplexer #(.enable("false")) multiplexer_24 (
    .in0(undriven_6), .in1(undriven_14), .out(multiplexer_24_out), .sel(F_AT));
  Multiplexer #(.enable("false")) multiplexer_25 (.in0(TVO1), .in1(1'b1), .out(multiplexer_25_out), .sel(F_AT));
  Multiplexer #(.enable("false")) multiplexer_26 (.in0(undriven_7), .in1(1'b1), .out(multiplexer_26_out), .sel(F_AT));
  Multiplexer #(.enable("false")) multiplexer_27 (.in0(undriven_8), .in1(1'b1), .out(multiplexer_27_out), .sel(F_AT));
  Multiplexer #(.enable("false")) multiplexer_28 (.in0(undriven_14), .in1(1'b1), .out(multiplexer_28_out), .sel(F_AT));
  Multiplexer #(.enable("false")) multiplexer_29 (
    .in0(multiplexer_19_out), .in1(undriven_15), .out(multiplexer_29_out), .sel(undriven_28));
  Multiplexer #(.enable("false")) multiplexer_30 (
    .in0(multiplexer_20_out), .in1(undriven_16), .out(multiplexer_30_out), .sel(undriven_28));
  Multiplexer #(.enable("false")) multiplexer_31 (
    .in0(multiplexer_21_out), .in1(undriven_17), .out(multiplexer_31_out), .sel(undriven_28));
  Multiplexer #(.enable("false")) multiplexer_32 (
    .in0(multiplexer_22_out), .in1(undriven_18), .out(multiplexer_32_out), .sel(undriven_28));
  Multiplexer #(.enable("false")) multiplexer_33 (
    .in0(multiplexer_23_out), .in1(undriven_19), .out(multiplexer_33_out), .sel(undriven_28));
  Multiplexer #(.enable("false")) multiplexer_34 (
    .in0(multiplexer_24_out), .in1(undriven_20), .out(multiplexer_34_out), .sel(undriven_28));
  Multiplexer #(.enable("false")) multiplexer_35 (
    .in0(multiplexer_25_out), .in1(undriven_21), .out(multiplexer_35_out), .sel(undriven_28));
  Multiplexer #(.enable("false")) multiplexer_36 (
    .in0(multiplexer_26_out), .in1(undriven_22), .out(multiplexer_36_out), .sel(undriven_28));
  Multiplexer #(.enable("false")) multiplexer_37 (
    .in0(multiplexer_27_out), .in1(undriven_23), .out(multiplexer_37_out), .sel(undriven_28));
  Multiplexer #(.enable("false")) multiplexer_38 (
    .in0(multiplexer_28_out), .in1(undriven_24), .out(multiplexer_38_out), .sel(undriven_28));
  Multiplexer #(.enable("false")) multiplexer_39 (
    .in0(undriven_9), .in1(undriven_25), .out(multiplexer_39_out), .sel(undriven_28));
  Multiplexer #(.enable("false")) multiplexer_40 (
    .in0(undriven_11), .in1(undriven_26), .out(multiplexer_40_out), .sel(undriven_28));
  Multiplexer #(.enable("false")) multiplexer_41 (
    .in0(nor_33_out), .in1(undriven_27), .out(multiplexer_41_out), .sel(undriven_28));
  Multiplexer #(.enable("false")) multiplexer_42 (
    .in0(not_10_out), .in1(1'b0), .out(multiplexer_42_out), .sel(undriven_28));
  not not_11 (not_11_out, multiplexer_29_out);
  not not_12 (not_12_out, multiplexer_30_out);
  not not_13 (not_13_out, multiplexer_31_out);
  not not_14 (not_14_out, multiplexer_32_out);
  not not_15 (not_15_out, multiplexer_33_out);
  // NOT_Gate not_16 is placed but not wired
  not not_17 (not_17_out, multiplexer_34_out);
  not not_18 (not_18_out, multiplexer_35_out);
  not not_19 (not_19_out, multiplexer_36_out);
  not not_20 (not_20_out, multiplexer_37_out);
  not not_21 (not_21_out, multiplexer_38_out);
  not not_22 (not_22_out, multiplexer_39_out);
  not not_23 (not_23_out, multiplexer_40_out);
  not not_24 (not_24_out, multiplexer_41_out);
  not not_25 (not_25_out, multiplexer_42_out);
  D_latch d_latch_8 (.EN(PCLK), .D(not_11_out), .Q(nPA0));  // open: NOT_Q
  D_latch d_latch_9 (.EN(PCLK), .D(not_12_out), .Q(nPA1));  // open: NOT_Q
  D_latch d_latch_10 (.EN(PCLK), .D(not_13_out), .Q(nPA2));  // open: NOT_Q
  D_latch d_latch_11 (.EN(PCLK), .D(not_14_out), .Q(nPA3));  // open: NOT_Q
  D_latch d_latch_12 (.EN(PCLK), .D(not_15_out), .Q(nPA4));  // open: NOT_Q
  D_latch d_latch_13 (.EN(PCLK), .D(not_17_out), .Q(nPA5));  // open: NOT_Q
  D_latch d_latch_14 (.EN(PCLK), .D(not_18_out), .Q(nPA6));  // open: NOT_Q
  D_latch d_latch_15 (.EN(PCLK), .D(not_19_out), .Q(nPA7));  // open: NOT_Q
  D_latch d_latch_16 (.EN(PCLK), .D(not_20_out), .Q(nPA8));  // open: NOT_Q
  D_latch d_latch_17 (.EN(PCLK), .D(not_21_out), .Q(nPA9));  // open: NOT_Q
  D_latch d_latch_18 (.EN(PCLK), .D(not_22_out), .Q(nPA10));  // open: NOT_Q
  D_latch d_latch_19 (.EN(PCLK), .D(not_23_out), .Q(nPA11));  // open: NOT_Q
  D_latch d_latch_20 (.EN(PCLK), .D(not_24_out), .Q(nPA12));  // open: NOT_Q
  D_latch d_latch_21 (.EN(PCLK), .D(not_25_out), .Q(nPA13));  // open: NOT_Q
  not not_26 (not_26_out, O8_16);

  // Other names for the same wires on the sheet: OBJ_DATA[7:0] = {OB7, OB6, OB5, OB4, OB3, OB2, OB1, OB0};
  //   OV_DATA[3:0] = {OV3, OV2, OV1, OV0}; PPU_DATA[7:0] = {PD7, PD6, PD5, PD4, PD3, PD2, PD1, PD0}

  // Notes on the sheet:
  //   2
  //   13
  //   !
  //   12
  //   E/EV''
  //   TVSTEP
  //   THSTEP
  //   TVSTEP
  //   TVZB
  //   0/TV
  //   TVZB''
  //   THIN
  //   FVZ
  //   /W5/1'
  //   TVIN
  //   /W5/2'
  //   /W6/2'
  //   /W6/1'
  //   TVLOAD
  //   THLOAD
  //   TVIN
  //   NTH
  //   THSTEP
  //   THLOAD
  //   NTV
  //   TVSTEP
  //   TVLOAD
  //   TVSTEP
  //   TVLOAD
  //   THIN
  //   THLOAD
  //   THSTEP
  //   TH0
  //   TH1
  //   TH2
  //   TH3
  //   TH4
  //   TVLOAD
  //   TVSTEP
  //   TV0
  //   TV1
  //   TV2
  //   TV3
  //   TV4
  //   0/TV
  //   FV0
  //   FV1
  //   FV2
  //   THZ
  //   NTHIN
  //   NTVIN
  //   TVZB
  //   THZB
  //   TVZ
  //   NTH0
  //   NTV0
  //   /BLNK
  //   FVIN
  //   /FVO0
  //   /BLNK
  //   /FVO1
  //   /FVO2
  //   THZB
  //   TVZB
  //   F/AT
  //   F/AT
  //   PARR
  //   !
endmodule

module PATTERN_READOUT (
  input  PCLK,
  input  H2_prime,
  input  BLNK,
  input  H1_prime,
  input  PAR_O,
  input  F_NT,
  input  H0_prime_prime,
  input  nSH2,
  input  FVO0,
  input  OV0,
  input  FVO1,
  input  OV1,
  input  FVO2,
  input  OV2,
  input  OV3,
  input  PD0,
  input  OB0,
  input  PD1,
  input  OB1,
  input  PD2,
  input  OB2,
  input  PD3,
  input  OB3,
  input  PD4,
  input  OB4,
  input  PD5,
  input  OB5,
  input  PD6,
  input  OB6,
  input  PD7,
  input  OB7,
  input  OBSEL,
  input  O8_16,
  input  BGBSEL,
  output PARR,
  output PAD0,
  output PAD1,
  output PAD2,
  output PAD3,
  output PAD4,
  output PAD5,
  output PAD6,
  output PAD7,
  output PAD8,
  output PAD9,
  output PAD10,
  output PAD11,
  output PAD12
);

  wire d_ff_1_qn, d_latch_1_q, d_latch_2_not_q, d_latch_3_not_q, d_latch_4_not_q, d_latch_5_not_q,
       d_latch_6_not_q, d_latch_7_not_q, d_latch_8_not_q, d_latch_9_not_q, d_latch_10_not_q,
       d_latch_11_not_q, d_latch_12_not_q, d_latch_13_not_q, d_latch_14_not_q, d_latch_15_not_q,
       d_latch_16_not_q, d_latch_17_not_q, d_latch_18_not_q, d_latch_19_not_q, d_latch_20_not_q,
       d_latch_21_not_q, d_latch_22_not_q, d_latch_23_not_q, d_latch_24_not_q, d_latch_25_not_q,
       d_latch_26_not_q, d_latch_27_not_q, d_latch_28_not_q, d_latch_29_not_q, d_latch_30_not_q,
       d_latch_31_not_q, d_latch_32_not_q, d_latch_33_not_q, d_latch_34_not_q, multiplexer_1_out,
       multiplexer_2_out, multiplexer_3_out, multiplexer_4_out, multiplexer_5_out, multiplexer_6_out,
       multiplexer_7_out, multiplexer_8_out, multiplexer_9_out, multiplexer_10_out, multiplexer_11_out,
       multiplexer_12_out, multiplexer_13_out, multiplexer_14_out, nor_2_out, nor_3_out, nor_4_out,
       not_1_out, not_2_out, not_3_out, not_4_out, not_5_out, not_6_out, not_7_out, not_8_out, not_9_out,
       not_10_out, not_11_out, not_12_out, xnor_1_out, xnor_2_out, xnor_3_out, xnor_4_out;

  not not_1 (not_1_out, H2_prime);
  not not_2 (not_2_out, H0_prime_prime);
  nor nor_1 (PARR, not_1_out, BLNK);
  nor nor_2 (nor_2_out, F_NT, not_2_out);
  not not_3 (not_3_out, nor_2_out);
  not not_4 (not_4_out, PD0);
  not not_5 (not_5_out, PD1);
  not not_6 (not_6_out, PD2);
  not not_7 (not_7_out, PD3);
  not not_8 (not_8_out, PD4);
  not not_9 (not_9_out, PD5);
  not not_10 (not_10_out, PD6);
  not not_11 (not_11_out, PD7);
  D_latch d_latch_1 (.EN(not_12_out), .D(not_3_out), .Q(d_latch_1_q));  // open: NOT_Q
  nor nor_3 (nor_3_out, not_12_out, nSH2);
  not not_12 (not_12_out, PCLK);
  nor nor_4 (nor_4_out, not_12_out, d_latch_1_q);
  D_Flip_Flop #(.trigger("low")) d_ff_1 (
    .clk(PCLK), .D(OB7), .Qn(d_ff_1_qn), .en(nor_3_out));  // open: Q, preset, reset
  D_latch d_latch_2 (.EN(not_12_out), .D(not_4_out), .NOT_Q(d_latch_2_not_q));  // open: Q
  D_latch d_latch_3 (.EN(not_12_out), .D(not_5_out), .NOT_Q(d_latch_3_not_q));  // open: Q
  D_latch d_latch_4 (.EN(not_12_out), .D(not_6_out), .NOT_Q(d_latch_4_not_q));  // open: Q
  D_latch d_latch_5 (.EN(not_12_out), .D(not_7_out), .NOT_Q(d_latch_5_not_q));  // open: Q
  D_latch d_latch_6 (.EN(not_12_out), .D(not_8_out), .NOT_Q(d_latch_6_not_q));  // open: Q
  D_latch d_latch_7 (.EN(not_12_out), .D(not_9_out), .NOT_Q(d_latch_7_not_q));  // open: Q
  D_latch d_latch_8 (.EN(not_12_out), .D(not_10_out), .NOT_Q(d_latch_8_not_q));  // open: Q
  D_latch d_latch_9 (.EN(not_12_out), .D(not_11_out), .NOT_Q(d_latch_9_not_q));  // open: Q
  D_latch d_latch_10 (.EN(nor_4_out), .D(OV0), .NOT_Q(d_latch_10_not_q));  // open: Q
  D_latch d_latch_11 (.EN(nor_4_out), .D(OV1), .NOT_Q(d_latch_11_not_q));  // open: Q
  D_latch d_latch_12 (.EN(nor_4_out), .D(OV2), .NOT_Q(d_latch_12_not_q));  // open: Q
  D_latch d_latch_13 (.EN(nor_4_out), .D(OV3), .NOT_Q(d_latch_13_not_q));  // open: Q
  D_latch d_latch_14 (.EN(nor_4_out), .D(d_latch_2_not_q), .NOT_Q(d_latch_14_not_q));  // open: Q
  D_latch d_latch_15 (.EN(nor_4_out), .D(OB0), .NOT_Q(d_latch_15_not_q));  // open: Q
  D_latch d_latch_16 (.EN(nor_4_out), .D(d_latch_3_not_q), .NOT_Q(d_latch_16_not_q));  // open: Q
  D_latch d_latch_17 (.EN(nor_4_out), .D(OB1), .NOT_Q(d_latch_17_not_q));  // open: Q
  D_latch d_latch_18 (.EN(nor_4_out), .D(d_latch_4_not_q), .NOT_Q(d_latch_18_not_q));  // open: Q
  D_latch d_latch_19 (.EN(nor_4_out), .D(OB2), .NOT_Q(d_latch_19_not_q));  // open: Q
  D_latch d_latch_20 (.EN(nor_4_out), .D(d_latch_5_not_q), .NOT_Q(d_latch_20_not_q));  // open: Q
  D_latch d_latch_21 (.EN(nor_4_out), .D(OB3), .NOT_Q(d_latch_21_not_q));  // open: Q
  D_latch d_latch_22 (.EN(nor_4_out), .D(d_latch_6_not_q), .NOT_Q(d_latch_22_not_q));  // open: Q
  D_latch d_latch_23 (.EN(nor_4_out), .D(OB4), .NOT_Q(d_latch_23_not_q));  // open: Q
  D_latch d_latch_24 (.EN(nor_4_out), .D(d_latch_7_not_q), .NOT_Q(d_latch_24_not_q));  // open: Q
  D_latch d_latch_25 (.EN(nor_4_out), .D(OB5), .NOT_Q(d_latch_25_not_q));  // open: Q
  D_latch d_latch_26 (.EN(nor_4_out), .D(d_latch_8_not_q), .NOT_Q(d_latch_26_not_q));  // open: Q
  D_latch d_latch_27 (.EN(nor_4_out), .D(OB6), .NOT_Q(d_latch_27_not_q));  // open: Q
  D_latch d_latch_28 (.EN(nor_4_out), .D(d_latch_9_not_q), .NOT_Q(d_latch_28_not_q));  // open: Q
  D_latch d_latch_29 (.EN(nor_4_out), .D(OB7), .NOT_Q(d_latch_29_not_q));  // open: Q
  D_latch d_latch_30 (.EN(nor_4_out), .D(OB0), .NOT_Q(d_latch_30_not_q));  // open: Q
  D_latch d_latch_31 (.EN(not_12_out), .D(d_latch_10_not_q), .NOT_Q(d_latch_31_not_q));  // open: Q
  D_latch d_latch_32 (.EN(not_12_out), .D(d_latch_11_not_q), .NOT_Q(d_latch_32_not_q));  // open: Q
  D_latch d_latch_33 (.EN(not_12_out), .D(d_latch_12_not_q), .NOT_Q(d_latch_33_not_q));  // open: Q
  D_latch d_latch_34 (.EN(not_12_out), .D(d_latch_13_not_q), .NOT_Q(d_latch_34_not_q));  // open: Q
  Multiplexer #(.disabled(0), .enable("false")) multiplexer_1 (
    .in0(d_latch_15_not_q), .in1(xnor_4_out), .out(multiplexer_1_out), .sel(O8_16));
  Multiplexer #(.enable("false")) multiplexer_2 (
    .in0(OBSEL), .in1(d_latch_30_not_q), .out(multiplexer_2_out), .sel(O8_16));
  xnor xnor_1 (xnor_1_out, d_ff_1_qn, d_latch_31_not_q);
  xnor xnor_2 (xnor_2_out, d_ff_1_qn, d_latch_32_not_q);
  xnor xnor_3 (xnor_3_out, d_ff_1_qn, d_latch_33_not_q);
  xnor xnor_4 (xnor_4_out, d_ff_1_qn, d_latch_34_not_q);
  Multiplexer #(.enable("false")) multiplexer_3 (.in0(FVO0), .in1(xnor_1_out), .out(multiplexer_3_out), .sel(PAR_O));
  Multiplexer #(.enable("false")) multiplexer_4 (.in0(FVO1), .in1(xnor_2_out), .out(multiplexer_4_out), .sel(PAR_O));
  Multiplexer #(.enable("false")) multiplexer_5 (.in0(FVO2), .in1(xnor_3_out), .out(multiplexer_5_out), .sel(PAR_O));
  Multiplexer #(.enable("false")) multiplexer_6 (
    .in0(d_latch_14_not_q), .in1(multiplexer_1_out), .out(multiplexer_6_out), .sel(PAR_O));
  Multiplexer #(.enable("false")) multiplexer_7 (
    .in0(d_latch_16_not_q), .in1(d_latch_17_not_q), .out(multiplexer_7_out), .sel(PAR_O));
  Multiplexer #(.enable("false")) multiplexer_8 (
    .in0(d_latch_18_not_q), .in1(d_latch_19_not_q), .out(multiplexer_8_out), .sel(PAR_O));
  Multiplexer #(.enable("false")) multiplexer_9 (
    .in0(d_latch_20_not_q), .in1(d_latch_21_not_q), .out(multiplexer_9_out), .sel(PAR_O));
  Multiplexer #(.enable("false")) multiplexer_10 (
    .in0(d_latch_22_not_q), .in1(d_latch_23_not_q), .out(multiplexer_10_out), .sel(PAR_O));
  Multiplexer #(.enable("false")) multiplexer_11 (
    .in0(d_latch_24_not_q), .in1(d_latch_25_not_q), .out(multiplexer_11_out), .sel(PAR_O));
  Multiplexer #(.enable("false")) multiplexer_12 (
    .in0(d_latch_26_not_q), .in1(d_latch_27_not_q), .out(multiplexer_12_out), .sel(PAR_O));
  Multiplexer #(.enable("false")) multiplexer_13 (
    .in0(d_latch_28_not_q), .in1(d_latch_29_not_q), .out(multiplexer_13_out), .sel(PAR_O));
  Multiplexer #(.enable("false")) multiplexer_14 (
    .in0(BGBSEL), .in1(multiplexer_2_out), .out(multiplexer_14_out), .sel(PAR_O));
  D_latch d_latch_35 (.EN(not_12_out), .D(multiplexer_3_out), .Q(PAD0));  // open: NOT_Q
  D_latch d_latch_36 (.EN(not_12_out), .D(multiplexer_4_out), .Q(PAD1));  // open: NOT_Q
  D_latch d_latch_37 (.EN(not_12_out), .D(multiplexer_5_out), .Q(PAD2));  // open: NOT_Q
  not not_13 (PAD3, H1_prime);
  D_latch d_latch_38 (.EN(not_12_out), .D(multiplexer_6_out), .NOT_Q(PAD4));  // open: Q
  D_latch d_latch_39 (.EN(not_12_out), .D(multiplexer_7_out), .NOT_Q(PAD5));  // open: Q
  D_latch d_latch_40 (.EN(not_12_out), .D(multiplexer_8_out), .NOT_Q(PAD6));  // open: Q
  D_latch d_latch_41 (.EN(not_12_out), .D(multiplexer_9_out), .NOT_Q(PAD7));  // open: Q
  D_latch d_latch_42 (.EN(not_12_out), .D(multiplexer_10_out), .NOT_Q(PAD8));  // open: Q
  D_latch d_latch_43 (.EN(not_12_out), .D(multiplexer_11_out), .NOT_Q(PAD9));  // open: Q
  D_latch d_latch_44 (.EN(not_12_out), .D(multiplexer_12_out), .NOT_Q(PAD10));  // open: Q
  D_latch d_latch_45 (.EN(not_12_out), .D(multiplexer_13_out), .NOT_Q(PAD11));  // open: Q
  D_latch d_latch_46 (.EN(not_12_out), .D(multiplexer_14_out), .NOT_Q(PAD12));  // open: Q

  // Notes on the sheet:
  //   OB0
  //    номер знакогенератора для OB
  //   обычный / удвоенный размер спрайта
  //    номер знакогенератора для BG
  //   O
  //   /PCLK
  //   VDIR
  //   OBSEL
  //   08/16
  //   08/16
  //   PAR/O
  //   BGSEL
  //   PA0 - PA2 - номер строки тайла 
  //   A/B  байт строки тайла
  //   PA4 - PA11 - номер тайла в знакогенераторе
  //   PA12 - номер знакогенератора для OB или BG
endmodule

module WRITE__2007 (
  input  PCLK,
  input  DB_PAR,
  input  D0,
  input  D1,
  input  D2,
  input  D3,
  input  D4,
  input  D5,
  input  D6,
  input  D7,
  output PD0,
  output PD1,
  output PD2,
  output PD3,
  output PD4,
  output PD5,
  output PD6,
  output PD7
);

  wire d_latch_1_q, d_latch_2_q, d_latch_3_q, d_latch_4_q, d_latch_5_q, d_latch_6_q, d_latch_7_q, d_latch_8_q;

  D_latch d_latch_1 (.EN(PCLK), .D(D0), .Q(d_latch_1_q));  // open: NOT_Q
  D_latch d_latch_2 (.EN(PCLK), .D(D1), .Q(d_latch_2_q));  // open: NOT_Q
  D_latch d_latch_3 (.EN(PCLK), .D(D2), .Q(d_latch_3_q));  // open: NOT_Q
  D_latch d_latch_4 (.EN(PCLK), .D(D3), .Q(d_latch_4_q));  // open: NOT_Q
  D_latch d_latch_5 (.EN(PCLK), .D(D4), .Q(d_latch_5_q));  // open: NOT_Q
  D_latch d_latch_6 (.EN(PCLK), .D(D5), .Q(d_latch_6_q));  // open: NOT_Q
  D_latch d_latch_7 (.EN(PCLK), .D(D6), .Q(d_latch_7_q));  // open: NOT_Q
  D_latch d_latch_8 (.EN(PCLK), .D(D7), .Q(d_latch_8_q));  // open: NOT_Q
  assign PD0 = DB_PAR ? d_latch_1_q : 1'bz;  // Controlled_Buffer controlled_buffer_1
  assign PD1 = DB_PAR ? d_latch_2_q : 1'bz;  // Controlled_Buffer controlled_buffer_2
  assign PD2 = DB_PAR ? d_latch_3_q : 1'bz;  // Controlled_Buffer controlled_buffer_3
  assign PD3 = DB_PAR ? d_latch_4_q : 1'bz;  // Controlled_Buffer controlled_buffer_4
  assign PD4 = DB_PAR ? d_latch_5_q : 1'bz;  // Controlled_Buffer controlled_buffer_5
  assign PD5 = DB_PAR ? d_latch_6_q : 1'bz;  // Controlled_Buffer controlled_buffer_6
  assign PD6 = DB_PAR ? d_latch_7_q : 1'bz;  // Controlled_Buffer controlled_buffer_7
  assign PD7 = DB_PAR ? d_latch_8_q : 1'bz;  // Controlled_Buffer controlled_buffer_8
endmodule

module PAR_5BIT_COUNTER (
  input  IN_NOR7_1,
  input  BLNK,
  input  STEP,
  input  LOAD,
  input  _1,
  input  PCLK,
  input  IN0,
  input  RES,
  input  CARRY_IN,
  input  IN1,
  input  IN2,
  input  IN3,
  input  IN4,
  output TxZB,
  output TxZ,
  output Q0,
  output Q1,
  output nQ1,
  output Q2,
  output Q3,
  output Q4
);

  wire controlled_buffer_1_out, controlled_buffer_2_out, controlled_buffer_3_out, controlled_buffer_4_out,
       controlled_buffer_5_out, d_latch_1_not_q, d_latch_2_not_q, d_latch_3_not_q, d_latch_4_not_q,
       d_latch_5_not_q, d_latch_6_not_q, d_latch_8_not_q, d_latch_9_not_q, d_latch_10_not_q,
       multiplexer_1_out, multiplexer_2_out, multiplexer_3_out, multiplexer_4_out, multiplexer_5_out,
       nor_1_out, nor_2_out, nor_3_out, nor_4_out, nor_5_out, nor_8_out, nor_9_out, nor_10_out, nor_11_out,
       not_1_out, not_2_out, not_3_out, not_4_out, not_5_out, not_6_out;

  nor nor_1 (nor_1_out, d_latch_6_not_q, RES);
  nor nor_2 (nor_2_out, nQ1, RES);
  nor nor_3 (nor_3_out, d_latch_8_not_q, RES);
  nor nor_4 (nor_4_out, d_latch_9_not_q, RES);
  nor nor_5 (nor_5_out, d_latch_10_not_q, RES);
  Multiplexer #(.enable("false")) multiplexer_1 (
    .in0(d_latch_6_not_q), .in1(nor_1_out), .out(multiplexer_1_out), .sel(CARRY_IN));
  Multiplexer #(.enable("false")) multiplexer_2 (.in0(nQ1), .in1(nor_2_out), .out(multiplexer_2_out), .sel(nor_8_out));
  Multiplexer #(.enable("false")) multiplexer_3 (
    .in0(d_latch_8_not_q), .in1(nor_3_out), .out(multiplexer_3_out), .sel(nor_9_out));
  Multiplexer #(.enable("false")) multiplexer_4 (
    .in0(d_latch_9_not_q), .in1(nor_4_out), .out(multiplexer_4_out), .sel(nor_10_out));
  Multiplexer #(.enable("false")) multiplexer_5 (
    .in0(d_latch_10_not_q), .in1(nor_5_out), .out(multiplexer_5_out), .sel(nor_11_out));
  assign controlled_buffer_1_out = PCLK ? nor_1_out : 1'bz;  // Controlled_Buffer controlled_buffer_1
  assign controlled_buffer_2_out = PCLK ? nor_2_out : 1'bz;  // Controlled_Buffer controlled_buffer_2
  assign controlled_buffer_3_out = PCLK ? nor_3_out : 1'bz;  // Controlled_Buffer controlled_buffer_3
  assign controlled_buffer_4_out = PCLK ? nor_4_out : 1'bz;  // Controlled_Buffer controlled_buffer_4
  assign controlled_buffer_5_out = PCLK ? nor_5_out : 1'bz;  // Controlled_Buffer controlled_buffer_5
  assign controlled_buffer_1_out = LOAD ? IN0 : 1'bz;  // Controlled_Buffer controlled_buffer_6
  D_latch d_latch_1 (.EN(PCLK), .D(multiplexer_1_out), .NOT_Q(d_latch_1_not_q));  // open: Q
  assign controlled_buffer_1_out = STEP ? d_latch_1_not_q : 1'bz;  // Controlled_Buffer controlled_buffer_7
  assign controlled_buffer_2_out = LOAD ? IN1 : 1'bz;  // Controlled_Buffer controlled_buffer_8
  D_latch d_latch_2 (.EN(PCLK), .D(multiplexer_2_out), .NOT_Q(d_latch_2_not_q));  // open: Q
  assign controlled_buffer_2_out = STEP ? d_latch_2_not_q : 1'bz;  // Controlled_Buffer controlled_buffer_9
  assign controlled_buffer_3_out = LOAD ? IN2 : 1'bz;  // Controlled_Buffer controlled_buffer_10
  D_latch d_latch_3 (.EN(PCLK), .D(multiplexer_3_out), .NOT_Q(d_latch_3_not_q));  // open: Q
  assign controlled_buffer_3_out = STEP ? d_latch_3_not_q : 1'bz;  // Controlled_Buffer controlled_buffer_11
  assign controlled_buffer_4_out = LOAD ? IN3 : 1'bz;  // Controlled_Buffer controlled_buffer_12
  D_latch d_latch_4 (.EN(PCLK), .D(multiplexer_4_out), .NOT_Q(d_latch_4_not_q));  // open: Q
  assign controlled_buffer_4_out = STEP ? d_latch_4_not_q : 1'bz;  // Controlled_Buffer controlled_buffer_13
  assign controlled_buffer_5_out = LOAD ? IN4 : 1'bz;  // Controlled_Buffer controlled_buffer_14
  D_latch d_latch_5 (.EN(PCLK), .D(multiplexer_5_out), .NOT_Q(d_latch_5_not_q));  // open: Q
  assign controlled_buffer_5_out = STEP ? d_latch_5_not_q : 1'bz;  // Controlled_Buffer controlled_buffer_15
  not not_1 (not_1_out, IN_NOR7_1);
  nor nor_6 (TxZ, d_latch_10_not_q, d_latch_9_not_q, d_latch_8_not_q, not_1_out, nQ1, d_latch_6_not_q, not_2_out);
  not not_2 (not_2_out, BLNK);
  nor nor_7 (TxZB, BLNK, d_latch_10_not_q, d_latch_9_not_q, not_1_out, d_latch_8_not_q, _1, d_latch_6_not_q);
  D_latch d_latch_6 (.EN(1'b1), .D(controlled_buffer_1_out), .Q(Q0), .NOT_Q(d_latch_6_not_q));
  nor nor_8 (nor_8_out, d_latch_6_not_q, not_3_out);
  not not_3 (not_3_out, CARRY_IN);
  D_latch d_latch_7 (.EN(1'b1), .D(controlled_buffer_2_out), .Q(Q1), .NOT_Q(nQ1));
  nor nor_9 (nor_9_out, nQ1, not_4_out);
  not not_4 (not_4_out, nor_8_out);
  D_latch d_latch_8 (.EN(1'b1), .D(controlled_buffer_3_out), .Q(Q2), .NOT_Q(d_latch_8_not_q));
  nor nor_10 (nor_10_out, d_latch_8_not_q, not_5_out);
  not not_5 (not_5_out, nor_9_out);
  D_latch d_latch_9 (.EN(1'b1), .D(controlled_buffer_4_out), .Q(Q3), .NOT_Q(d_latch_9_not_q));
  nor nor_11 (nor_11_out, d_latch_9_not_q, not_6_out);
  not not_6 (not_6_out, nor_10_out);
  D_latch d_latch_10 (.EN(1'b1), .D(controlled_buffer_5_out), .Q(Q4), .NOT_Q(d_latch_10_not_q));
endmodule

module PAR_3BIT_COUNTER (
  input  FVZ_IN,
  input  BLNK,
  input  STEP,
  input  LOAD,
  input  PCLK,
  input  IN0,
  input  CARRY_IN,
  input  IN1,
  input  IN2,
  output TxZ,
  output Q0,
  output nQ0,
  output Q1,
  output nQ1,
  output Q2,
  output nQ2
);

  wire controlled_inverter_1_out, controlled_inverter_2_out, controlled_inverter_3_out, d_latch_1_not_q,
       d_latch_2_not_q, d_latch_3_not_q, nor_2_out, nor_3_out, not_1_out, not_2_out, xor_1_out, xor_2_out,
       xor_3_out;

  xor xor_1 (xor_1_out, CARRY_IN, nQ0);
  assign controlled_inverter_1_out = PCLK ? ~nQ0 : 1'bz;  // Controlled_Inverter controlled_inverter_1
  xor xor_2 (xor_2_out, nor_2_out, nQ1);
  assign controlled_inverter_2_out = PCLK ? ~nQ1 : 1'bz;  // Controlled_Inverter controlled_inverter_2
  xor xor_3 (xor_3_out, nor_3_out, nQ2);
  assign controlled_inverter_3_out = PCLK ? ~nQ2 : 1'bz;  // Controlled_Inverter controlled_inverter_3
  assign controlled_inverter_1_out = LOAD ? IN0 : 1'bz;  // Controlled_Buffer controlled_buffer_1
  D_latch d_latch_1 (.EN(PCLK), .D(xor_1_out), .NOT_Q(d_latch_1_not_q));  // open: Q
  assign controlled_inverter_1_out = STEP ? d_latch_1_not_q : 1'bz;  // Controlled_Buffer controlled_buffer_2
  assign controlled_inverter_2_out = LOAD ? IN1 : 1'bz;  // Controlled_Buffer controlled_buffer_3
  D_latch d_latch_2 (.EN(PCLK), .D(xor_2_out), .NOT_Q(d_latch_2_not_q));  // open: Q
  assign controlled_inverter_2_out = STEP ? d_latch_2_not_q : 1'bz;  // Controlled_Buffer controlled_buffer_4
  assign controlled_inverter_3_out = LOAD ? IN2 : 1'bz;  // Controlled_Buffer controlled_buffer_5
  D_latch d_latch_3 (.EN(PCLK), .D(xor_3_out), .NOT_Q(d_latch_3_not_q));  // open: Q
  assign controlled_inverter_3_out = STEP ? d_latch_3_not_q : 1'bz;  // Controlled_Buffer controlled_buffer_6
  nor nor_1 (TxZ, nQ2, nQ1, nQ0, BLNK, FVZ_IN);
  D_latch d_latch_4 (.EN(1'b1), .D(controlled_inverter_1_out), .Q(Q0), .NOT_Q(nQ0));
  nor nor_2 (nor_2_out, nQ0, not_1_out);
  not not_1 (not_1_out, CARRY_IN);
  D_latch d_latch_5 (.EN(1'b1), .D(controlled_inverter_2_out), .Q(Q1), .NOT_Q(nQ1));
  nor nor_3 (nor_3_out, nQ1, not_2_out);
  not not_2 (not_2_out, nor_2_out);
  D_latch d_latch_6 (.EN(1'b1), .D(controlled_inverter_3_out), .Q(Q2), .NOT_Q(nQ2));
endmodule

module PAR_1BIT_COUNTER (
  input  STEP,
  input  LOAD,
  input  PCLK,
  input  IN,
  input  CARRY_IN,
  input  BLNK,
  output Q,
  output CARRY_OUT
);

  wire controlled_inverter_1_out, d_latch_1_not_q, d_latch_2_not_q, not_1_out, not_2_out, xor_1_out;

  xor xor_1 (xor_1_out, CARRY_IN, d_latch_2_not_q);
  D_latch d_latch_1 (.EN(PCLK), .D(xor_1_out), .NOT_Q(d_latch_1_not_q));  // open: Q
  assign controlled_inverter_1_out = PCLK ? ~d_latch_2_not_q : 1'bz;  // Controlled_Inverter controlled_inverter_1
  not not_1 (not_1_out, CARRY_IN);
  not not_2 (not_2_out, BLNK);
  assign controlled_inverter_1_out = LOAD ? IN : 1'bz;  // Controlled_Buffer controlled_buffer_1
  assign controlled_inverter_1_out = STEP ? d_latch_1_not_q : 1'bz;  // Controlled_Buffer controlled_buffer_2
  D_latch d_latch_2 (.EN(1'b1), .D(controlled_inverter_1_out), .Q(Q), .NOT_Q(d_latch_2_not_q));
  nor nor_1 (CARRY_OUT, d_latch_2_not_q, not_1_out, not_2_out);

  // Notes on the sheet:
  //   carry_out
endmodule

module BG_COLOR (
  input  PCLK,
  input  CLPB,
  input  FH0,
  input  FH1,
  input  FH2,
  input  PD0,
  input  PD1,
  input  PD2,
  input  PD3,
  input  PD4,
  input  PD5,
  input  PD6,
  input  PD7,
  input  THO1,
  input  TVO1,
  input  F_AT,
  input  H0_prime_prime,
  input  F_TA,
  input  F_TB,
  input  nFO,
  output BGC0,
  output BGC1,
  output BGC2,
  output BGC3
);

  wire d_latch_10_not_q, d_latch_11_not_q, d_latch_12_not_q, d_latch_13_not_q, d_latch_14_not_q,
       d_latch_15_not_q, d_latch_16_not_q, d_latch_17_not_q, d_latch_18_q, d_latch_19_not_q,
       d_latch_20_not_q, d_latch_21_not_q, d_latch_22_not_q, d_latch_23_not_q, d_latch_24_not_q,
       d_latch_25_not_q, d_latch_26_not_q, d_latch_27_not_q, d_latch_28_q, d_latch_29_q, d_latch_30_q,
       d_latch_31_q, multiplexer_1_out, multiplexer_2_out, multiplexer_3_out, multiplexer_4_out,
       multiplexer_5_out, multiplexer_6_out, nor_1_out, nor_2_out, nor_3_out, nor_4_out, nor_5_out,
       nor_6_out, nor_7_out, not_1_out, not_2_out, not_3_out, not_4_out, not_5_out, not_6_out, not_7_out,
       not_8_out, not_9_out, not_10_out, SHIFT_REGISTER_2_p1, SHIFT_REGISTER_2_p2, SHIFT_REGISTER_2_p3,
       SHIFT_REGISTER_3_p1, SHIFT_REGISTER_3_p2, SHIFT_REGISTER_3_p3, SHIFT_REGISTER_4_p1,
       SHIFT_REGISTER_4_p2, SHIFT_REGISTER_4_p3, SHIFT_REGISTER_p1, SHIFT_REGISTER_p2, SHIFT_REGISTER_p3,
       undriven, undriven_2, undriven_3, undriven_4, undriven_5, undriven_6, undriven_7, undriven_8,
       undriven_9, undriven_10, undriven_11, undriven_12, undriven_13, undriven_14, undriven_15, undriven_16,
       undriven_17, undriven_18, undriven_19, undriven_20;
  wire [0:0] d_latch_9_q;
  wire [7:0] d_latch_1_not_q;

  not not_1 (not_1_out, F_AT);
  not not_2 (not_2_out, H0_prime_prime);
  not not_3 (not_3_out, F_TA);
  not not_4 (not_4_out, F_TB);
  not not_5 (not_5_out, nFO);
  not not_6 (not_6_out, PCLK);
  nor nor_1 (nor_1_out, PCLK, d_latch_18_q, not_2_out);
  D_latch d_latch_1 (.EN(nor_2_out), .D(PD0), .NOT_Q(d_latch_1_not_q[0]));  // open: Q
  D_latch d_latch_2 (.EN(nor_2_out), .D(PD1), .NOT_Q(d_latch_1_not_q[1]));  // open: Q
  D_latch d_latch_3 (.EN(nor_2_out), .D(PD2), .NOT_Q(d_latch_1_not_q[2]));  // open: Q
  D_latch d_latch_4 (.EN(nor_2_out), .D(PD3), .NOT_Q(d_latch_1_not_q[3]));  // open: Q
  D_latch d_latch_5 (.EN(nor_2_out), .D(PD4), .NOT_Q(d_latch_1_not_q[4]));  // open: Q
  D_latch d_latch_6 (.EN(nor_2_out), .D(PD5), .NOT_Q(d_latch_1_not_q[5]));  // open: Q
  D_latch d_latch_7 (.EN(nor_2_out), .D(PD6), .NOT_Q(d_latch_1_not_q[6]));  // open: Q
  D_latch d_latch_8 (.EN(nor_2_out), .D(PD7), .NOT_Q(d_latch_1_not_q[7]));  // open: Q
  D_latch d_latch_9 (.EN(PCLK), .D(THO1), .Q(d_latch_9_q[0]));  // open: NOT_Q
  D_latch d_latch_10 (.EN(nor_1_out), .D(PD1), .NOT_Q(d_latch_10_not_q));  // open: Q
  D_latch d_latch_11 (.EN(nor_1_out), .D(PD3), .NOT_Q(d_latch_11_not_q));  // open: Q
  D_latch d_latch_12 (.EN(nor_1_out), .D(PD5), .NOT_Q(d_latch_12_not_q));  // open: Q
  D_latch d_latch_13 (.EN(nor_1_out), .D(PD7), .NOT_Q(d_latch_13_not_q));  // open: Q
  D_latch d_latch_14 (.EN(nor_1_out), .D(PD0), .NOT_Q(d_latch_14_not_q));  // open: Q
  D_latch d_latch_15 (.EN(nor_1_out), .D(PD2), .NOT_Q(d_latch_15_not_q));  // open: Q
  D_latch d_latch_16 (.EN(nor_1_out), .D(PD4), .NOT_Q(d_latch_16_not_q));  // open: Q
  D_latch d_latch_17 (.EN(nor_1_out), .D(PD6), .NOT_Q(d_latch_17_not_q));  // open: Q
  D_latch d_latch_18 (.EN(PCLK), .D(not_1_out), .Q(d_latch_18_q));  // open: NOT_Q
  Multiplexer #(.select(2), .enable("false")) multiplexer_1 (
    .in0(d_latch_10_not_q), .in1(d_latch_11_not_q), .in2(d_latch_12_not_q), .in3(d_latch_13_not_q),
    .out(multiplexer_1_out), .sel({TVO1, d_latch_9_q[0]}));
  Multiplexer #(.select(2), .enable("false")) multiplexer_2 (
    .in0(d_latch_14_not_q), .in1(d_latch_15_not_q), .in2(d_latch_16_not_q), .in3(d_latch_17_not_q),
    .out(multiplexer_2_out), .sel({TVO1, d_latch_9_q[0]}));
  nor nor_2 (nor_2_out, PCLK, not_2_out, not_3_out);
  nor nor_3 (nor_3_out, PCLK, not_2_out, not_4_out);
  D_latch d_latch_19 (.EN(nor_3_out), .D(multiplexer_1_out), .NOT_Q(d_latch_19_not_q));  // open: Q
  D_latch d_latch_20 (.EN(nor_3_out), .D(multiplexer_2_out), .NOT_Q(d_latch_20_not_q));  // open: Q
  nor nor_4 (nor_4_out, not_7_out, nor_5_out, nor_7_out);
  not not_7 (not_7_out, PCLK);
  nor nor_5 (nor_5_out, PCLK, nor_6_out, not_5_out);
  nor nor_6 (nor_6_out, not_2_out, not_4_out);
  D_latch d_latch_21 (.EN(nor_4_out), .D(d_latch_19_not_q), .NOT_Q(d_latch_21_not_q));  // open: Q
  D_latch d_latch_22 (.EN(nor_4_out), .D(d_latch_20_not_q), .NOT_Q(d_latch_22_not_q));  // open: Q
  nor nor_7 (nor_7_out, PCLK, not_5_out);
  // SHIFT_REG SHIFT_REGISTER: pin names not known; wires that end beside it: SHIFT_REGISTER_p1, SHIFT_REGISTER_p2, SHIFT_REGISTER_p3, SHIFT_REGISTER_p1
  // SHIFT_REG SHIFT_REGISTER_2: pin names not known; wires that end beside it: SHIFT_REGISTER_2_p1, SHIFT_REGISTER_2_p2, SHIFT_REGISTER_2_p3, SHIFT_REGISTER_2_p1
  // SHIFT_REG SHIFT_REGISTER_3: pin names not known; wires that end beside it: SHIFT_REGISTER_3_p1, SHIFT_REGISTER_3_p2, SHIFT_REGISTER_3_p3, SHIFT_REGISTER_3_p1
  // SHIFT_REG SHIFT_REGISTER_4: pin names not known; wires that end beside it: SHIFT_REGISTER_4_p1, SHIFT_REGISTER_4_p2, SHIFT_REGISTER_4_p3, SHIFT_REGISTER_4_p1
  Multiplexer #(.select(3), .enable("false")) multiplexer_3 (
    .in0(SHIFT_REGISTER_p1), .in1(SHIFT_REGISTER_p2), .in2(SHIFT_REGISTER_p3), .in3(undriven),
    .in4(undriven_14), .in5(undriven_16), .in6(undriven_18), .in7(undriven_20), .out(multiplexer_3_out),
    .sel({FH2, FH1, FH0}));
  Multiplexer #(.select(3), .enable("false")) multiplexer_4 (
    .in0(SHIFT_REGISTER_2_p1), .in1(SHIFT_REGISTER_2_p2), .in2(SHIFT_REGISTER_2_p3), .in3(undriven_2),
    .in4(undriven_3), .in5(undriven_4), .in6(undriven_5), .in7(undriven_6), .out(multiplexer_4_out),
    .sel({FH2, FH1, FH0}));
  Multiplexer #(.select(3), .enable("false")) multiplexer_5 (
    .in0(SHIFT_REGISTER_3_p1), .in1(SHIFT_REGISTER_3_p2), .in2(SHIFT_REGISTER_3_p3), .in3(undriven_7),
    .in4(undriven_8), .in5(undriven_9), .in6(undriven_10), .in7(undriven_11), .out(multiplexer_5_out),
    .sel({FH2, FH1, FH0}));
  Multiplexer #(.select(3), .enable("false")) multiplexer_6 (
    .in0(SHIFT_REGISTER_4_p1), .in1(SHIFT_REGISTER_4_p2), .in2(SHIFT_REGISTER_4_p3), .in3(undriven_12),
    .in4(undriven_15), .in5(undriven_17), .in6(undriven_19), .in7(undriven_13), .out(multiplexer_6_out),
    .sel({FH2, FH1, FH0}));
  not not_8 (not_8_out, multiplexer_3_out);
  not not_9 (not_9_out, multiplexer_5_out);
  not not_10 (not_10_out, multiplexer_6_out);
  D_latch d_latch_23 (.EN(not_6_out), .D(not_8_out), .NOT_Q(d_latch_23_not_q));  // open: Q
  D_latch d_latch_24 (.EN(not_6_out), .D(multiplexer_4_out), .NOT_Q(d_latch_24_not_q));  // open: Q
  D_latch d_latch_25 (.EN(not_6_out), .D(not_9_out), .NOT_Q(d_latch_25_not_q));  // open: Q
  D_latch d_latch_26 (.EN(not_6_out), .D(not_10_out), .NOT_Q(d_latch_26_not_q));  // open: Q
  D_latch d_latch_27 (.EN(PCLK), .D(CLPB), .NOT_Q(d_latch_27_not_q));  // open: Q
  D_latch d_latch_28 (.EN(PCLK), .D(d_latch_23_not_q), .Q(d_latch_28_q));  // open: NOT_Q
  D_latch d_latch_29 (.EN(PCLK), .D(d_latch_24_not_q), .Q(d_latch_29_q));  // open: NOT_Q
  D_latch d_latch_30 (.EN(PCLK), .D(d_latch_25_not_q), .Q(d_latch_30_q));  // open: NOT_Q
  D_latch d_latch_31 (.EN(PCLK), .D(d_latch_26_not_q), .Q(d_latch_31_q));  // open: NOT_Q
  nor nor_8 (BGC0, d_latch_27_not_q, d_latch_28_q);
  nor nor_9 (BGC1, d_latch_27_not_q, d_latch_29_q);
  nor nor_10 (BGC2, d_latch_27_not_q, d_latch_30_q);
  nor nor_11 (BGC3, d_latch_27_not_q, d_latch_31_q);

  // Notes on the sheet:
  //   PD/SEL
  //   PD/SR
  //   SRLOAD
  //   STEP
  //   NEXT
  //   STEP2
  //   PCLK
  //   /PCLK
endmodule

module SHIFT_REG (
  input  STEP1,
  input  DATA_IN,
  input  STEP2,
  output OUT_0,
  output OUT_1,
  output OUT_2,
  output OUT_3,
  output OUT_4,
  output OUT_5,
  output OUT_6,
  output OUT_7
);

  wire d_latch_1_not_q, d_latch_3_not_q, d_latch_5_not_q, d_latch_7_not_q, d_latch_9_not_q, d_latch_11_not_q,
       d_latch_13_not_q, d_latch_15_not_q;

  D_latch d_latch_1 (.EN(STEP1), .D(DATA_IN), .NOT_Q(d_latch_1_not_q));  // open: Q
  D_latch d_latch_2 (.EN(STEP2), .D(d_latch_1_not_q), .NOT_Q(OUT_0));  // open: Q
  D_latch d_latch_3 (.EN(STEP1), .D(OUT_0), .NOT_Q(d_latch_3_not_q));  // open: Q
  D_latch d_latch_4 (.EN(STEP2), .D(d_latch_3_not_q), .NOT_Q(OUT_1));  // open: Q
  D_latch d_latch_5 (.EN(STEP1), .D(OUT_1), .NOT_Q(d_latch_5_not_q));  // open: Q
  D_latch d_latch_6 (.EN(STEP2), .D(d_latch_5_not_q), .NOT_Q(OUT_2));  // open: Q
  D_latch d_latch_7 (.EN(STEP1), .D(OUT_2), .NOT_Q(d_latch_7_not_q));  // open: Q
  D_latch d_latch_8 (.EN(STEP2), .D(d_latch_7_not_q), .NOT_Q(OUT_3));  // open: Q
  D_latch d_latch_9 (.EN(STEP1), .D(OUT_3), .NOT_Q(d_latch_9_not_q));  // open: Q
  D_latch d_latch_10 (.EN(STEP2), .D(d_latch_9_not_q), .NOT_Q(OUT_4));  // open: Q
  D_latch d_latch_11 (.EN(STEP1), .D(OUT_4), .NOT_Q(d_latch_11_not_q));  // open: Q
  D_latch d_latch_12 (.EN(STEP2), .D(d_latch_11_not_q), .NOT_Q(OUT_5));  // open: Q
  D_latch d_latch_13 (.EN(STEP1), .D(OUT_5), .NOT_Q(d_latch_13_not_q));  // open: Q
  D_latch d_latch_14 (.EN(STEP2), .D(d_latch_13_not_q), .NOT_Q(OUT_6));  // open: Q
  D_latch d_latch_15 (.EN(STEP1), .D(OUT_6), .NOT_Q(d_latch_15_not_q));  // open: Q
  D_latch d_latch_16 (.EN(STEP2), .D(d_latch_15_not_q), .NOT_Q(OUT_7));  // open: Q
endmodule

module SHIFT_REG_LOAD (
  input  _0,
  input  _1,
  input  _2,
  input  _3,
  input  _4,
  input  _5,
  input  _6,
  input  _7,
  input  LOAD,
  input  STEP,
  input  NEXT,
  output OUT
);

  wire controlled_buffer_1_out, controlled_buffer_3_out, controlled_buffer_5_out, controlled_buffer_7_out,
       controlled_buffer_9_out, controlled_buffer_11_out, controlled_buffer_13_out, controlled_buffer_15_out,
       d_latch_1_not_q, d_latch_2_not_q, d_latch_3_not_q, d_latch_4_not_q, d_latch_5_not_q, d_latch_6_not_q,
       d_latch_7_not_q, d_latch_8_not_q, d_latch_9_not_q, d_latch_10_not_q, d_latch_11_not_q,
       d_latch_12_not_q, d_latch_13_not_q, d_latch_14_not_q, d_latch_15_not_q;

  assign controlled_buffer_1_out = STEP ? 1'b1 : 1'bz;  // Controlled_Buffer controlled_buffer_1
  assign controlled_buffer_1_out = LOAD ? _0 : 1'bz;  // Controlled_Buffer controlled_buffer_2
  D_latch d_latch_1 (.EN(1'b1), .D(controlled_buffer_1_out), .NOT_Q(d_latch_1_not_q));  // open: Q
  D_latch d_latch_2 (.EN(NEXT), .D(d_latch_1_not_q), .NOT_Q(d_latch_2_not_q));  // open: Q
  assign controlled_buffer_3_out = LOAD ? _1 : 1'bz;  // Controlled_Buffer controlled_buffer_3
  assign controlled_buffer_3_out = STEP ? d_latch_2_not_q : 1'bz;  // Controlled_Buffer controlled_buffer_4
  D_latch d_latch_3 (.EN(1'b1), .D(controlled_buffer_3_out), .NOT_Q(d_latch_3_not_q));  // open: Q
  D_latch d_latch_4 (.EN(NEXT), .D(d_latch_3_not_q), .NOT_Q(d_latch_4_not_q));  // open: Q
  assign controlled_buffer_5_out = STEP ? d_latch_4_not_q : 1'bz;  // Controlled_Buffer controlled_buffer_5
  assign controlled_buffer_5_out = LOAD ? _2 : 1'bz;  // Controlled_Buffer controlled_buffer_6
  D_latch d_latch_5 (.EN(1'b1), .D(controlled_buffer_5_out), .NOT_Q(d_latch_5_not_q));  // open: Q
  D_latch d_latch_6 (.EN(NEXT), .D(d_latch_5_not_q), .NOT_Q(d_latch_6_not_q));  // open: Q
  assign controlled_buffer_7_out = LOAD ? _3 : 1'bz;  // Controlled_Buffer controlled_buffer_7
  assign controlled_buffer_7_out = STEP ? d_latch_6_not_q : 1'bz;  // Controlled_Buffer controlled_buffer_8
  D_latch d_latch_7 (.EN(1'b1), .D(controlled_buffer_7_out), .NOT_Q(d_latch_7_not_q));  // open: Q
  D_latch d_latch_8 (.EN(NEXT), .D(d_latch_7_not_q), .NOT_Q(d_latch_8_not_q));  // open: Q
  assign controlled_buffer_9_out = STEP ? d_latch_8_not_q : 1'bz;  // Controlled_Buffer controlled_buffer_9
  assign controlled_buffer_9_out = LOAD ? _4 : 1'bz;  // Controlled_Buffer controlled_buffer_10
  D_latch d_latch_9 (.EN(1'b1), .D(controlled_buffer_9_out), .NOT_Q(d_latch_9_not_q));  // open: Q
  D_latch d_latch_10 (.EN(NEXT), .D(d_latch_9_not_q), .NOT_Q(d_latch_10_not_q));  // open: Q
  assign controlled_buffer_11_out = LOAD ? _5 : 1'bz;  // Controlled_Buffer controlled_buffer_11
  assign controlled_buffer_11_out = STEP ? d_latch_10_not_q : 1'bz;  // Controlled_Buffer controlled_buffer_12
  D_latch d_latch_11 (.EN(1'b1), .D(controlled_buffer_11_out), .NOT_Q(d_latch_11_not_q));  // open: Q
  D_latch d_latch_12 (.EN(NEXT), .D(d_latch_11_not_q), .NOT_Q(d_latch_12_not_q));  // open: Q
  assign controlled_buffer_13_out = STEP ? d_latch_12_not_q : 1'bz;  // Controlled_Buffer controlled_buffer_13
  assign controlled_buffer_13_out = LOAD ? _6 : 1'bz;  // Controlled_Buffer controlled_buffer_14
  D_latch d_latch_13 (.EN(1'b1), .D(controlled_buffer_13_out), .NOT_Q(d_latch_13_not_q));  // open: Q
  D_latch d_latch_14 (.EN(NEXT), .D(d_latch_13_not_q), .NOT_Q(d_latch_14_not_q));  // open: Q
  assign controlled_buffer_15_out = LOAD ? _7 : 1'bz;  // Controlled_Buffer controlled_buffer_15
  assign controlled_buffer_15_out = STEP ? d_latch_14_not_q : 1'bz;  // Controlled_Buffer controlled_buffer_16
  D_latch d_latch_15 (.EN(1'b1), .D(controlled_buffer_15_out), .NOT_Q(d_latch_15_not_q));  // open: Q
  D_latch d_latch_16 (.EN(NEXT), .D(d_latch_15_not_q), .NOT_Q(OUT));  // open: Q
endmodule

module SEL4x16 (
  input  PCLK,
  input  L0,
  input  L1,
  input  C2,
  input  C3,
  output _15,
  output _14,
  output _13,
  output _12,
  output _11,
  output _10,
  output _9,
  output _8,
  output _7,
  output _6,
  output _5,
  output _4,
  output _3,
  output _2,
  output _1,
  output _0
);

  wire not_1_out, not_2_out, not_3_out, not_4_out, transistor_1_out, transistor_5_out, transistor_9_out,
       transistor_10_out, transistor_17_out, transistor_21_out, transistor_25_out, transistor_29_out,
       transistor_33_out, transistor_37_out, transistor_41_out, transistor_42_out, transistor_49_out,
       transistor_53_out, transistor_57_out, transistor_61_out;

  not not_1 (not_1_out, L0);
  not not_2 (not_2_out, L1);
  not not_3 (not_3_out, C2);
  not not_4 (not_4_out, C3);
  and and_1 (_15, PCLK, transistor_1_out);
  Transistor #(.\type ("n")) transistor_1 (.in(1'b0), .out(transistor_1_out), .gate(not_1_out));
  Transistor #(.\type ("n")) transistor_2 (.in(1'b0), .out(transistor_1_out), .gate(not_2_out));
  Transistor #(.\type ("n")) transistor_3 (.in(1'b0), .out(transistor_1_out), .gate(not_3_out));
  Transistor #(.\type ("n")) transistor_4 (.in(1'b0), .out(transistor_1_out), .gate(not_4_out));
  Pull_Resistor #(.pull(1)) pull_resistor_1 (.node(transistor_1_out));
  and and_2 (_13, PCLK, transistor_10_out);
  and and_3 (_14, PCLK, transistor_5_out);
  Transistor #(.\type ("n")) transistor_5 (.in(1'b0), .out(transistor_5_out), .gate(not_1_out));
  Transistor #(.\type ("n")) transistor_6 (.in(1'b0), .out(transistor_5_out), .gate(not_2_out));
  Transistor #(.\type ("n")) transistor_7 (.in(1'b0), .out(transistor_5_out), .gate(C2));
  Transistor #(.\type ("n")) transistor_8 (.in(1'b0), .out(transistor_5_out), .gate(not_4_out));
  Pull_Resistor #(.pull(1)) pull_resistor_2 (.node(transistor_5_out));
  and and_4 (_12, PCLK, transistor_9_out);
  Transistor #(.\type ("n")) transistor_9 (.in(1'b0), .out(transistor_9_out), .gate(not_1_out));
  Transistor #(.\type ("n")) transistor_10 (.in(1'b0), .out(transistor_10_out), .gate(not_1_out));
  Transistor #(.\type ("n")) transistor_11 (.in(1'b0), .out(transistor_10_out), .gate(not_2_out));
  Transistor #(.\type ("n")) transistor_12 (.in(1'b0), .out(transistor_9_out), .gate(not_2_out));
  Transistor #(.\type ("n")) transistor_13 (.in(1'b0), .out(transistor_9_out), .gate(C2));
  Transistor #(.\type ("n")) transistor_14 (.in(1'b0), .out(transistor_10_out), .gate(not_3_out));
  Transistor #(.\type ("n")) transistor_15 (.in(1'b0), .out(transistor_10_out), .gate(C3));
  Transistor #(.\type ("n")) transistor_16 (.in(1'b0), .out(transistor_9_out), .gate(C3));
  Pull_Resistor #(.pull(1)) pull_resistor_3 (.node(transistor_9_out));
  Pull_Resistor #(.pull(1)) pull_resistor_4 (.node(transistor_10_out));
  and and_5 (_11, PCLK, transistor_17_out);
  Transistor #(.\type ("n")) transistor_17 (.in(1'b0), .out(transistor_17_out), .gate(L0));
  Transistor #(.\type ("n")) transistor_18 (.in(1'b0), .out(transistor_17_out), .gate(not_2_out));
  Transistor #(.\type ("n")) transistor_19 (.in(1'b0), .out(transistor_17_out), .gate(not_3_out));
  Transistor #(.\type ("n")) transistor_20 (.in(1'b0), .out(transistor_17_out), .gate(not_4_out));
  Pull_Resistor #(.pull(1)) pull_resistor_5 (.node(transistor_17_out));
  and and_6 (_10, PCLK, transistor_21_out);
  Transistor #(.\type ("n")) transistor_21 (.in(1'b0), .out(transistor_21_out), .gate(L0));
  Transistor #(.\type ("n")) transistor_22 (.in(1'b0), .out(transistor_21_out), .gate(not_2_out));
  Transistor #(.\type ("n")) transistor_23 (.in(1'b0), .out(transistor_21_out), .gate(C2));
  Transistor #(.\type ("n")) transistor_24 (.in(1'b0), .out(transistor_21_out), .gate(not_4_out));
  Pull_Resistor #(.pull(1)) pull_resistor_6 (.node(transistor_21_out));
  and and_7 (_9, PCLK, transistor_25_out);
  Transistor #(.\type ("n")) transistor_25 (.in(1'b0), .out(transistor_25_out), .gate(L0));
  Transistor #(.\type ("n")) transistor_26 (.in(1'b0), .out(transistor_25_out), .gate(not_2_out));
  Transistor #(.\type ("n")) transistor_27 (.in(1'b0), .out(transistor_25_out), .gate(not_3_out));
  Transistor #(.\type ("n")) transistor_28 (.in(1'b0), .out(transistor_25_out), .gate(C3));
  Pull_Resistor #(.pull(1)) pull_resistor_7 (.node(transistor_25_out));
  and and_8 (_8, PCLK, transistor_29_out);
  Transistor #(.\type ("n")) transistor_29 (.in(1'b0), .out(transistor_29_out), .gate(L0));
  Transistor #(.\type ("n")) transistor_30 (.in(1'b0), .out(transistor_29_out), .gate(not_2_out));
  Transistor #(.\type ("n")) transistor_31 (.in(1'b0), .out(transistor_29_out), .gate(C2));
  Transistor #(.\type ("n")) transistor_32 (.in(1'b0), .out(transistor_29_out), .gate(C3));
  Pull_Resistor #(.pull(1)) pull_resistor_8 (.node(transistor_29_out));
  and and_9 (_7, PCLK, transistor_33_out);
  Transistor #(.\type ("n")) transistor_33 (.in(1'b0), .out(transistor_33_out), .gate(not_1_out));
  Transistor #(.\type ("n")) transistor_34 (.in(1'b0), .out(transistor_33_out), .gate(L1));
  Transistor #(.\type ("n")) transistor_35 (.in(1'b0), .out(transistor_33_out), .gate(not_3_out));
  Transistor #(.\type ("n")) transistor_36 (.in(1'b0), .out(transistor_33_out), .gate(not_4_out));
  Pull_Resistor #(.pull(1)) pull_resistor_9 (.node(transistor_33_out));
  and and_10 (_5, PCLK, transistor_42_out);
  and and_11 (_6, PCLK, transistor_37_out);
  Transistor #(.\type ("n")) transistor_37 (.in(1'b0), .out(transistor_37_out), .gate(not_1_out));
  Transistor #(.\type ("n")) transistor_38 (.in(1'b0), .out(transistor_37_out), .gate(L1));
  Transistor #(.\type ("n")) transistor_39 (.in(1'b0), .out(transistor_37_out), .gate(C2));
  Transistor #(.\type ("n")) transistor_40 (.in(1'b0), .out(transistor_37_out), .gate(not_4_out));
  Pull_Resistor #(.pull(1)) pull_resistor_10 (.node(transistor_37_out));
  and and_12 (_4, PCLK, transistor_41_out);
  Transistor #(.\type ("n")) transistor_41 (.in(1'b0), .out(transistor_41_out), .gate(not_1_out));
  Transistor #(.\type ("n")) transistor_42 (.in(1'b0), .out(transistor_42_out), .gate(not_1_out));
  Transistor #(.\type ("n")) transistor_43 (.in(1'b0), .out(transistor_41_out), .gate(L1));
  Transistor #(.\type ("n")) transistor_44 (.in(1'b0), .out(transistor_42_out), .gate(L1));
  Transistor #(.\type ("n")) transistor_45 (.in(1'b0), .out(transistor_41_out), .gate(C2));
  Transistor #(.\type ("n")) transistor_46 (.in(1'b0), .out(transistor_42_out), .gate(not_3_out));
  Transistor #(.\type ("n")) transistor_47 (.in(1'b0), .out(transistor_42_out), .gate(C3));
  Transistor #(.\type ("n")) transistor_48 (.in(1'b0), .out(transistor_41_out), .gate(C3));
  Pull_Resistor #(.pull(1)) pull_resistor_11 (.node(transistor_41_out));
  Pull_Resistor #(.pull(1)) pull_resistor_12 (.node(transistor_42_out));
  and and_13 (_3, PCLK, transistor_49_out);
  Transistor #(.\type ("n")) transistor_49 (.in(1'b0), .out(transistor_49_out), .gate(L0));
  Transistor #(.\type ("n")) transistor_50 (.in(1'b0), .out(transistor_49_out), .gate(L1));
  Transistor #(.\type ("n")) transistor_51 (.in(1'b0), .out(transistor_49_out), .gate(not_3_out));
  Transistor #(.\type ("n")) transistor_52 (.in(1'b0), .out(transistor_49_out), .gate(not_4_out));
  Pull_Resistor #(.pull(1)) pull_resistor_13 (.node(transistor_49_out));
  and and_14 (_2, PCLK, transistor_53_out);
  Transistor #(.\type ("n")) transistor_53 (.in(1'b0), .out(transistor_53_out), .gate(L0));
  Transistor #(.\type ("n")) transistor_54 (.in(1'b0), .out(transistor_53_out), .gate(L1));
  Transistor #(.\type ("n")) transistor_55 (.in(1'b0), .out(transistor_53_out), .gate(C2));
  Transistor #(.\type ("n")) transistor_56 (.in(1'b0), .out(transistor_53_out), .gate(not_4_out));
  Pull_Resistor #(.pull(1)) pull_resistor_14 (.node(transistor_53_out));
  and and_15 (_1, PCLK, transistor_57_out);
  Transistor #(.\type ("n")) transistor_57 (.in(1'b0), .out(transistor_57_out), .gate(L0));
  Transistor #(.\type ("n")) transistor_58 (.in(1'b0), .out(transistor_57_out), .gate(L1));
  Transistor #(.\type ("n")) transistor_59 (.in(1'b0), .out(transistor_57_out), .gate(not_3_out));
  Transistor #(.\type ("n")) transistor_60 (.in(1'b0), .out(transistor_57_out), .gate(C3));
  Pull_Resistor #(.pull(1)) pull_resistor_15 (.node(transistor_57_out));
  and and_16 (_0, PCLK, transistor_61_out);
  Transistor #(.\type ("n")) transistor_61 (.in(1'b0), .out(transistor_61_out), .gate(L0));
  Transistor #(.\type ("n")) transistor_62 (.in(1'b0), .out(transistor_61_out), .gate(L1));
  Transistor #(.\type ("n")) transistor_63 (.in(1'b0), .out(transistor_61_out), .gate(C2));
  Transistor #(.\type ("n")) transistor_64 (.in(1'b0), .out(transistor_61_out), .gate(C3));
  Pull_Resistor #(.pull(1)) pull_resistor_16 (.node(transistor_61_out));
endmodule

module SEL12x3 (
  input  PCLK,
  input  nTx,
  input  IN0,
  input  IN1,
  input  IN2,
  input  IN3,
  input  IN4,
  input  IN5,
  input  IN6,
  input  IN7,
  input  IN8,
  input  IN9,
  input  IN10,
  input  IN11,
  input  _0,
  input  _1,
  output OUT2,
  output OUT1,
  output OUT0
);

  wire multiplexer_1_out, multiplexer_2_out, multiplexer_3_out, not_1_out;

  not not_1 (not_1_out, nTx);
  Multiplexer #(.select(2), .enable("false")) multiplexer_1 (
    .in0(IN0), .in1(IN2), .in2(IN1), .in3(IN3), .out(multiplexer_1_out), .sel({_1, _0}));
  Multiplexer #(.select(2), .enable("false")) multiplexer_2 (
    .in0(IN4), .in1(IN6), .in2(IN5), .in3(IN7), .out(multiplexer_2_out), .sel({_1, _0}));
  Multiplexer #(.select(2), .enable("false")) multiplexer_3 (
    .in0(IN8), .in1(IN10), .in2(IN9), .in3(IN11), .out(multiplexer_3_out), .sel({_1, _0}));
  D_Flip_Flop #(.trigger("high")) d_ff_1 (
    .clk(PCLK), .D(multiplexer_1_out), .Q(OUT2), .reset(not_1_out));  // open: Qn, preset, en
  D_Flip_Flop #(.trigger("high")) d_ff_2 (
    .clk(PCLK), .D(multiplexer_2_out), .Q(OUT1), .reset(not_1_out));  // open: Qn, preset, en
  D_Flip_Flop #(.trigger("high")) d_ff_3 (
    .clk(PCLK), .D(multiplexer_3_out), .Q(OUT0), .reset(not_1_out));  // open: Qn, preset, en
endmodule

module SEL16x12_R (
  input  PCLK,
  input  _15,
  input  _14,
  input  _13,
  input  _12,
  input  _11,
  input  _10,
  input  _9,
  input  _8,
  input  _7,
  input  _6,
  input  _5,
  input  _4,
  input  _3,
  input  _2,
  input  _1,
  input  _0,
  output OUT0,
  output OUT1,
  output OUT2,
  output OUT3,
  output OUT4,
  output OUT5,
  output OUT6,
  output OUT7,
  output OUT8,
  output OUT9,
  output OUT10,
  output OUT11
);

  wire transistor_1_out, transistor_2_out, transistor_3_out, transistor_5_out, transistor_7_out,
       transistor_9_out, transistor_10_out, transistor_12_out, transistor_15_out, transistor_17_out,
       transistor_18_out, transistor_34_out;

  and and_1 (OUT0, PCLK, transistor_1_out);
  and and_2 (OUT1, PCLK, transistor_12_out);
  and and_3 (OUT2, PCLK, transistor_34_out);
  and and_4 (OUT3, PCLK, transistor_2_out);
  and and_5 (OUT4, PCLK, transistor_3_out);
  and and_6 (OUT5, PCLK, transistor_15_out);
  and and_7 (OUT6, PCLK, transistor_5_out);
  and and_8 (OUT7, PCLK, transistor_7_out);
  and and_9 (OUT8, PCLK, transistor_17_out);
  and and_10 (OUT9, PCLK, transistor_18_out);
  and and_11 (OUT10, PCLK, transistor_9_out);
  and and_12 (OUT11, PCLK, transistor_10_out);
  Transistor #(.\type ("n")) transistor_1 (.in(1'b0), .out(transistor_1_out), .gate(_14));
  Transistor #(.\type ("n")) transistor_2 (.in(1'b0), .out(transistor_2_out), .gate(_14));
  Transistor #(.\type ("n")) transistor_3 (.in(1'b0), .out(transistor_3_out), .gate(_15));
  Transistor #(.\type ("n")) transistor_4 (.in(1'b0), .out(transistor_3_out), .gate(_14));
  Transistor #(.\type ("n")) transistor_5 (.in(1'b0), .out(transistor_5_out), .gate(_14));
  Transistor #(.\type ("n")) transistor_6 (.in(1'b0), .out(transistor_5_out), .gate(_15));
  Transistor #(.\type ("n")) transistor_7 (.in(1'b0), .out(transistor_7_out), .gate(_15));
  Transistor #(.\type ("n")) transistor_8 (.in(1'b0), .out(transistor_7_out), .gate(_14));
  Transistor #(.\type ("n")) transistor_9 (.in(1'b0), .out(transistor_9_out), .gate(_15));
  Transistor #(.\type ("n")) transistor_10 (.in(1'b0), .out(transistor_10_out), .gate(_14));
  Transistor #(.\type ("n")) transistor_11 (.in(1'b0), .out(transistor_1_out), .gate(_13));
  Transistor #(.\type ("n")) transistor_12 (.in(1'b0), .out(transistor_12_out), .gate(_13));
  Transistor #(.\type ("n")) transistor_13 (.in(1'b0), .out(transistor_2_out), .gate(_13));
  Transistor #(.\type ("n")) transistor_14 (.in(1'b0), .out(transistor_3_out), .gate(_12));
  Transistor #(.\type ("n")) transistor_15 (.in(1'b0), .out(transistor_15_out), .gate(_13));
  Transistor #(.\type ("n")) transistor_16 (.in(1'b0), .out(transistor_7_out), .gate(_13));
  Transistor #(.\type ("n")) transistor_17 (.in(1'b0), .out(transistor_17_out), .gate(_12));
  Transistor #(.\type ("n")) transistor_18 (.in(1'b0), .out(transistor_18_out), .gate(_12));
  Transistor #(.\type ("n")) transistor_19 (.in(1'b0), .out(transistor_18_out), .gate(_13));
  Transistor #(.\type ("n")) transistor_20 (.in(1'b0), .out(transistor_9_out), .gate(_12));
  Transistor #(.\type ("n")) transistor_21 (.in(1'b0), .out(transistor_10_out), .gate(_13));
  Transistor #(.\type ("n")) transistor_22 (.in(1'b0), .out(transistor_1_out), .gate(_11));
  Transistor #(.\type ("n")) transistor_23 (.in(1'b0), .out(transistor_12_out), .gate(_11));
  Transistor #(.\type ("n")) transistor_24 (.in(1'b0), .out(transistor_3_out), .gate(_11));
  Transistor #(.\type ("n")) transistor_25 (.in(1'b0), .out(transistor_15_out), .gate(_11));
  Transistor #(.\type ("n")) transistor_26 (.in(1'b0), .out(transistor_5_out), .gate(_11));
  Transistor #(.\type ("n")) transistor_27 (.in(1'b0), .out(transistor_7_out), .gate(_11));
  Transistor #(.\type ("n")) transistor_28 (.in(1'b0), .out(transistor_17_out), .gate(_11));
  Transistor #(.\type ("n")) transistor_29 (.in(1'b0), .out(transistor_18_out), .gate(_11));
  Transistor #(.\type ("n")) transistor_30 (.in(1'b0), .out(transistor_10_out), .gate(_11));
  Transistor #(.\type ("n")) transistor_31 (.in(1'b0), .out(transistor_1_out), .gate(_9));
  Transistor #(.\type ("n")) transistor_32 (.in(1'b0), .out(transistor_1_out), .gate(_10));
  Transistor #(.\type ("n")) transistor_33 (.in(1'b0), .out(transistor_12_out), .gate(_9));
  Transistor #(.\type ("n")) transistor_34 (.in(1'b0), .out(transistor_34_out), .gate(_9));
  Transistor #(.\type ("n")) transistor_35 (.in(1'b0), .out(transistor_2_out), .gate(_9));
  Transistor #(.\type ("n")) transistor_36 (.in(1'b0), .out(transistor_2_out), .gate(_10));
  Transistor #(.\type ("n")) transistor_37 (.in(1'b0), .out(transistor_3_out), .gate(_10));
  Transistor #(.\type ("n")) transistor_38 (.in(1'b0), .out(transistor_3_out), .gate(_9));
  Transistor #(.\type ("n")) transistor_39 (.in(1'b0), .out(transistor_15_out), .gate(_10));
  Transistor #(.\type ("n")) transistor_40 (.in(1'b0), .out(transistor_5_out), .gate(_9));
  Transistor #(.\type ("n")) transistor_41 (.in(1'b0), .out(transistor_7_out), .gate(_10));
  Transistor #(.\type ("n")) transistor_42 (.in(1'b0), .out(transistor_17_out), .gate(_9));
  Transistor #(.\type ("n")) transistor_43 (.in(1'b0), .out(transistor_17_out), .gate(_10));
  Transistor #(.\type ("n")) transistor_44 (.in(1'b0), .out(transistor_18_out), .gate(_10));
  Transistor #(.\type ("n")) transistor_45 (.in(1'b0), .out(transistor_9_out), .gate(_10));
  Transistor #(.\type ("n")) transistor_46 (.in(1'b0), .out(transistor_9_out), .gate(_9));
  Transistor #(.\type ("n")) transistor_47 (.in(1'b0), .out(transistor_15_out), .gate(_8));
  Transistor #(.\type ("n")) transistor_48 (.in(1'b0), .out(transistor_12_out), .gate(_7));
  Transistor #(.\type ("n")) transistor_49 (.in(1'b0), .out(transistor_34_out), .gate(_7));
  Transistor #(.\type ("n")) transistor_50 (.in(1'b0), .out(transistor_2_out), .gate(_6));
  Transistor #(.\type ("n")) transistor_51 (.in(1'b0), .out(transistor_15_out), .gate(_7));
  Transistor #(.\type ("n")) transistor_52 (.in(1'b0), .out(transistor_5_out), .gate(_7));
  Transistor #(.\type ("n")) transistor_53 (.in(1'b0), .out(transistor_7_out), .gate(_6));
  Transistor #(.\type ("n")) transistor_54 (.in(1'b0), .out(transistor_18_out), .gate(_7));
  Transistor #(.\type ("n")) transistor_55 (.in(1'b0), .out(transistor_9_out), .gate(_7));
  Transistor #(.\type ("n")) transistor_56 (.in(1'b0), .out(transistor_10_out), .gate(_7));
  Transistor #(.\type ("n")) transistor_57 (.in(1'b0), .out(transistor_1_out), .gate(_4));
  Transistor #(.\type ("n")) transistor_58 (.in(1'b0), .out(transistor_34_out), .gate(_5));
  Transistor #(.\type ("n")) transistor_59 (.in(1'b0), .out(transistor_34_out), .gate(_4));
  Transistor #(.\type ("n")) transistor_60 (.in(1'b0), .out(transistor_2_out), .gate(_5));
  Transistor #(.\type ("n")) transistor_61 (.in(1'b0), .out(transistor_2_out), .gate(_4));
  Transistor #(.\type ("n")) transistor_62 (.in(1'b0), .out(transistor_15_out), .gate(_4));
  Transistor #(.\type ("n")) transistor_63 (.in(1'b0), .out(transistor_15_out), .gate(_5));
  Transistor #(.\type ("n")) transistor_64 (.in(1'b0), .out(transistor_5_out), .gate(_4));
  Transistor #(.\type ("n")) transistor_65 (.in(1'b0), .out(transistor_7_out), .gate(_4));
  Transistor #(.\type ("n")) transistor_66 (.in(1'b0), .out(transistor_18_out), .gate(_5));
  Transistor #(.\type ("n")) transistor_67 (.in(1'b0), .out(transistor_18_out), .gate(_4));
  Transistor #(.\type ("n")) transistor_68 (.in(1'b0), .out(transistor_9_out), .gate(_4));
  Transistor #(.\type ("n")) transistor_69 (.in(1'b0), .out(transistor_10_out), .gate(_4));
  Transistor #(.\type ("n")) transistor_70 (.in(1'b0), .out(transistor_12_out), .gate(_3));
  Transistor #(.\type ("n")) transistor_71 (.in(1'b0), .out(transistor_2_out), .gate(_3));
  Transistor #(.\type ("n")) transistor_72 (.in(1'b0), .out(transistor_5_out), .gate(_3));
  Transistor #(.\type ("n")) transistor_73 (.in(1'b0), .out(transistor_7_out), .gate(_3));
  Transistor #(.\type ("n")) transistor_74 (.in(1'b0), .out(transistor_18_out), .gate(_3));
  Transistor #(.\type ("n")) transistor_75 (.in(1'b0), .out(transistor_10_out), .gate(_3));
  Transistor #(.\type ("n")) transistor_76 (.in(1'b0), .out(transistor_1_out), .gate(_2));
  Transistor #(.\type ("n")) transistor_77 (.in(1'b0), .out(transistor_12_out), .gate(_2));
  Transistor #(.\type ("n")) transistor_78 (.in(1'b0), .out(transistor_12_out), .gate(_1));
  Transistor #(.\type ("n")) transistor_79 (.in(1'b0), .out(transistor_2_out), .gate(_1));
  Transistor #(.\type ("n")) transistor_80 (.in(1'b0), .out(transistor_15_out), .gate(_1));
  Transistor #(.\type ("n")) transistor_81 (.in(1'b0), .out(transistor_15_out), .gate(_2));
  Transistor #(.\type ("n")) transistor_82 (.in(1'b0), .out(transistor_7_out), .gate(_1));
  Transistor #(.\type ("n")) transistor_83 (.in(1'b0), .out(transistor_7_out), .gate(_2));
  Transistor #(.\type ("n")) transistor_84 (.in(1'b0), .out(transistor_17_out), .gate(_2));
  Transistor #(.\type ("n")) transistor_85 (.in(1'b0), .out(transistor_18_out), .gate(_1));
  Transistor #(.\type ("n")) transistor_86 (.in(1'b0), .out(transistor_18_out), .gate(_2));
  Transistor #(.\type ("n")) transistor_87 (.in(1'b0), .out(transistor_9_out), .gate(_1));
  Transistor #(.\type ("n")) transistor_88 (.in(1'b0), .out(transistor_9_out), .gate(_2));
  Transistor #(.\type ("n")) transistor_89 (.in(1'b0), .out(transistor_10_out), .gate(_2));
  Transistor #(.\type ("n")) transistor_90 (.in(1'b0), .out(transistor_10_out), .gate(_1));
  Transistor #(.\type ("n")) transistor_91 (.in(1'b0), .out(transistor_1_out), .gate(_0));
  Transistor #(.\type ("n")) transistor_92 (.in(1'b0), .out(transistor_12_out), .gate(_0));
  Transistor #(.\type ("n")) transistor_93 (.in(1'b0), .out(transistor_3_out), .gate(_0));
  Transistor #(.\type ("n")) transistor_94 (.in(1'b0), .out(transistor_7_out), .gate(_0));
  Transistor #(.\type ("n")) transistor_95 (.in(1'b0), .out(transistor_17_out), .gate(_0));
  Transistor #(.\type ("n")) transistor_96 (.in(1'b0), .out(transistor_18_out), .gate(_0));
  Transistor #(.\type ("n")) transistor_97 (.in(1'b0), .out(transistor_10_out), .gate(_0));
  Pull_Resistor #(.pull(1)) pull_resistor_1 (.node(transistor_1_out));
  Pull_Resistor #(.pull(1)) pull_resistor_2 (.node(transistor_12_out));
  Pull_Resistor #(.pull(1)) pull_resistor_3 (.node(transistor_34_out));
  Pull_Resistor #(.pull(1)) pull_resistor_4 (.node(transistor_2_out));
  Pull_Resistor #(.pull(1)) pull_resistor_5 (.node(transistor_3_out));
  Pull_Resistor #(.pull(1)) pull_resistor_6 (.node(transistor_15_out));
  Pull_Resistor #(.pull(1)) pull_resistor_7 (.node(transistor_5_out));
  Pull_Resistor #(.pull(1)) pull_resistor_8 (.node(transistor_7_out));
  Pull_Resistor #(.pull(1)) pull_resistor_9 (.node(transistor_17_out));
  Pull_Resistor #(.pull(1)) pull_resistor_10 (.node(transistor_18_out));
  Pull_Resistor #(.pull(1)) pull_resistor_11 (.node(transistor_9_out));
  Pull_Resistor #(.pull(1)) pull_resistor_12 (.node(transistor_10_out));

  // Notes on the sheet:
  //   RED
endmodule

module SEL16x12_G (
  input  PCLK,
  input  _15,
  input  _14,
  input  _13,
  input  _12,
  input  _11,
  input  _10,
  input  _9,
  input  _8,
  input  _7,
  input  _6,
  input  _5,
  input  _4,
  input  _3,
  input  _2,
  input  _1,
  input  _0,
  output OUT0,
  output OUT1,
  output OUT2,
  output OUT3,
  output OUT4,
  output OUT5,
  output OUT6,
  output OUT7,
  output OUT8,
  output OUT9,
  output OUT10,
  output OUT11
);

  wire transistor_1_out, transistor_2_out, transistor_3_out, transistor_4_out, transistor_5_out,
       transistor_7_out, transistor_8_out, transistor_9_out, transistor_15_out, transistor_16_out,
       transistor_21_out, transistor_26_out;

  and and_1 (OUT0, PCLK, transistor_1_out);
  and and_2 (OUT1, PCLK, transistor_2_out);
  and and_3 (OUT2, PCLK, transistor_26_out);
  and and_4 (OUT3, PCLK, transistor_3_out);
  and and_5 (OUT4, PCLK, transistor_4_out);
  and and_6 (OUT5, PCLK, transistor_15_out);
  and and_7 (OUT6, PCLK, transistor_16_out);
  and and_8 (OUT7, PCLK, transistor_5_out);
  and and_9 (OUT8, PCLK, transistor_7_out);
  and and_10 (OUT9, PCLK, transistor_21_out);
  and and_11 (OUT10, PCLK, transistor_8_out);
  and and_12 (OUT11, PCLK, transistor_9_out);
  Transistor #(.\type ("n")) transistor_1 (.in(1'b0), .out(transistor_1_out), .gate(_14));
  Transistor #(.\type ("n")) transistor_2 (.in(1'b0), .out(transistor_2_out), .gate(_15));
  Transistor #(.\type ("n")) transistor_3 (.in(1'b0), .out(transistor_3_out), .gate(_15));
  Transistor #(.\type ("n")) transistor_4 (.in(1'b0), .out(transistor_4_out), .gate(_15));
  Transistor #(.\type ("n")) transistor_5 (.in(1'b0), .out(transistor_5_out), .gate(_15));
  Transistor #(.\type ("n")) transistor_6 (.in(1'b0), .out(transistor_5_out), .gate(_14));
  Transistor #(.\type ("n")) transistor_7 (.in(1'b0), .out(transistor_7_out), .gate(_14));
  Transistor #(.\type ("n")) transistor_8 (.in(1'b0), .out(transistor_8_out), .gate(_14));
  Transistor #(.\type ("n")) transistor_9 (.in(1'b0), .out(transistor_9_out), .gate(_14));
  Transistor #(.\type ("n")) transistor_10 (.in(1'b0), .out(transistor_9_out), .gate(_15));
  Transistor #(.\type ("n")) transistor_11 (.in(1'b0), .out(transistor_1_out), .gate(_13));
  Transistor #(.\type ("n")) transistor_12 (.in(1'b0), .out(transistor_2_out), .gate(_13));
  Transistor #(.\type ("n")) transistor_13 (.in(1'b0), .out(transistor_3_out), .gate(_12));
  Transistor #(.\type ("n")) transistor_14 (.in(1'b0), .out(transistor_3_out), .gate(_13));
  Transistor #(.\type ("n")) transistor_15 (.in(1'b0), .out(transistor_15_out), .gate(_13));
  Transistor #(.\type ("n")) transistor_16 (.in(1'b0), .out(transistor_16_out), .gate(_12));
  Transistor #(.\type ("n")) transistor_17 (.in(1'b0), .out(transistor_5_out), .gate(_13));
  Transistor #(.\type ("n")) transistor_18 (.in(1'b0), .out(transistor_5_out), .gate(_12));
  Transistor #(.\type ("n")) transistor_19 (.in(1'b0), .out(transistor_7_out), .gate(_13));
  Transistor #(.\type ("n")) transistor_20 (.in(1'b0), .out(transistor_7_out), .gate(_12));
  Transistor #(.\type ("n")) transistor_21 (.in(1'b0), .out(transistor_21_out), .gate(_13));
  Transistor #(.\type ("n")) transistor_22 (.in(1'b0), .out(transistor_21_out), .gate(_12));
  Transistor #(.\type ("n")) transistor_23 (.in(1'b0), .out(transistor_8_out), .gate(_13));
  Transistor #(.\type ("n")) transistor_24 (.in(1'b0), .out(transistor_9_out), .gate(_12));
  Transistor #(.\type ("n")) transistor_25 (.in(1'b0), .out(transistor_1_out), .gate(_11));
  Transistor #(.\type ("n")) transistor_26 (.in(1'b0), .out(transistor_26_out), .gate(_11));
  Transistor #(.\type ("n")) transistor_27 (.in(1'b0), .out(transistor_15_out), .gate(_11));
  Transistor #(.\type ("n")) transistor_28 (.in(1'b0), .out(transistor_16_out), .gate(_11));
  Transistor #(.\type ("n")) transistor_29 (.in(1'b0), .out(transistor_5_out), .gate(_11));
  Transistor #(.\type ("n")) transistor_30 (.in(1'b0), .out(transistor_7_out), .gate(_11));
  Transistor #(.\type ("n")) transistor_31 (.in(1'b0), .out(transistor_21_out), .gate(_11));
  Transistor #(.\type ("n")) transistor_32 (.in(1'b0), .out(transistor_8_out), .gate(_11));
  Transistor #(.\type ("n")) transistor_33 (.in(1'b0), .out(transistor_9_out), .gate(_11));
  Transistor #(.\type ("n")) transistor_34 (.in(1'b0), .out(transistor_1_out), .gate(_9));
  Transistor #(.\type ("n")) transistor_35 (.in(1'b0), .out(transistor_2_out), .gate(_10));
  Transistor #(.\type ("n")) transistor_36 (.in(1'b0), .out(transistor_2_out), .gate(_9));
  Transistor #(.\type ("n")) transistor_37 (.in(1'b0), .out(transistor_26_out), .gate(_9));
  Transistor #(.\type ("n")) transistor_38 (.in(1'b0), .out(transistor_26_out), .gate(_10));
  Transistor #(.\type ("n")) transistor_39 (.in(1'b0), .out(transistor_3_out), .gate(_9));
  Transistor #(.\type ("n")) transistor_40 (.in(1'b0), .out(transistor_4_out), .gate(_10));
  Transistor #(.\type ("n")) transistor_41 (.in(1'b0), .out(transistor_4_out), .gate(_9));
  Transistor #(.\type ("n")) transistor_42 (.in(1'b0), .out(transistor_16_out), .gate(_9));
  Transistor #(.\type ("n")) transistor_43 (.in(1'b0), .out(transistor_5_out), .gate(_10));
  Transistor #(.\type ("n")) transistor_44 (.in(1'b0), .out(transistor_7_out), .gate(_9));
  Transistor #(.\type ("n")) transistor_45 (.in(1'b0), .out(transistor_21_out), .gate(_9));
  Transistor #(.\type ("n")) transistor_46 (.in(1'b0), .out(transistor_8_out), .gate(_9));
  Transistor #(.\type ("n")) transistor_47 (.in(1'b0), .out(transistor_9_out), .gate(_10));
  Transistor #(.\type ("n")) transistor_48 (.in(1'b0), .out(transistor_2_out), .gate(_8));
  Transistor #(.\type ("n")) transistor_49 (.in(1'b0), .out(transistor_3_out), .gate(_8));
  Transistor #(.\type ("n")) transistor_50 (.in(1'b0), .out(transistor_4_out), .gate(_8));
  Transistor #(.\type ("n")) transistor_51 (.in(1'b0), .out(transistor_15_out), .gate(_8));
  Transistor #(.\type ("n")) transistor_52 (.in(1'b0), .out(transistor_16_out), .gate(_8));
  Transistor #(.\type ("n")) transistor_53 (.in(1'b0), .out(transistor_5_out), .gate(_8));
  Transistor #(.\type ("n")) transistor_54 (.in(1'b0), .out(transistor_8_out), .gate(_8));
  Transistor #(.\type ("n")) transistor_55 (.in(1'b0), .out(transistor_9_out), .gate(_8));
  Transistor #(.\type ("n")) transistor_56 (.in(1'b0), .out(transistor_2_out), .gate(_7));
  Transistor #(.\type ("n")) transistor_57 (.in(1'b0), .out(transistor_26_out), .gate(_7));
  Transistor #(.\type ("n")) transistor_58 (.in(1'b0), .out(transistor_3_out), .gate(_7));
  Transistor #(.\type ("n")) transistor_59 (.in(1'b0), .out(transistor_3_out), .gate(_6));
  Transistor #(.\type ("n")) transistor_60 (.in(1'b0), .out(transistor_15_out), .gate(_6));
  Transistor #(.\type ("n")) transistor_61 (.in(1'b0), .out(transistor_16_out), .gate(_7));
  Transistor #(.\type ("n")) transistor_62 (.in(1'b0), .out(transistor_16_out), .gate(_6));
  Transistor #(.\type ("n")) transistor_63 (.in(1'b0), .out(transistor_5_out), .gate(_6));
  Transistor #(.\type ("n")) transistor_64 (.in(1'b0), .out(transistor_21_out), .gate(_7));
  Transistor #(.\type ("n")) transistor_65 (.in(1'b0), .out(transistor_8_out), .gate(_6));
  Transistor #(.\type ("n")) transistor_66 (.in(1'b0), .out(transistor_8_out), .gate(_7));
  Transistor #(.\type ("n")) transistor_67 (.in(1'b0), .out(transistor_1_out), .gate(_4));
  Transistor #(.\type ("n")) transistor_68 (.in(1'b0), .out(transistor_1_out), .gate(_5));
  Transistor #(.\type ("n")) transistor_69 (.in(1'b0), .out(transistor_2_out), .gate(_5));
  Transistor #(.\type ("n")) transistor_70 (.in(1'b0), .out(transistor_26_out), .gate(_4));
  Transistor #(.\type ("n")) transistor_71 (.in(1'b0), .out(transistor_3_out), .gate(_4));
  Transistor #(.\type ("n")) transistor_72 (.in(1'b0), .out(transistor_4_out), .gate(_5));
  Transistor #(.\type ("n")) transistor_73 (.in(1'b0), .out(transistor_4_out), .gate(_4));
  Transistor #(.\type ("n")) transistor_74 (.in(1'b0), .out(transistor_15_out), .gate(_4));
  Transistor #(.\type ("n")) transistor_75 (.in(1'b0), .out(transistor_15_out), .gate(_5));
  Transistor #(.\type ("n")) transistor_76 (.in(1'b0), .out(transistor_16_out), .gate(_5));
  Transistor #(.\type ("n")) transistor_77 (.in(1'b0), .out(transistor_16_out), .gate(_4));
  Transistor #(.\type ("n")) transistor_78 (.in(1'b0), .out(transistor_7_out), .gate(_5));
  Transistor #(.\type ("n")) transistor_79 (.in(1'b0), .out(transistor_21_out), .gate(_5));
  Transistor #(.\type ("n")) transistor_80 (.in(1'b0), .out(transistor_21_out), .gate(_4));
  Transistor #(.\type ("n")) transistor_81 (.in(1'b0), .out(transistor_8_out), .gate(_4));
  Transistor #(.\type ("n")) transistor_82 (.in(1'b0), .out(transistor_9_out), .gate(_5));
  Transistor #(.\type ("n")) transistor_83 (.in(1'b0), .out(transistor_2_out), .gate(_3));
  Transistor #(.\type ("n")) transistor_84 (.in(1'b0), .out(transistor_4_out), .gate(_3));
  Transistor #(.\type ("n")) transistor_85 (.in(1'b0), .out(transistor_15_out), .gate(_3));
  Transistor #(.\type ("n")) transistor_86 (.in(1'b0), .out(transistor_21_out), .gate(_3));
  Transistor #(.\type ("n")) transistor_87 (.in(1'b0), .out(transistor_1_out), .gate(_2));
  Transistor #(.\type ("n")) transistor_88 (.in(1'b0), .out(transistor_2_out), .gate(_1));
  Transistor #(.\type ("n")) transistor_89 (.in(1'b0), .out(transistor_3_out), .gate(_1));
  Transistor #(.\type ("n")) transistor_90 (.in(1'b0), .out(transistor_3_out), .gate(_2));
  Transistor #(.\type ("n")) transistor_91 (.in(1'b0), .out(transistor_15_out), .gate(_1));
  Transistor #(.\type ("n")) transistor_92 (.in(1'b0), .out(transistor_16_out), .gate(_1));
  Transistor #(.\type ("n")) transistor_93 (.in(1'b0), .out(transistor_7_out), .gate(_2));
  Transistor #(.\type ("n")) transistor_94 (.in(1'b0), .out(transistor_21_out), .gate(_1));
  Transistor #(.\type ("n")) transistor_95 (.in(1'b0), .out(transistor_8_out), .gate(_2));
  Transistor #(.\type ("n")) transistor_96 (.in(1'b0), .out(transistor_9_out), .gate(_2));
  Transistor #(.\type ("n")) transistor_97 (.in(1'b0), .out(transistor_1_out), .gate(_0));
  Transistor #(.\type ("n")) transistor_98 (.in(1'b0), .out(transistor_3_out), .gate(_0));
  Transistor #(.\type ("n")) transistor_99 (.in(1'b0), .out(transistor_5_out), .gate(_0));
  Transistor #(.\type ("n")) transistor_100 (.in(1'b0), .out(transistor_7_out), .gate(_0));
  Transistor #(.\type ("n")) transistor_101 (.in(1'b0), .out(transistor_8_out), .gate(_0));
  Transistor #(.\type ("n")) transistor_102 (.in(1'b0), .out(transistor_9_out), .gate(_0));
  Pull_Resistor #(.pull(1)) pull_resistor_1 (.node(transistor_1_out));
  Pull_Resistor #(.pull(1)) pull_resistor_2 (.node(transistor_2_out));
  Pull_Resistor #(.pull(1)) pull_resistor_3 (.node(transistor_26_out));
  Pull_Resistor #(.pull(1)) pull_resistor_4 (.node(transistor_3_out));
  Pull_Resistor #(.pull(1)) pull_resistor_5 (.node(transistor_4_out));
  Pull_Resistor #(.pull(1)) pull_resistor_6 (.node(transistor_15_out));
  Pull_Resistor #(.pull(1)) pull_resistor_7 (.node(transistor_16_out));
  Pull_Resistor #(.pull(1)) pull_resistor_8 (.node(transistor_5_out));
  Pull_Resistor #(.pull(1)) pull_resistor_9 (.node(transistor_7_out));
  Pull_Resistor #(.pull(1)) pull_resistor_10 (.node(transistor_21_out));
  Pull_Resistor #(.pull(1)) pull_resistor_11 (.node(transistor_8_out));
  Pull_Resistor #(.pull(1)) pull_resistor_12 (.node(transistor_9_out));

  // Notes on the sheet:
  //   GREEN
endmodule

module SEL16x12_B (
  input  PCLK,
  input  _15,
  input  _14,
  input  _13,
  input  _12,
  input  _11,
  input  _10,
  input  _9,
  input  _8,
  input  _7,
  input  _6,
  input  _5,
  input  _4,
  input  _3,
  input  _2,
  input  _1,
  input  _0,
  output OUT0,
  output OUT1,
  output OUT2,
  output OUT3,
  output OUT4,
  output OUT5,
  output OUT6,
  output OUT7,
  output OUT8,
  output OUT9,
  output OUT10,
  output OUT11
);

  wire transistor_1_out, transistor_2_out, transistor_3_out, transistor_4_out, transistor_6_out,
       transistor_7_out, transistor_8_out, transistor_10_out, transistor_13_out, transistor_14_out,
       transistor_18_out, transistor_20_out;

  and and_1 (OUT0, PCLK, transistor_1_out);
  and and_2 (OUT1, PCLK, transistor_10_out);
  and and_3 (OUT2, PCLK, transistor_2_out);
  and and_4 (OUT3, PCLK, transistor_3_out);
  and and_5 (OUT4, PCLK, transistor_4_out);
  and and_6 (OUT5, PCLK, transistor_13_out);
  and and_7 (OUT6, PCLK, transistor_14_out);
  and and_8 (OUT7, PCLK, transistor_6_out);
  and and_9 (OUT8, PCLK, transistor_7_out);
  and and_10 (OUT9, PCLK, transistor_18_out);
  and and_11 (OUT10, PCLK, transistor_20_out);
  and and_12 (OUT11, PCLK, transistor_8_out);
  Transistor #(.\type ("n")) transistor_1 (.in(1'b0), .out(transistor_1_out), .gate(_14));
  Transistor #(.\type ("n")) transistor_2 (.in(1'b0), .out(transistor_2_out), .gate(_15));
  Transistor #(.\type ("n")) transistor_3 (.in(1'b0), .out(transistor_3_out), .gate(_14));
  Transistor #(.\type ("n")) transistor_4 (.in(1'b0), .out(transistor_4_out), .gate(_15));
  Transistor #(.\type ("n")) transistor_5 (.in(1'b0), .out(transistor_4_out), .gate(_14));
  Transistor #(.\type ("n")) transistor_6 (.in(1'b0), .out(transistor_6_out), .gate(_14));
  Transistor #(.\type ("n")) transistor_7 (.in(1'b0), .out(transistor_7_out), .gate(_14));
  Transistor #(.\type ("n")) transistor_8 (.in(1'b0), .out(transistor_8_out), .gate(_14));
  Transistor #(.\type ("n")) transistor_9 (.in(1'b0), .out(transistor_1_out), .gate(_13));
  Transistor #(.\type ("n")) transistor_10 (.in(1'b0), .out(transistor_10_out), .gate(_13));
  Transistor #(.\type ("n")) transistor_11 (.in(1'b0), .out(transistor_2_out), .gate(_12));
  Transistor #(.\type ("n")) transistor_12 (.in(1'b0), .out(transistor_4_out), .gate(_13));
  Transistor #(.\type ("n")) transistor_13 (.in(1'b0), .out(transistor_13_out), .gate(_13));
  Transistor #(.\type ("n")) transistor_14 (.in(1'b0), .out(transistor_14_out), .gate(_13));
  Transistor #(.\type ("n")) transistor_15 (.in(1'b0), .out(transistor_6_out), .gate(_12));
  Transistor #(.\type ("n")) transistor_16 (.in(1'b0), .out(transistor_6_out), .gate(_13));
  Transistor #(.\type ("n")) transistor_17 (.in(1'b0), .out(transistor_7_out), .gate(_13));
  Transistor #(.\type ("n")) transistor_18 (.in(1'b0), .out(transistor_18_out), .gate(_12));
  Transistor #(.\type ("n")) transistor_19 (.in(1'b0), .out(transistor_18_out), .gate(_13));
  Transistor #(.\type ("n")) transistor_20 (.in(1'b0), .out(transistor_20_out), .gate(_13));
  Transistor #(.\type ("n")) transistor_21 (.in(1'b0), .out(transistor_8_out), .gate(_13));
  Transistor #(.\type ("n")) transistor_22 (.in(1'b0), .out(transistor_8_out), .gate(_12));
  Transistor #(.\type ("n")) transistor_23 (.in(1'b0), .out(transistor_2_out), .gate(_11));
  Transistor #(.\type ("n")) transistor_24 (.in(1'b0), .out(transistor_13_out), .gate(_11));
  Transistor #(.\type ("n")) transistor_25 (.in(1'b0), .out(transistor_18_out), .gate(_11));
  Transistor #(.\type ("n")) transistor_26 (.in(1'b0), .out(transistor_1_out), .gate(_10));
  Transistor #(.\type ("n")) transistor_27 (.in(1'b0), .out(transistor_10_out), .gate(_10));
  Transistor #(.\type ("n")) transistor_28 (.in(1'b0), .out(transistor_2_out), .gate(_10));
  Transistor #(.\type ("n")) transistor_29 (.in(1'b0), .out(transistor_2_out), .gate(_9));
  Transistor #(.\type ("n")) transistor_30 (.in(1'b0), .out(transistor_3_out), .gate(_9));
  Transistor #(.\type ("n")) transistor_31 (.in(1'b0), .out(transistor_3_out), .gate(_10));
  Transistor #(.\type ("n")) transistor_32 (.in(1'b0), .out(transistor_13_out), .gate(_10));
  Transistor #(.\type ("n")) transistor_33 (.in(1'b0), .out(transistor_14_out), .gate(_9));
  Transistor #(.\type ("n")) transistor_34 (.in(1'b0), .out(transistor_14_out), .gate(_10));
  Transistor #(.\type ("n")) transistor_35 (.in(1'b0), .out(transistor_6_out), .gate(_10));
  Transistor #(.\type ("n")) transistor_36 (.in(1'b0), .out(transistor_7_out), .gate(_9));
  Transistor #(.\type ("n")) transistor_37 (.in(1'b0), .out(transistor_18_out), .gate(_10));
  Transistor #(.\type ("n")) transistor_38 (.in(1'b0), .out(transistor_18_out), .gate(_9));
  Transistor #(.\type ("n")) transistor_39 (.in(1'b0), .out(transistor_20_out), .gate(_9));
  Transistor #(.\type ("n")) transistor_40 (.in(1'b0), .out(transistor_20_out), .gate(_10));
  Transistor #(.\type ("n")) transistor_41 (.in(1'b0), .out(transistor_8_out), .gate(_10));
  Transistor #(.\type ("n")) transistor_42 (.in(1'b0), .out(transistor_10_out), .gate(_8));
  Transistor #(.\type ("n")) transistor_43 (.in(1'b0), .out(transistor_3_out), .gate(_8));
  Transistor #(.\type ("n")) transistor_44 (.in(1'b0), .out(transistor_4_out), .gate(_8));
  Transistor #(.\type ("n")) transistor_45 (.in(1'b0), .out(transistor_13_out), .gate(_8));
  Transistor #(.\type ("n")) transistor_46 (.in(1'b0), .out(transistor_6_out), .gate(_8));
  Transistor #(.\type ("n")) transistor_47 (.in(1'b0), .out(transistor_18_out), .gate(_8));
  Transistor #(.\type ("n")) transistor_48 (.in(1'b0), .out(transistor_8_out), .gate(_8));
  Transistor #(.\type ("n")) transistor_49 (.in(1'b0), .out(transistor_1_out), .gate(_7));
  Transistor #(.\type ("n")) transistor_50 (.in(1'b0), .out(transistor_10_out), .gate(_7));
  Transistor #(.\type ("n")) transistor_51 (.in(1'b0), .out(transistor_10_out), .gate(_6));
  Transistor #(.\type ("n")) transistor_52 (.in(1'b0), .out(transistor_2_out), .gate(_6));
  Transistor #(.\type ("n")) transistor_53 (.in(1'b0), .out(transistor_2_out), .gate(_7));
  Transistor #(.\type ("n")) transistor_54 (.in(1'b0), .out(transistor_3_out), .gate(_6));
  Transistor #(.\type ("n")) transistor_55 (.in(1'b0), .out(transistor_4_out), .gate(_7));
  Transistor #(.\type ("n")) transistor_56 (.in(1'b0), .out(transistor_13_out), .gate(_7));
  Transistor #(.\type ("n")) transistor_57 (.in(1'b0), .out(transistor_13_out), .gate(_6));
  Transistor #(.\type ("n")) transistor_58 (.in(1'b0), .out(transistor_14_out), .gate(_6));
  Transistor #(.\type ("n")) transistor_59 (.in(1'b0), .out(transistor_6_out), .gate(_6));
  Transistor #(.\type ("n")) transistor_60 (.in(1'b0), .out(transistor_7_out), .gate(_7));
  Transistor #(.\type ("n")) transistor_61 (.in(1'b0), .out(transistor_18_out), .gate(_6));
  Transistor #(.\type ("n")) transistor_62 (.in(1'b0), .out(transistor_20_out), .gate(_6));
  Transistor #(.\type ("n")) transistor_63 (.in(1'b0), .out(transistor_1_out), .gate(_4));
  Transistor #(.\type ("n")) transistor_64 (.in(1'b0), .out(transistor_10_out), .gate(_5));
  Transistor #(.\type ("n")) transistor_65 (.in(1'b0), .out(transistor_2_out), .gate(_4));
  Transistor #(.\type ("n")) transistor_66 (.in(1'b0), .out(transistor_3_out), .gate(_5));
  Transistor #(.\type ("n")) transistor_67 (.in(1'b0), .out(transistor_4_out), .gate(_4));
  Transistor #(.\type ("n")) transistor_68 (.in(1'b0), .out(transistor_13_out), .gate(_4));
  Transistor #(.\type ("n")) transistor_69 (.in(1'b0), .out(transistor_14_out), .gate(_4));
  Transistor #(.\type ("n")) transistor_70 (.in(1'b0), .out(transistor_6_out), .gate(_5));
  Transistor #(.\type ("n")) transistor_71 (.in(1'b0), .out(transistor_7_out), .gate(_4));
  Transistor #(.\type ("n")) transistor_72 (.in(1'b0), .out(transistor_18_out), .gate(_4));
  Transistor #(.\type ("n")) transistor_73 (.in(1'b0), .out(transistor_20_out), .gate(_4));
  Transistor #(.\type ("n")) transistor_74 (.in(1'b0), .out(transistor_8_out), .gate(_4));
  Transistor #(.\type ("n")) transistor_75 (.in(1'b0), .out(transistor_8_out), .gate(_5));
  Transistor #(.\type ("n")) transistor_76 (.in(1'b0), .out(transistor_10_out), .gate(_3));
  Transistor #(.\type ("n")) transistor_77 (.in(1'b0), .out(transistor_2_out), .gate(_3));
  Transistor #(.\type ("n")) transistor_78 (.in(1'b0), .out(transistor_13_out), .gate(_3));
  Transistor #(.\type ("n")) transistor_79 (.in(1'b0), .out(transistor_18_out), .gate(_3));
  Transistor #(.\type ("n")) transistor_80 (.in(1'b0), .out(transistor_20_out), .gate(_3));
  Transistor #(.\type ("n")) transistor_81 (.in(1'b0), .out(transistor_1_out), .gate(_2));
  Transistor #(.\type ("n")) transistor_82 (.in(1'b0), .out(transistor_1_out), .gate(_1));
  Transistor #(.\type ("n")) transistor_83 (.in(1'b0), .out(transistor_10_out), .gate(_1));
  Transistor #(.\type ("n")) transistor_84 (.in(1'b0), .out(transistor_10_out), .gate(_2));
  Transistor #(.\type ("n")) transistor_85 (.in(1'b0), .out(transistor_2_out), .gate(_2));
  Transistor #(.\type ("n")) transistor_86 (.in(1'b0), .out(transistor_3_out), .gate(_2));
  Transistor #(.\type ("n")) transistor_87 (.in(1'b0), .out(transistor_3_out), .gate(_1));
  Transistor #(.\type ("n")) transistor_88 (.in(1'b0), .out(transistor_13_out), .gate(_2));
  Transistor #(.\type ("n")) transistor_89 (.in(1'b0), .out(transistor_13_out), .gate(_1));
  Transistor #(.\type ("n")) transistor_90 (.in(1'b0), .out(transistor_14_out), .gate(_2));
  Transistor #(.\type ("n")) transistor_91 (.in(1'b0), .out(transistor_6_out), .gate(_1));
  Transistor #(.\type ("n")) transistor_92 (.in(1'b0), .out(transistor_6_out), .gate(_2));
  Transistor #(.\type ("n")) transistor_93 (.in(1'b0), .out(transistor_7_out), .gate(_2));
  Transistor #(.\type ("n")) transistor_94 (.in(1'b0), .out(transistor_18_out), .gate(_1));
  Transistor #(.\type ("n")) transistor_95 (.in(1'b0), .out(transistor_18_out), .gate(_2));
  Transistor #(.\type ("n")) transistor_96 (.in(1'b0), .out(transistor_20_out), .gate(_2));
  Transistor #(.\type ("n")) transistor_97 (.in(1'b0), .out(transistor_8_out), .gate(_2));
  Transistor #(.\type ("n")) transistor_98 (.in(1'b0), .out(transistor_1_out), .gate(_0));
  Transistor #(.\type ("n")) transistor_99 (.in(1'b0), .out(transistor_2_out), .gate(_0));
  Transistor #(.\type ("n")) transistor_100 (.in(1'b0), .out(transistor_14_out), .gate(_0));
  Transistor #(.\type ("n")) transistor_101 (.in(1'b0), .out(transistor_7_out), .gate(_0));
  Transistor #(.\type ("n")) transistor_102 (.in(1'b0), .out(transistor_18_out), .gate(_0));
  Transistor #(.\type ("n")) transistor_103 (.in(1'b0), .out(transistor_20_out), .gate(_0));
  Pull_Resistor #(.pull(1)) pull_resistor_1 (.node(transistor_1_out));
  Pull_Resistor #(.pull(1)) pull_resistor_2 (.node(transistor_10_out));
  Pull_Resistor #(.pull(1)) pull_resistor_3 (.node(transistor_2_out));
  Pull_Resistor #(.pull(1)) pull_resistor_4 (.node(transistor_3_out));
  Pull_Resistor #(.pull(1)) pull_resistor_5 (.node(transistor_4_out));
  Pull_Resistor #(.pull(1)) pull_resistor_6 (.node(transistor_13_out));
  Pull_Resistor #(.pull(1)) pull_resistor_7 (.node(transistor_14_out));
  Pull_Resistor #(.pull(1)) pull_resistor_8 (.node(transistor_6_out));
  Pull_Resistor #(.pull(1)) pull_resistor_9 (.node(transistor_7_out));
  Pull_Resistor #(.pull(1)) pull_resistor_10 (.node(transistor_18_out));
  Pull_Resistor #(.pull(1)) pull_resistor_11 (.node(transistor_20_out));
  Pull_Resistor #(.pull(1)) pull_resistor_12 (.node(transistor_8_out));

  // Notes on the sheet:
  //   BLUE
endmodule
